// Logisim project GameOfLife.circ as structural Verilog: 11 circuits, main circuit mem
// V
module main (
  input  in_1,
  input  in_2,
  input  in_3,
  input  Run
);

  wire cdm_1_change_bit_state, clock_1_out, inputstate_1_out_5, inputstate_1_out_7, inputstate_1_out_9,
       inputstate_1_out_11, inputstate_1_out_13, inputstate_1_out_15, inputstate_1_out_17,
       inputstate_1_out_19, inputstate_1_out_21, inputstate_1_out_23, inputstate_1_out_25,
       inputstate_1_out_27, inputstate_1_out_29, inputstate_1_out_31, inputstate_1_out_33,
       inputstate_1_out_35, speed_changer_1_out_4, tunnel, tunnel_t, tunnel_t_t, tunnel_t_t_t, v;
  wire [3:0] X, Y;
  wire [15:0] inputstate_1_out_4, inputstate_1_out_6, inputstate_1_out_8, inputstate_1_out_10,
       inputstate_1_out_12, inputstate_1_out_14, inputstate_1_out_16, inputstate_1_out_18,
       inputstate_1_out_20, inputstate_1_out_22, inputstate_1_out_24, inputstate_1_out_26,
       inputstate_1_out_28, inputstate_1_out_30, inputstate_1_out_32, inputstate_1_out_34, mem_1_out_36,
       mem_1_out_37, mem_1_out_38, mem_1_out_39, mem_1_out_40, mem_1_out_41, mem_1_out_42, mem_1_out_43,
       mem_1_out_44, mem_1_out_45, mem_1_out_46, mem_1_out_47, mem_1_out_48, mem_1_out_49, mem_1_out_50,
       mem_1_out_51;

  cdm cdm_1 (
    .Change_Bit_State(cdm_1_change_bit_state), .out_7(Y), .out_8(X), .in_1(tunnel), .in_2(tunnel_t_t_t),
    .in_3(tunnel_t_t), .in_4(tunnel_t), .in_5(v));
  Clock #(.highDuration(90), .lowDuration(90)) clock_1 (.out(clock_1_out));
  mem mem_1 (
    .in_4(inputstate_1_out_4), .in_5(inputstate_1_out_5), .in_6(inputstate_1_out_6),
    .in_7(inputstate_1_out_7), .in_8(inputstate_1_out_8), .in_9(inputstate_1_out_9),
    .in_10(inputstate_1_out_10), .in_11(inputstate_1_out_11), .in_12(inputstate_1_out_12),
    .in_13(inputstate_1_out_13), .in_14(inputstate_1_out_14), .in_15(inputstate_1_out_15),
    .in_16(inputstate_1_out_16), .in_17(inputstate_1_out_17), .in_18(inputstate_1_out_18),
    .in_19(inputstate_1_out_19), .in_20(inputstate_1_out_20), .in_21(inputstate_1_out_21),
    .in_22(inputstate_1_out_22), .in_23(inputstate_1_out_23), .in_24(inputstate_1_out_24),
    .in_25(inputstate_1_out_25), .in_26(inputstate_1_out_26), .in_27(inputstate_1_out_27),
    .in_28(inputstate_1_out_28), .in_29(inputstate_1_out_29), .in_32(inputstate_1_out_32),
    .in_33(inputstate_1_out_33), .in_30(inputstate_1_out_30), .in_31(inputstate_1_out_31),
    .in_34(inputstate_1_out_34), .in_35(inputstate_1_out_35), .in_1(Run), .out_36(mem_1_out_36),
    .out_37(mem_1_out_37), .out_38(mem_1_out_38), .out_39(mem_1_out_39), .out_40(mem_1_out_40),
    .out_41(mem_1_out_41), .out_42(mem_1_out_42), .out_43(mem_1_out_43), .out_44(mem_1_out_44),
    .out_45(mem_1_out_45), .out_46(mem_1_out_46), .out_47(mem_1_out_47), .out_48(mem_1_out_48),
    .out_49(mem_1_out_49), .out_50(mem_1_out_50), .out_51(mem_1_out_51), .in_2(clock_1_out),
    .in_3(speed_changer_1_out_4));
  DotMatrix #(.inputtype("row"), .matrixcols(16), .matrixrows(16)) dotmatrix_1 (
    .row0(mem_1_out_36), .row1(mem_1_out_37), .row2(mem_1_out_38), .row3(mem_1_out_39), .row4(mem_1_out_40),
    .row5(mem_1_out_41), .row6(mem_1_out_42), .row7(mem_1_out_43), .row8(mem_1_out_44), .row9(mem_1_out_45),
    .row10(mem_1_out_46), .row11(mem_1_out_47), .row12(mem_1_out_48), .row13(mem_1_out_49),
    .row14(mem_1_out_50), .row15(mem_1_out_51));
  inputState inputstate_1 (
    .in_1(Y), .in_2(X), .in_3(cdm_1_change_bit_state), .out_5(inputstate_1_out_5),
    .out_7(inputstate_1_out_7), .out_9(inputstate_1_out_9), .out_11(inputstate_1_out_11),
    .out_13(inputstate_1_out_13), .out_15(inputstate_1_out_15), .out_17(inputstate_1_out_17),
    .out_19(inputstate_1_out_19), .out_21(inputstate_1_out_21), .out_23(inputstate_1_out_23),
    .out_25(inputstate_1_out_25), .out_27(inputstate_1_out_27), .out_29(inputstate_1_out_29),
    .out_31(inputstate_1_out_31), .out_33(inputstate_1_out_33), .out_35(inputstate_1_out_35),
    .out_4(inputstate_1_out_4), .out_6(inputstate_1_out_6), .out_8(inputstate_1_out_8),
    .out_10(inputstate_1_out_10), .out_12(inputstate_1_out_12), .out_14(inputstate_1_out_14),
    .out_16(inputstate_1_out_16), .out_18(inputstate_1_out_18), .out_20(inputstate_1_out_20),
    .out_22(inputstate_1_out_22), .out_24(inputstate_1_out_24), .out_26(inputstate_1_out_26),
    .out_28(inputstate_1_out_28), .out_30(inputstate_1_out_30), .out_32(inputstate_1_out_32),
    .out_34(inputstate_1_out_34));
  speed_changer speed_changer_1 (.out_4(speed_changer_1_out_4), .in_2(in_1), .in_3(in_2), .in_1(in_3));
  // Probe on X
  Button button (.out(tunnel_t_t_t));
  Button button_2 (.out(tunnel_t));
  Button button_3 (.out(tunnel_t_t));
  Button button_4 (.out(tunnel));
  Button u_v (.out(v));
  // Probe on Y
endmodule

module mem (
  input  in_1,
  input  in_2,
  input  in_3,
  input  [15:0] in_4,
  input  in_5,
  input  [15:0] in_6,
  input  in_7,
  input  [15:0] in_8,
  input  in_9,
  input  [15:0] in_10,
  input  in_11,
  input  [15:0] in_12,
  input  in_13,
  input  [15:0] in_14,
  input  in_15,
  input  [15:0] in_16,
  input  in_17,
  input  [15:0] in_18,
  input  in_19,
  input  [15:0] in_20,
  input  in_21,
  input  [15:0] in_22,
  input  in_23,
  input  [15:0] in_24,
  input  in_25,
  input  [15:0] in_26,
  input  in_27,
  input  [15:0] in_28,
  input  in_29,
  input  [15:0] in_30,
  input  in_31,
  input  [15:0] in_32,
  input  in_33,
  input  [15:0] in_34,
  input  in_35,
  output [15:0] out_36,
  output [15:0] out_37,
  output [15:0] out_38,
  output [15:0] out_39,
  output [15:0] out_40,
  output [15:0] out_41,
  output [15:0] out_42,
  output [15:0] out_43,
  output [15:0] out_44,
  output [15:0] out_45,
  output [15:0] out_46,
  output [15:0] out_47,
  output [15:0] out_48,
  output [15:0] out_49,
  output [15:0] out_50,
  output [15:0] out_51
);

  wire Cl, cl_t, controlled_buffer_2_out, controlled_buffer_3_out, controlled_buffer_4_out,
       controlled_buffer_5_out, controlled_buffer_6_out, controlled_buffer_7_out, controlled_buffer_8_out,
       controlled_buffer_9_out, controlled_buffer_10_out, controlled_buffer_11_out, controlled_buffer_12_out,
       controlled_buffer_13_out, controlled_buffer_16_out, is, pull_resistor_2_node, pull_resistor_3_node,
       pull_resistor_5_node;
  wire [15:0] _1, _2, _3, _4, _5, _6, _7, _8, _9, _10, _11, _12, _13, _14, _15, _16,
       controlled_buffer_41_out, controlled_buffer_43_out, controlled_buffer_44_out,
       controlled_buffer_45_out, controlled_buffer_46_out, controlled_buffer_47_out,
       controlled_buffer_48_out, controlled_buffer_49_out, down,
       get_new_state_for_one_string_of_matrix_1_out_4, get_new_state_for_one_string_of_matrix_2_out_4,
       get_new_state_for_one_string_of_matrix_3_out_4, get_new_state_for_one_string_of_matrix_4_out_4,
       get_new_state_for_one_string_of_matrix_5_out_4, get_new_state_for_one_string_of_matrix_6_out_4,
       get_new_state_for_one_string_of_matrix_7_out_4, get_new_state_for_one_string_of_matrix_8_out_4,
       get_new_state_for_one_string_of_matrix_9_out_4, get_new_state_for_one_string_of_matrix_10_out_4,
       get_new_state_for_one_string_of_matrix_11_out_4, get_new_state_for_one_string_of_matrix_12_out_4,
       get_new_state_for_one_string_of_matrix_13_out_4, get_new_state_for_one_string_of_matrix_14_out_4,
       get_new_state_for_one_string_of_matrix_15_out_4, get_new_state_for_one_string_of_matrix_16_out_4,
       multiplexer_2_out, multiplexer_3_out, multiplexer_4_out, multiplexer_5_out, multiplexer_6_out,
       multiplexer_7_out, multiplexer_8_out, multiplexer_9_out, multiplexer_10_out, multiplexer_11_out,
       multiplexer_12_out, multiplexer_13_out, multiplexer_14_out, multiplexer_15_out, multiplexer_16_out,
       multiplexer_17_out, pull_resistor_18_node, pull_resistor_19_node, pull_resistor_20_node,
       pull_resistor_21_node, pull_resistor_22_node, pull_resistor_23_node, pull_resistor_24_node,
       pull_resistor_26_node, register_2_q, register_3_q, register_4_q, register_5_q, register_6_q,
       register_7_q, register_8_q, register_9_q, register_10_q, register_11_q, register_12_q, register_13_q,
       register_14_q, register_15_q, up, xor_1_out, xor_2_out, xor_3_out, xor_4_out, xor_5_out, xor_6_out,
       xor_7_out, xor_8_out, xor_9_out, xor_10_out, xor_11_out, xor_12_out, xor_13_out, xor_14_out,
       xor_15_out, xor_16_out;
  wire [17:0] convert_16_to_18_1_out_2, convert_16_to_18_2_out_2, convert_16_to_18_3_out_2,
       convert_16_to_18_4_out_2, convert_16_to_18_5_out_2, convert_16_to_18_6_out_2,
       convert_16_to_18_7_out_2, convert_16_to_18_8_out_2, convert_16_to_18_9_out_2,
       convert_16_to_18_10_out_2, convert_16_to_18_11_out_2, convert_16_to_18_12_out_2,
       convert_16_to_18_13_out_2, convert_16_to_18_14_out_2, convert_16_to_18_15_out_2,
       convert_16_to_18_16_out_2, convert_16_to_18_17_out_2, convert_16_to_18_18_out_2,
       convert_16_to_18_19_out_2, convert_16_to_18_20_out_2, convert_16_to_18_21_out_2,
       convert_16_to_18_22_out_2, convert_16_to_18_23_out_2, convert_16_to_18_24_out_2,
       convert_16_to_18_25_out_2, convert_16_to_18_26_out_2, convert_16_to_18_27_out_2,
       convert_16_to_18_28_out_2, convert_16_to_18_29_out_2, convert_16_to_18_30_out_2,
       convert_16_to_18_31_out_2, convert_16_to_18_32_out_2, convert_16_to_18_33_out_2,
       convert_16_to_18_34_out_2, convert_16_to_18_35_out_2, convert_16_to_18_36_out_2,
       convert_16_to_18_37_out_2, convert_16_to_18_38_out_2, convert_16_to_18_39_out_2,
       convert_16_to_18_40_out_2, convert_16_to_18_41_out_2, convert_16_to_18_42_out_2,
       convert_16_to_18_43_out_2, convert_16_to_18_44_out_2, convert_16_to_18_45_out_2,
       convert_16_to_18_46_out_2, convert_16_to_18_47_out_2, convert_16_to_18_48_out_2;

  pointer pointer_1 (.in_1(cl_t), .in_2(in_5), .in_3(in_4), .out_4(_1));
  pointer pointer_2 (.in_1(cl_t), .in_2(in_7), .in_3(in_6), .out_4(_2));
  pointer pointer_3 (.in_1(cl_t), .in_2(in_9), .in_3(in_8), .out_4(_3));
  pointer pointer_4 (.in_1(cl_t), .in_2(in_11), .in_3(in_10), .out_4(_4));
  pointer pointer_5 (.in_1(cl_t), .in_2(in_13), .in_3(in_12), .out_4(_5));
  pointer pointer_6 (.in_1(cl_t), .in_2(in_15), .in_3(in_14), .out_4(_6));
  pointer pointer_7 (.in_1(cl_t), .in_2(in_17), .in_3(in_16), .out_4(_7));
  pointer pointer_8 (.in_1(cl_t), .in_2(in_19), .in_3(in_18), .out_4(_8));
  pointer pointer_9 (.in_1(cl_t), .in_2(in_21), .in_3(in_20), .out_4(_9));
  pointer pointer_10 (.in_1(cl_t), .in_2(in_23), .in_3(in_22), .out_4(_10));
  pointer pointer_11 (.in_1(cl_t), .in_2(in_25), .in_3(in_24), .out_4(_11));
  pointer pointer_12 (.in_1(cl_t), .in_2(in_27), .in_3(in_26), .out_4(_12));
  pointer pointer_13 (.in_1(cl_t), .in_2(in_29), .in_3(in_28), .out_4(_13));
  pointer pointer_14 (.in_1(cl_t), .in_2(in_31), .in_3(in_30), .out_4(_14));
  pointer pointer_15 (.in_1(cl_t), .in_2(in_33), .in_3(in_32), .out_4(_15));
  pointer pointer_16 (.in_1(cl_t), .in_2(in_35), .in_3(in_34), .out_4(_16));
  Multiplexer #(.enable("false")) multiplexer_1 (.in0(in_2), .in1(in_3), .out(cl_t), .sel(in_1));
  assign Cl = in_1 ? cl_t : 1'bz;  // Controlled_Buffer controlled_buffer_1
  Pull_Resistor pull_resistor_1 (.node(Cl));
  assign xor_1_out = up ^ in_4;  // XOR_Gate xor_1, 16 bits wide
  assign controlled_buffer_2_out = in_5 ? in_5 : 1'bz;  // Controlled_Buffer controlled_buffer_2
  assign xor_2_out = register_2_q ^ in_6;  // XOR_Gate xor_2, 16 bits wide
  assign controlled_buffer_3_out = in_7 ? in_7 : 1'bz;  // Controlled_Buffer controlled_buffer_3
  assign xor_3_out = register_3_q ^ in_8;  // XOR_Gate xor_3, 16 bits wide
  assign controlled_buffer_4_out = in_9 ? in_9 : 1'bz;  // Controlled_Buffer controlled_buffer_4
  assign xor_4_out = register_4_q ^ in_10;  // XOR_Gate xor_4, 16 bits wide
  assign controlled_buffer_5_out = in_11 ? in_11 : 1'bz;  // Controlled_Buffer controlled_buffer_5
  assign xor_5_out = register_5_q ^ in_12;  // XOR_Gate xor_5, 16 bits wide
  assign controlled_buffer_6_out = in_13 ? in_13 : 1'bz;  // Controlled_Buffer controlled_buffer_6
  assign xor_6_out = register_6_q ^ in_14;  // XOR_Gate xor_6, 16 bits wide
  assign controlled_buffer_7_out = in_15 ? in_15 : 1'bz;  // Controlled_Buffer controlled_buffer_7
  assign xor_7_out = register_7_q ^ in_16;  // XOR_Gate xor_7, 16 bits wide
  assign controlled_buffer_8_out = in_17 ? in_17 : 1'bz;  // Controlled_Buffer controlled_buffer_8
  assign xor_8_out = register_8_q ^ in_18;  // XOR_Gate xor_8, 16 bits wide
  assign controlled_buffer_9_out = in_19 ? in_19 : 1'bz;  // Controlled_Buffer controlled_buffer_9
  assign xor_9_out = register_9_q ^ in_20;  // XOR_Gate xor_9, 16 bits wide
  assign controlled_buffer_10_out = in_21 ? in_21 : 1'bz;  // Controlled_Buffer controlled_buffer_10
  assign xor_10_out = register_10_q ^ in_22;  // XOR_Gate xor_10, 16 bits wide
  assign controlled_buffer_11_out = in_23 ? in_23 : 1'bz;  // Controlled_Buffer controlled_buffer_11
  assign xor_11_out = register_11_q ^ in_24;  // XOR_Gate xor_11, 16 bits wide
  assign controlled_buffer_12_out = in_25 ? in_25 : 1'bz;  // Controlled_Buffer controlled_buffer_12
  assign xor_12_out = register_12_q ^ in_26;  // XOR_Gate xor_12, 16 bits wide
  assign controlled_buffer_13_out = in_27 ? in_27 : 1'bz;  // Controlled_Buffer controlled_buffer_13
  assign xor_13_out = register_13_q ^ in_28;  // XOR_Gate xor_13, 16 bits wide
  Pull_Resistor pull_resistor_2 (.node(pull_resistor_2_node));
  assign pull_resistor_2_node = in_29 ? in_29 : 1'bz;  // Controlled_Buffer controlled_buffer_14
  assign xor_14_out = register_14_q ^ in_30;  // XOR_Gate xor_14, 16 bits wide
  Pull_Resistor pull_resistor_3 (.node(pull_resistor_3_node));
  assign pull_resistor_3_node = in_31 ? in_31 : 1'bz;  // Controlled_Buffer controlled_buffer_15
  assign xor_15_out = register_15_q ^ in_32;  // XOR_Gate xor_15, 16 bits wide
  assign controlled_buffer_16_out = in_33 ? in_33 : 1'bz;  // Controlled_Buffer controlled_buffer_16
  Pull_Resistor pull_resistor_4 (.node(controlled_buffer_16_out));
  assign xor_16_out = down ^ in_34;  // XOR_Gate xor_16, 16 bits wide
  Pull_Resistor pull_resistor_5 (.node(pull_resistor_5_node));
  assign pull_resistor_5_node = in_35 ? in_35 : 1'bz;  // Controlled_Buffer controlled_buffer_17
  not not_1 (is, in_1);
  Multiplexer #(.width(16), .enable("false")) multiplexer_2 (
    .in0(get_new_state_for_one_string_of_matrix_1_out_4), .in1(xor_1_out), .out(multiplexer_2_out), .sel(is));
  Pull_Resistor pull_resistor_6 (.node(controlled_buffer_2_out));
  Multiplexer #(.width(16), .enable("false")) multiplexer_3 (
    .in0(get_new_state_for_one_string_of_matrix_2_out_4), .in1(xor_2_out), .out(multiplexer_3_out), .sel(is));
  Pull_Resistor pull_resistor_7 (.node(controlled_buffer_3_out));
  Multiplexer #(.width(16), .enable("false")) multiplexer_4 (
    .in0(get_new_state_for_one_string_of_matrix_3_out_4), .in1(xor_3_out), .out(multiplexer_4_out), .sel(is));
  Pull_Resistor pull_resistor_8 (.node(controlled_buffer_4_out));
  Multiplexer #(.width(16), .enable("false")) multiplexer_5 (
    .in0(get_new_state_for_one_string_of_matrix_4_out_4), .in1(xor_4_out), .out(multiplexer_5_out), .sel(is));
  Pull_Resistor pull_resistor_9 (.node(controlled_buffer_5_out));
  Multiplexer #(.width(16), .enable("false")) multiplexer_6 (
    .in0(get_new_state_for_one_string_of_matrix_5_out_4), .in1(xor_5_out), .out(multiplexer_6_out), .sel(is));
  Pull_Resistor pull_resistor_10 (.node(controlled_buffer_6_out));
  Multiplexer #(.width(16), .enable("false")) multiplexer_7 (
    .in0(get_new_state_for_one_string_of_matrix_6_out_4), .in1(xor_6_out), .out(multiplexer_7_out), .sel(is));
  Pull_Resistor pull_resistor_11 (.node(controlled_buffer_7_out));
  Multiplexer #(.width(16), .enable("false")) multiplexer_8 (
    .in0(get_new_state_for_one_string_of_matrix_7_out_4), .in1(xor_7_out), .out(multiplexer_8_out), .sel(is));
  Pull_Resistor pull_resistor_12 (.node(controlled_buffer_8_out));
  Multiplexer #(.width(16), .enable("false")) multiplexer_9 (
    .in0(get_new_state_for_one_string_of_matrix_8_out_4), .in1(xor_8_out), .out(multiplexer_9_out), .sel(is));
  Pull_Resistor pull_resistor_13 (.node(controlled_buffer_9_out));
  Multiplexer #(.width(16), .enable("false")) multiplexer_10 (
    .in0(get_new_state_for_one_string_of_matrix_9_out_4), .in1(xor_9_out), .out(multiplexer_10_out), .sel(is));
  Pull_Resistor pull_resistor_14 (.node(controlled_buffer_10_out));
  Multiplexer #(.width(16), .enable("false")) multiplexer_11 (
    .in0(get_new_state_for_one_string_of_matrix_10_out_4), .in1(xor_10_out), .out(multiplexer_11_out),
    .sel(is));
  Pull_Resistor pull_resistor_15 (.node(controlled_buffer_11_out));
  Multiplexer #(.width(16), .enable("false")) multiplexer_12 (
    .in0(get_new_state_for_one_string_of_matrix_11_out_4), .in1(xor_11_out), .out(multiplexer_12_out),
    .sel(is));
  Pull_Resistor pull_resistor_16 (.node(controlled_buffer_12_out));
  Multiplexer #(.width(16), .enable("false")) multiplexer_13 (
    .in0(get_new_state_for_one_string_of_matrix_12_out_4), .in1(xor_12_out), .out(multiplexer_13_out),
    .sel(is));
  Pull_Resistor pull_resistor_17 (.node(controlled_buffer_13_out));
  Multiplexer #(.width(16), .enable("false")) multiplexer_14 (
    .in0(get_new_state_for_one_string_of_matrix_13_out_4), .in1(xor_13_out), .out(multiplexer_14_out),
    .sel(is));
  Multiplexer #(.width(16), .enable("false")) multiplexer_15 (
    .in0(get_new_state_for_one_string_of_matrix_14_out_4), .in1(xor_14_out), .out(multiplexer_15_out),
    .sel(is));
  Multiplexer #(.width(16), .enable("false")) multiplexer_16 (
    .in0(get_new_state_for_one_string_of_matrix_15_out_4), .in1(xor_15_out), .out(multiplexer_16_out),
    .sel(is));
  Multiplexer #(.width(16), .enable("false")) multiplexer_17 (
    .in0(get_new_state_for_one_string_of_matrix_16_out_4), .in1(xor_16_out), .out(multiplexer_17_out),
    .sel(is));
  Register #(.width(16)) register_1 (.D(multiplexer_2_out), .Q(up), .clk(controlled_buffer_2_out));  // open: en, clr
  assign controlled_buffer_2_out = Cl ? Cl : 1'bz;  // Controlled_Buffer controlled_buffer_18
  Register #(.width(16)) register_2 (
    .D(multiplexer_3_out), .Q(register_2_q), .clk(controlled_buffer_3_out));  // open: en, clr
  assign controlled_buffer_3_out = Cl ? Cl : 1'bz;  // Controlled_Buffer controlled_buffer_19
  Register #(.width(16)) register_3 (
    .D(multiplexer_4_out), .Q(register_3_q), .clk(controlled_buffer_4_out));  // open: en, clr
  assign controlled_buffer_4_out = Cl ? Cl : 1'bz;  // Controlled_Buffer controlled_buffer_20
  Register #(.width(16)) register_4 (
    .D(multiplexer_5_out), .Q(register_4_q), .clk(controlled_buffer_5_out));  // open: en, clr
  assign controlled_buffer_5_out = Cl ? Cl : 1'bz;  // Controlled_Buffer controlled_buffer_21
  Register #(.width(16)) register_5 (
    .D(multiplexer_6_out), .Q(register_5_q), .clk(controlled_buffer_6_out));  // open: en, clr
  assign controlled_buffer_6_out = Cl ? Cl : 1'bz;  // Controlled_Buffer controlled_buffer_22
  Register #(.width(16)) register_6 (
    .D(multiplexer_7_out), .Q(register_6_q), .clk(controlled_buffer_7_out));  // open: en, clr
  assign controlled_buffer_7_out = Cl ? Cl : 1'bz;  // Controlled_Buffer controlled_buffer_23
  Register #(.width(16)) register_7 (
    .D(multiplexer_8_out), .Q(register_7_q), .clk(controlled_buffer_8_out));  // open: en, clr
  assign controlled_buffer_8_out = Cl ? Cl : 1'bz;  // Controlled_Buffer controlled_buffer_24
  Register #(.width(16)) register_8 (
    .D(multiplexer_9_out), .Q(register_8_q), .clk(controlled_buffer_9_out));  // open: en, clr
  assign controlled_buffer_9_out = Cl ? Cl : 1'bz;  // Controlled_Buffer controlled_buffer_25
  Register #(.width(16)) register_9 (
    .D(multiplexer_10_out), .Q(register_9_q), .clk(controlled_buffer_10_out));  // open: en, clr
  assign controlled_buffer_10_out = Cl ? Cl : 1'bz;  // Controlled_Buffer controlled_buffer_26
  Register #(.width(16)) register_10 (
    .D(multiplexer_11_out), .Q(register_10_q), .clk(controlled_buffer_11_out));  // open: en, clr
  assign controlled_buffer_11_out = Cl ? Cl : 1'bz;  // Controlled_Buffer controlled_buffer_27
  Register #(.width(16)) register_11 (
    .D(multiplexer_12_out), .Q(register_11_q), .clk(controlled_buffer_12_out));  // open: en, clr
  assign controlled_buffer_12_out = Cl ? Cl : 1'bz;  // Controlled_Buffer controlled_buffer_28
  Register #(.width(16)) register_12 (
    .D(multiplexer_13_out), .Q(register_12_q), .clk(controlled_buffer_13_out));  // open: en, clr
  assign controlled_buffer_13_out = Cl ? Cl : 1'bz;  // Controlled_Buffer controlled_buffer_29
  Register #(.width(16)) register_13 (
    .D(multiplexer_14_out), .Q(register_13_q), .clk(pull_resistor_2_node));  // open: en, clr
  assign pull_resistor_2_node = Cl ? Cl : 1'bz;  // Controlled_Buffer controlled_buffer_30
  Register #(.width(16)) register_14 (
    .D(multiplexer_15_out), .Q(register_14_q), .clk(pull_resistor_3_node));  // open: en, clr
  assign pull_resistor_3_node = Cl ? Cl : 1'bz;  // Controlled_Buffer controlled_buffer_31
  Register #(.width(16)) register_15 (
    .D(multiplexer_16_out), .Q(register_15_q), .clk(controlled_buffer_16_out));  // open: en, clr
  assign controlled_buffer_16_out = Cl ? Cl : 1'bz;  // Controlled_Buffer controlled_buffer_32
  Register #(.width(16)) register_16 (.D(multiplexer_17_out), .Q(down), .clk(pull_resistor_5_node));  // open: en, clr
  assign pull_resistor_5_node = Cl ? Cl : 1'bz;  // Controlled_Buffer controlled_buffer_33
  convert_16_to_18 convert_16_to_18_1 (.in_1(down), .out_2(convert_16_to_18_1_out_2));
  convert_16_to_18 convert_16_to_18_2 (.in_1(up), .out_2(convert_16_to_18_2_out_2));
  get_new_state_for_one_string_of_Matrix get_new_state_for_one_string_of_matrix_1 (
    .in_1(convert_16_to_18_1_out_2), .in_2(convert_16_to_18_2_out_2), .in_3(convert_16_to_18_3_out_2),
    .out_4(get_new_state_for_one_string_of_matrix_1_out_4));
  convert_16_to_18 convert_16_to_18_3 (.in_1(register_2_q), .out_2(convert_16_to_18_3_out_2));
  convert_16_to_18 convert_16_to_18_4 (.in_1(up), .out_2(convert_16_to_18_4_out_2));
  convert_16_to_18 convert_16_to_18_5 (.in_1(register_2_q), .out_2(convert_16_to_18_5_out_2));
  get_new_state_for_one_string_of_Matrix get_new_state_for_one_string_of_matrix_2 (
    .in_1(convert_16_to_18_4_out_2), .in_2(convert_16_to_18_5_out_2), .in_3(convert_16_to_18_6_out_2),
    .out_4(get_new_state_for_one_string_of_matrix_2_out_4));
  convert_16_to_18 convert_16_to_18_6 (.in_1(register_3_q), .out_2(convert_16_to_18_6_out_2));
  convert_16_to_18 convert_16_to_18_7 (.in_1(register_2_q), .out_2(convert_16_to_18_7_out_2));
  get_new_state_for_one_string_of_Matrix get_new_state_for_one_string_of_matrix_3 (
    .in_1(convert_16_to_18_7_out_2), .in_2(convert_16_to_18_8_out_2), .in_3(convert_16_to_18_9_out_2),
    .out_4(get_new_state_for_one_string_of_matrix_3_out_4));
  convert_16_to_18 convert_16_to_18_8 (.in_1(register_3_q), .out_2(convert_16_to_18_8_out_2));
  convert_16_to_18 convert_16_to_18_9 (.in_1(register_4_q), .out_2(convert_16_to_18_9_out_2));
  convert_16_to_18 convert_16_to_18_10 (.in_1(register_3_q), .out_2(convert_16_to_18_10_out_2));
  convert_16_to_18 convert_16_to_18_11 (.in_1(register_4_q), .out_2(convert_16_to_18_11_out_2));
  get_new_state_for_one_string_of_Matrix get_new_state_for_one_string_of_matrix_4 (
    .in_1(convert_16_to_18_10_out_2), .in_2(convert_16_to_18_11_out_2), .in_3(convert_16_to_18_12_out_2),
    .out_4(get_new_state_for_one_string_of_matrix_4_out_4));
  convert_16_to_18 convert_16_to_18_12 (.in_1(register_5_q), .out_2(convert_16_to_18_12_out_2));
  convert_16_to_18 convert_16_to_18_13 (.in_1(register_4_q), .out_2(convert_16_to_18_13_out_2));
  get_new_state_for_one_string_of_Matrix get_new_state_for_one_string_of_matrix_5 (
    .in_1(convert_16_to_18_13_out_2), .in_2(convert_16_to_18_14_out_2), .in_3(convert_16_to_18_15_out_2),
    .out_4(get_new_state_for_one_string_of_matrix_5_out_4));
  convert_16_to_18 convert_16_to_18_14 (.in_1(register_5_q), .out_2(convert_16_to_18_14_out_2));
  convert_16_to_18 convert_16_to_18_15 (.in_1(register_6_q), .out_2(convert_16_to_18_15_out_2));
  convert_16_to_18 convert_16_to_18_16 (.in_1(register_5_q), .out_2(convert_16_to_18_16_out_2));
  convert_16_to_18 convert_16_to_18_17 (.in_1(register_6_q), .out_2(convert_16_to_18_17_out_2));
  get_new_state_for_one_string_of_Matrix get_new_state_for_one_string_of_matrix_6 (
    .in_1(convert_16_to_18_16_out_2), .in_2(convert_16_to_18_17_out_2), .in_3(convert_16_to_18_18_out_2),
    .out_4(get_new_state_for_one_string_of_matrix_6_out_4));
  convert_16_to_18 convert_16_to_18_18 (.in_1(register_7_q), .out_2(convert_16_to_18_18_out_2));
  convert_16_to_18 convert_16_to_18_19 (.in_1(register_6_q), .out_2(convert_16_to_18_19_out_2));
  convert_16_to_18 convert_16_to_18_20 (.in_1(register_7_q), .out_2(convert_16_to_18_20_out_2));
  get_new_state_for_one_string_of_Matrix get_new_state_for_one_string_of_matrix_7 (
    .in_1(convert_16_to_18_19_out_2), .in_2(convert_16_to_18_20_out_2), .in_3(convert_16_to_18_21_out_2),
    .out_4(get_new_state_for_one_string_of_matrix_7_out_4));
  convert_16_to_18 convert_16_to_18_21 (.in_1(register_8_q), .out_2(convert_16_to_18_21_out_2));
  convert_16_to_18 convert_16_to_18_22 (.in_1(register_7_q), .out_2(convert_16_to_18_22_out_2));
  get_new_state_for_one_string_of_Matrix get_new_state_for_one_string_of_matrix_8 (
    .in_1(convert_16_to_18_22_out_2), .in_2(convert_16_to_18_23_out_2), .in_3(convert_16_to_18_24_out_2),
    .out_4(get_new_state_for_one_string_of_matrix_8_out_4));
  convert_16_to_18 convert_16_to_18_23 (.in_1(register_8_q), .out_2(convert_16_to_18_23_out_2));
  convert_16_to_18 convert_16_to_18_24 (.in_1(register_9_q), .out_2(convert_16_to_18_24_out_2));
  convert_16_to_18 convert_16_to_18_25 (.in_1(register_8_q), .out_2(convert_16_to_18_25_out_2));
  get_new_state_for_one_string_of_Matrix get_new_state_for_one_string_of_matrix_9 (
    .in_1(convert_16_to_18_25_out_2), .in_2(convert_16_to_18_26_out_2), .in_3(convert_16_to_18_27_out_2),
    .out_4(get_new_state_for_one_string_of_matrix_9_out_4));
  convert_16_to_18 convert_16_to_18_26 (.in_1(register_9_q), .out_2(convert_16_to_18_26_out_2));
  convert_16_to_18 convert_16_to_18_27 (.in_1(register_10_q), .out_2(convert_16_to_18_27_out_2));
  convert_16_to_18 convert_16_to_18_28 (.in_1(register_9_q), .out_2(convert_16_to_18_28_out_2));
  get_new_state_for_one_string_of_Matrix get_new_state_for_one_string_of_matrix_10 (
    .in_1(convert_16_to_18_28_out_2), .in_2(convert_16_to_18_29_out_2), .in_3(convert_16_to_18_30_out_2),
    .out_4(get_new_state_for_one_string_of_matrix_10_out_4));
  convert_16_to_18 convert_16_to_18_29 (.in_1(register_10_q), .out_2(convert_16_to_18_29_out_2));
  convert_16_to_18 convert_16_to_18_30 (.in_1(register_11_q), .out_2(convert_16_to_18_30_out_2));
  convert_16_to_18 convert_16_to_18_31 (.in_1(register_10_q), .out_2(convert_16_to_18_31_out_2));
  get_new_state_for_one_string_of_Matrix get_new_state_for_one_string_of_matrix_11 (
    .in_1(convert_16_to_18_31_out_2), .in_2(convert_16_to_18_32_out_2), .in_3(convert_16_to_18_33_out_2),
    .out_4(get_new_state_for_one_string_of_matrix_11_out_4));
  convert_16_to_18 convert_16_to_18_32 (.in_1(register_11_q), .out_2(convert_16_to_18_32_out_2));
  convert_16_to_18 convert_16_to_18_33 (.in_1(register_12_q), .out_2(convert_16_to_18_33_out_2));
  convert_16_to_18 convert_16_to_18_34 (.in_1(register_11_q), .out_2(convert_16_to_18_34_out_2));
  get_new_state_for_one_string_of_Matrix get_new_state_for_one_string_of_matrix_12 (
    .in_1(convert_16_to_18_34_out_2), .in_2(convert_16_to_18_35_out_2), .in_3(convert_16_to_18_36_out_2),
    .out_4(get_new_state_for_one_string_of_matrix_12_out_4));
  convert_16_to_18 convert_16_to_18_35 (.in_1(register_12_q), .out_2(convert_16_to_18_35_out_2));
  convert_16_to_18 convert_16_to_18_36 (.in_1(register_13_q), .out_2(convert_16_to_18_36_out_2));
  convert_16_to_18 convert_16_to_18_37 (.in_1(register_12_q), .out_2(convert_16_to_18_37_out_2));
  get_new_state_for_one_string_of_Matrix get_new_state_for_one_string_of_matrix_13 (
    .in_1(convert_16_to_18_37_out_2), .in_2(convert_16_to_18_38_out_2), .in_3(convert_16_to_18_39_out_2),
    .out_4(get_new_state_for_one_string_of_matrix_13_out_4));
  convert_16_to_18 convert_16_to_18_38 (.in_1(register_13_q), .out_2(convert_16_to_18_38_out_2));
  convert_16_to_18 convert_16_to_18_39 (.in_1(register_14_q), .out_2(convert_16_to_18_39_out_2));
  convert_16_to_18 convert_16_to_18_40 (.in_1(register_13_q), .out_2(convert_16_to_18_40_out_2));
  get_new_state_for_one_string_of_Matrix get_new_state_for_one_string_of_matrix_14 (
    .in_1(convert_16_to_18_40_out_2), .in_2(convert_16_to_18_41_out_2), .in_3(convert_16_to_18_42_out_2),
    .out_4(get_new_state_for_one_string_of_matrix_14_out_4));
  convert_16_to_18 convert_16_to_18_41 (.in_1(register_14_q), .out_2(convert_16_to_18_41_out_2));
  convert_16_to_18 convert_16_to_18_42 (.in_1(register_15_q), .out_2(convert_16_to_18_42_out_2));
  convert_16_to_18 convert_16_to_18_43 (.in_1(register_14_q), .out_2(convert_16_to_18_43_out_2));
  get_new_state_for_one_string_of_Matrix get_new_state_for_one_string_of_matrix_15 (
    .in_1(convert_16_to_18_43_out_2), .in_2(convert_16_to_18_44_out_2), .in_3(convert_16_to_18_45_out_2),
    .out_4(get_new_state_for_one_string_of_matrix_15_out_4));
  convert_16_to_18 convert_16_to_18_44 (.in_1(register_15_q), .out_2(convert_16_to_18_44_out_2));
  convert_16_to_18 convert_16_to_18_45 (.in_1(down), .out_2(convert_16_to_18_45_out_2));
  convert_16_to_18 convert_16_to_18_46 (.in_1(register_15_q), .out_2(convert_16_to_18_46_out_2));
  convert_16_to_18 convert_16_to_18_47 (.in_1(down), .out_2(convert_16_to_18_47_out_2));
  get_new_state_for_one_string_of_Matrix get_new_state_for_one_string_of_matrix_16 (
    .in_1(convert_16_to_18_46_out_2), .in_2(convert_16_to_18_47_out_2), .in_3(convert_16_to_18_48_out_2),
    .out_4(get_new_state_for_one_string_of_matrix_16_out_4));
  convert_16_to_18 convert_16_to_18_48 (.in_1(up), .out_2(convert_16_to_18_48_out_2));
  Pull_Resistor pull_resistor_18 (.node(pull_resistor_18_node));
  assign pull_resistor_18_node = is ? _1 : 16'bz;  // Controlled_Buffer controlled_buffer_34
  Pull_Resistor pull_resistor_19 (.node(pull_resistor_19_node));
  assign pull_resistor_19_node = is ? _2 : 16'bz;  // Controlled_Buffer controlled_buffer_35
  assign out_37 = pull_resistor_19_node ^ register_2_q;  // XOR_Gate xor_17, 16 bits wide
  Pull_Resistor pull_resistor_20 (.node(pull_resistor_20_node));
  assign pull_resistor_20_node = is ? _3 : 16'bz;  // Controlled_Buffer controlled_buffer_36
  assign out_38 = pull_resistor_20_node ^ register_3_q;  // XOR_Gate xor_18, 16 bits wide
  Pull_Resistor pull_resistor_21 (.node(pull_resistor_21_node));
  assign pull_resistor_21_node = is ? _4 : 16'bz;  // Controlled_Buffer controlled_buffer_37
  assign out_39 = pull_resistor_21_node ^ register_4_q;  // XOR_Gate xor_19, 16 bits wide
  Pull_Resistor pull_resistor_22 (.node(pull_resistor_22_node));
  assign pull_resistor_22_node = is ? _5 : 16'bz;  // Controlled_Buffer controlled_buffer_38
  assign out_40 = pull_resistor_22_node ^ register_5_q;  // XOR_Gate xor_20, 16 bits wide
  Pull_Resistor pull_resistor_23 (.node(pull_resistor_23_node));
  assign pull_resistor_23_node = is ? _6 : 16'bz;  // Controlled_Buffer controlled_buffer_39
  assign out_41 = pull_resistor_23_node ^ register_6_q;  // XOR_Gate xor_21, 16 bits wide
  Pull_Resistor pull_resistor_24 (.node(pull_resistor_24_node));
  assign pull_resistor_24_node = is ? _7 : 16'bz;  // Controlled_Buffer controlled_buffer_40
  assign out_42 = pull_resistor_24_node ^ register_7_q;  // XOR_Gate xor_22, 16 bits wide
  assign controlled_buffer_41_out = is ? _8 : 16'bz;  // Controlled_Buffer controlled_buffer_41
  Pull_Resistor pull_resistor_25 (.node(controlled_buffer_41_out));
  assign out_43 = controlled_buffer_41_out ^ register_8_q;  // XOR_Gate xor_23, 16 bits wide
  Pull_Resistor pull_resistor_26 (.node(pull_resistor_26_node));
  assign pull_resistor_26_node = is ? _9 : 16'bz;  // Controlled_Buffer controlled_buffer_42
  assign out_44 = pull_resistor_26_node ^ register_9_q;  // XOR_Gate xor_24, 16 bits wide
  assign controlled_buffer_43_out = is ? _10 : 16'bz;  // Controlled_Buffer controlled_buffer_43
  Pull_Resistor pull_resistor_27 (.node(controlled_buffer_43_out));
  assign out_45 = controlled_buffer_43_out ^ register_10_q;  // XOR_Gate xor_25, 16 bits wide
  assign controlled_buffer_44_out = is ? _11 : 16'bz;  // Controlled_Buffer controlled_buffer_44
  Pull_Resistor pull_resistor_28 (.node(controlled_buffer_44_out));
  assign out_46 = controlled_buffer_44_out ^ register_11_q;  // XOR_Gate xor_26, 16 bits wide
  assign controlled_buffer_45_out = is ? _12 : 16'bz;  // Controlled_Buffer controlled_buffer_45
  Pull_Resistor pull_resistor_29 (.node(controlled_buffer_45_out));
  assign out_47 = controlled_buffer_45_out ^ register_12_q;  // XOR_Gate xor_27, 16 bits wide
  assign controlled_buffer_46_out = is ? _13 : 16'bz;  // Controlled_Buffer controlled_buffer_46
  Pull_Resistor pull_resistor_30 (.node(controlled_buffer_46_out));
  assign out_48 = controlled_buffer_46_out ^ register_13_q;  // XOR_Gate xor_28, 16 bits wide
  assign controlled_buffer_47_out = is ? _14 : 16'bz;  // Controlled_Buffer controlled_buffer_47
  Pull_Resistor pull_resistor_31 (.node(controlled_buffer_47_out));
  assign out_49 = controlled_buffer_47_out ^ register_14_q;  // XOR_Gate xor_29, 16 bits wide
  assign controlled_buffer_48_out = is ? _15 : 16'bz;  // Controlled_Buffer controlled_buffer_48
  Pull_Resistor pull_resistor_32 (.node(controlled_buffer_48_out));
  assign out_50 = controlled_buffer_48_out ^ register_15_q;  // XOR_Gate xor_30, 16 bits wide
  assign controlled_buffer_49_out = is ? _16 : 16'bz;  // Controlled_Buffer controlled_buffer_49
  Pull_Resistor pull_resistor_33 (.node(controlled_buffer_49_out));
  assign out_51 = controlled_buffer_49_out ^ down;  // XOR_Gate xor_31, 16 bits wide
  assign out_36 = pull_resistor_18_node ^ up;  // XOR_Gate xor_32, 16 bits wide
endmodule

module pointer (
  input  in_1,
  input  in_2,
  input  [15:0] in_3,
  output [15:0] out_4
);

  wire controlled_buffer_1_out, not_1_out;

  not not_1 (not_1_out, in_2);
  assign controlled_buffer_1_out = not_1_out ? in_1 : 1'bz;  // Controlled_Buffer controlled_buffer_1
  Pull_Resistor pull_resistor_1 (.node(controlled_buffer_1_out));
  \xor  xor_1 (.in_2(in_3[0]), .in_1(controlled_buffer_1_out), .out_3(out_4[0]));
  \xor  xor_2 (.in_2(in_3[1]), .in_1(controlled_buffer_1_out), .out_3(out_4[1]));
  \xor  xor_3 (.in_2(in_3[2]), .in_1(controlled_buffer_1_out), .out_3(out_4[2]));
  \xor  xor_4 (.in_2(in_3[3]), .in_1(controlled_buffer_1_out), .out_3(out_4[3]));
  \xor  xor_5 (.in_2(in_3[4]), .in_1(controlled_buffer_1_out), .out_3(out_4[4]));
  \xor  xor_6 (.in_2(in_3[5]), .in_1(controlled_buffer_1_out), .out_3(out_4[5]));
  \xor  xor_7 (.in_2(in_3[6]), .in_1(controlled_buffer_1_out), .out_3(out_4[6]));
  \xor  xor_8 (.in_2(in_3[7]), .in_1(controlled_buffer_1_out), .out_3(out_4[7]));
  \xor  xor_9 (.in_2(in_3[8]), .in_1(controlled_buffer_1_out), .out_3(out_4[8]));
  \xor  xor_10 (.in_2(in_3[9]), .in_1(controlled_buffer_1_out), .out_3(out_4[9]));
  \xor  xor_11 (.in_2(in_3[10]), .in_1(controlled_buffer_1_out), .out_3(out_4[10]));
  \xor  xor_12 (.in_2(in_3[11]), .in_1(controlled_buffer_1_out), .out_3(out_4[11]));
  \xor  xor_13 (.in_2(in_3[12]), .in_1(controlled_buffer_1_out), .out_3(out_4[12]));
  \xor  xor_14 (.in_2(in_3[13]), .in_1(controlled_buffer_1_out), .out_3(out_4[13]));
  \xor  xor_15 (.in_2(in_3[14]), .in_1(controlled_buffer_1_out), .out_3(out_4[14]));
  \xor  xor_16 (.in_2(in_3[15]), .in_1(controlled_buffer_1_out), .out_3(out_4[15]));
endmodule

module \xor  (
  input  in_1,
  input  in_2,
  output out_3
);

  Pull_Resistor pull_resistor_1 (.node(out_3));
  assign out_3 = in_2 ? in_1 : 1'bz;  // Controlled_Buffer controlled_buffer_1
endmodule

module cdm (
  input  in_1,
  input  in_2,
  input  in_3,
  input  in_4,
  input  in_5,
  output Change_Bit_State,
  output [3:0] out_7,
  output [3:0] out_8
);

  wire and_2_out, and_3_out, and_4_out, cdm_8_mark5_1_p1, cdm_8_mark5_1_p2, cdm_8_mark5_1_p4,
       cdm_8_mark5_1_p5, cdm_8_mark5_1_p6, cdm_8_mark5_1_p8, cdm_8_mark5_1_p9, cdm_8_mark5_1_p10, clk,
       decoder_1_out0, decoder_1_out1, decoder_2_out0, decoder_2_out1, IOsel, nor_1_out, nor_2_out,
       not_1_out, not_2_out, not_3_out, not_4_out, not_5_out, READwrite, transistor_1_out;
  wire [3:0] IOaddr;
  wire [6:0] controlled_buffer_1_out, register_1_q;
  wire [7:0] cdm_8_mark5_1_p13, cdm_8_mark5_1_p14, IOdat, setBit;
  wire [7:4] cdm_8_mark5_1_p12;
  wire [7:7] s_r_ff_1_qn;

  Clock #(.lowDuration(2)) clock_1 (.out(clk));
  // Probe on cdm_8_mark5_1_p1
  // Probe on 7'b0001000
  Transistor #(.\type ("n")) transistor_1 (.in(1'b0), .out(transistor_1_out), .gate(in_1));
  assign controlled_buffer_1_out = in_1 ? 7'b0001000 : 7'bz;  // Controlled_Buffer controlled_buffer_1
  // Probe on cdm_8_mark5_1_p5
  // Probe on cdm_8_mark5_1_p4
  // Probe on cdm_8_mark5_1_p2
  // Probe on cdm_8_mark5_1_p6
  // Probe on 7'b1000000
  Transistor #(.\type ("n")) transistor_2 (.in(1'b0), .out(transistor_1_out), .gate(in_2));
  assign controlled_buffer_1_out = in_2 ? 7'b1000000 : 7'bz;  // Controlled_Buffer controlled_buffer_2
  not not_1 (not_1_out, transistor_1_out);
  nor nor_1 (nor_1_out, not_1_out, transistor_1_out);
  not not_2 (not_2_out, decoder_2_out1);
  nor nor_2 (nor_2_out, not_2_out, decoder_2_out1);
  // Probe on IOdat
  // Probe on IOaddr
  and and_1 (IOsel, cdm_8_mark5_1_p12[4], cdm_8_mark5_1_p12[5], cdm_8_mark5_1_p12[6], cdm_8_mark5_1_p12[7], decoder_1_out1);
  // Probe on cdm_8_mark5_1_p8
  Decoder #(.disabled(0)) decoder_1 (
    .out0(decoder_1_out0), .out1(decoder_1_out1), .sel(cdm_8_mark5_1_p9), .en(cdm_8_mark5_1_p10));
  // CdM_8_mark5 cdm_8_mark5_1: pin names not known; wires that end beside it: cdm_8_mark5_1_p1, cdm_8_mark5_1_p2, clk, cdm_8_mark5_1_p4, cdm_8_mark5_1_p5, cdm_8_mark5_1_p6, setBit, cdm_8_mark5_1_p8, cdm_8_mark5_1_p9, cdm_8_mark5_1_p10, READwrite, {cdm_8_mark5_1_p12, IOaddr}, cdm_8_mark5_1_p13, cdm_8_mark5_1_p14
  not not_3 (not_3_out, READwrite);
  assign cdm_8_mark5_1_p14 = READwrite ? IOdat : 8'bz;  // Controlled_Buffer controlled_buffer_3
  // Probe on 7'b0100000
  Transistor #(.\type ("n")) transistor_3 (.in(1'b0), .out(transistor_1_out), .gate(in_3));
  assign controlled_buffer_1_out = in_3 ? 7'b0100000 : 7'bz;  // Controlled_Buffer controlled_buffer_4
  S_R_Flip_Flop #(.trigger("low")) s_r_ff_1 (
    .S(nor_1_out), .clk(1'b0), .R(nor_2_out), .Qn(s_r_ff_1_qn[7]));  // open: Q, preset, reset, en
  assign IOdat = not_3_out ? cdm_8_mark5_1_p13 : 8'bz;  // Controlled_Buffer controlled_buffer_5
  // Probe on 7'b0010000
  Transistor #(.\type ("n")) transistor_4 (.in(1'b0), .out(transistor_1_out), .gate(in_4));
  assign controlled_buffer_1_out = in_4 ? 7'b0010000 : 7'bz;  // Controlled_Buffer controlled_buffer_6
  // Probe on {cdm_8_mark5_1_p12, IOaddr}
  and and_2 (and_2_out, decoder_1_out1, ~IOsel);  // AND_Gate
  // Probe on {7{1'b0}}
  Transistor #(.\type ("n")) transistor_5 (.in(1'b0), .out(transistor_1_out), .gate(in_5));
  assign controlled_buffer_1_out = in_5 ? {7{1'b0}} : 7'bz;  // Controlled_Buffer controlled_buffer_7
  Pull_Resistor #(.pull(1)) pull_resistor_1 (.node(transistor_1_out));
  Register #(.width(7), .trigger("falling")) register_1 (
    .D(controlled_buffer_1_out), .en(1'b1), .Q(register_1_q), .clk(not_4_out));  // open: clr
  not not_4 (not_4_out, not_5_out);
  not not_5 (not_5_out, transistor_1_out);
  // Probe on IOdat
  RAM ram_1 (
    .addr({cdm_8_mark5_1_p12, IOaddr}), .data(IOdat), .sel(and_2_out), .clk(clk), .ld(READwrite));  // open: clr
  ROM rom_1 (.addr({cdm_8_mark5_1_p12, IOaddr}), .data(IOdat), .sel(decoder_1_out0));
  assign IOdat = decoder_2_out1 ? {s_r_ff_1_qn[7], register_1_q} : 8'bz;  // Controlled_Buffer controlled_buffer_8
  Decoder #(.disabled(0)) decoder_2 (.out0(decoder_2_out0), .out1(decoder_2_out1), .sel(READwrite), .en(and_3_out));
  and and_3 (and_3_out, IOsel, IOaddr[0], IOaddr[1], ~IOaddr[2], ~IOaddr[3]);  // AND_Gate
  Register #(.trigger("falling")) register_2 (
    .D(IOdat), .en(decoder_2_out0), .Q({out_7, out_8}), .clk(clk));  // open: clr
  and and_4 (and_4_out, IOsel, IOaddr[0], ~IOaddr[1], ~IOaddr[2], ~IOaddr[3]);  // AND_Gate
  assign Change_Bit_State = READwrite ? and_4_out : 1'bz;  // Controlled_Buffer controlled_buffer_9
  Pull_Resistor pull_resistor_2 (.node(Change_Bit_State));

  // Notes on the sheet:
  //   contents of rom_1 (hex, n*v repeats v):
  //   d0 f0 c1 d1 8 a4 c5 cd 0 d0 f3 d2 10 d3 0 b1 5 e4 f 95 e1 1a 8f a3 ee f 95 e1 21 8b a3 ee f 95 e1 28
  //   1b a3 ee f 95 e1 31 86 1b 86 a3 ee f 95 e1 3b d0 f1 a0 d0 f3 ee f ee f
  //   Current position of pointer
endmodule

module inputState (
  input  [3:0] in_1,
  input  [3:0] in_2,
  input  in_3,
  output [15:0] out_4,
  output out_5,
  output [15:0] out_6,
  output out_7,
  output [15:0] out_8,
  output out_9,
  output [15:0] out_10,
  output out_11,
  output [15:0] out_12,
  output out_13,
  output [15:0] out_14,
  output out_15,
  output [15:0] out_16,
  output out_17,
  output [15:0] out_18,
  output out_19,
  output [15:0] out_20,
  output out_21,
  output [15:0] out_22,
  output out_23,
  output [15:0] out_24,
  output out_25,
  output [15:0] out_26,
  output out_27,
  output [15:0] out_28,
  output out_29,
  output [15:0] out_30,
  output out_31,
  output [15:0] out_32,
  output out_33,
  output [15:0] out_34,
  output out_35
);

  wire decoder_1_out0, decoder_1_out1, decoder_1_out2, decoder_1_out3, decoder_1_out4, decoder_1_out5,
       decoder_1_out6, decoder_1_out7, decoder_1_out8, decoder_1_out9, decoder_1_out10, decoder_1_out11,
       decoder_1_out12, decoder_1_out13, decoder_1_out14, decoder_1_out15, decoder_2_out0, decoder_2_out1,
       decoder_2_out2, decoder_2_out3, decoder_2_out4, decoder_2_out5, decoder_2_out6, decoder_2_out7,
       decoder_2_out8, decoder_2_out9, decoder_2_out10, decoder_2_out11, decoder_2_out12, decoder_2_out13,
       decoder_2_out14, decoder_2_out15, input_1_out_20, input_2_out_20, input_3_out_20, input_4_out_20,
       input_5_out_20, input_6_out_20, input_7_out_20, input_8_out_20, input_9_out_20, input_10_out_20,
       input_11_out_20, input_12_out_20, input_13_out_20, input_14_out_20, input_15_out_20, input_16_out_20,
       not_1_out, not_2_out, not_3_out, not_4_out, not_5_out, not_6_out, not_7_out, not_8_out, not_9_out,
       not_10_out, not_11_out, not_12_out, not_13_out, not_14_out, not_15_out, not_16_out, not_17_out,
       not_18_out, not_19_out, not_20_out, not_21_out, not_22_out, not_23_out, not_24_out, not_25_out,
       not_26_out, not_27_out, not_28_out, not_29_out, not_30_out, not_31_out, not_32_out, not_33_out,
       not_34_out, not_35_out, not_36_out, not_37_out, not_38_out, not_39_out, not_40_out, not_41_out,
       not_42_out, not_43_out, not_44_out, not_45_out, not_46_out, not_47_out, not_48_out, not_49_out,
       not_50_out, not_51_out, not_52_out, not_53_out, not_54_out, not_55_out, not_56_out, not_57_out,
       not_58_out, not_59_out, not_60_out, not_61_out, not_62_out, not_63_out, not_64_out, not_65_out,
       not_67_out, not_68_out, not_69_out, not_70_out, not_72_out, not_73_out, not_75_out, not_76_out,
       not_77_out, not_78_out, not_80_out, not_82_out, not_83_out, not_84_out, not_85_out, not_86_out,
       not_88_out, not_90_out, not_91_out, not_92_out, not_94_out, not_95_out, not_96_out, not_97_out,
       not_98_out, not_99_out, not_101_out, not_103_out, not_104_out, not_105_out, not_107_out, not_108_out,
       not_109_out, not_111_out, not_112_out, not_113_out, not_115_out, not_116_out, not_117_out,
       not_119_out, not_120_out, not_121_out, not_122_out, not_124_out, not_126_out, not_127_out, not_128_out;

  Decoder #(.select(4), .enable("false")) decoder_1 (
    .out0(decoder_1_out0), .out1(decoder_1_out1), .out2(decoder_1_out2), .out3(decoder_1_out3),
    .out4(decoder_1_out4), .out5(decoder_1_out5), .out6(decoder_1_out6), .out7(decoder_1_out7),
    .out8(decoder_1_out8), .out9(decoder_1_out9), .out10(decoder_1_out10), .out11(decoder_1_out11),
    .out12(decoder_1_out12), .out13(decoder_1_out13), .out14(decoder_1_out14), .out15(decoder_1_out15),
    .sel(in_2));
  Decoder #(.select(4), .enable("false")) decoder_2 (
    .out0(decoder_2_out0), .out1(decoder_2_out1), .out2(decoder_2_out2), .out3(decoder_2_out3),
    .out4(decoder_2_out4), .out5(decoder_2_out5), .out6(decoder_2_out6), .out7(decoder_2_out7),
    .out8(decoder_2_out8), .out9(decoder_2_out9), .out10(decoder_2_out10), .out11(decoder_2_out11),
    .out12(decoder_2_out12), .out13(decoder_2_out13), .out14(decoder_2_out14), .out15(decoder_2_out15),
    .sel(in_1));
  \input  input_1 (
    .in_1(decoder_1_out0), .in_18(in_3), .in_2(decoder_2_out0), .in_3(decoder_2_out1), .in_4(decoder_2_out2),
    .in_5(decoder_2_out3), .in_6(decoder_2_out4), .in_7(decoder_2_out5), .in_8(decoder_2_out6),
    .in_9(decoder_2_out7), .in_10(decoder_2_out8), .in_11(decoder_2_out9), .in_12(decoder_2_out10),
    .in_13(decoder_2_out11), .in_14(decoder_2_out12), .in_15(decoder_2_out13), .in_16(decoder_2_out14),
    .in_17(decoder_2_out15), .out_19(out_4), .out_20(input_1_out_20));
  \input  input_2 (
    .in_1(decoder_1_out1), .in_18(in_3), .in_2(decoder_2_out0), .in_3(decoder_2_out1), .in_4(decoder_2_out2),
    .in_5(decoder_2_out3), .in_6(decoder_2_out4), .in_7(decoder_2_out5), .in_8(decoder_2_out6),
    .in_9(decoder_2_out7), .in_10(decoder_2_out8), .in_11(decoder_2_out9), .in_12(decoder_2_out10),
    .in_13(decoder_2_out11), .in_14(decoder_2_out12), .in_15(decoder_2_out13), .in_16(decoder_2_out14),
    .in_17(decoder_2_out15), .out_19(out_6), .out_20(input_2_out_20));
  \input  input_3 (
    .in_1(decoder_1_out2), .in_18(in_3), .in_2(decoder_2_out0), .in_3(decoder_2_out1), .in_4(decoder_2_out2),
    .in_5(decoder_2_out3), .in_6(decoder_2_out4), .in_7(decoder_2_out5), .in_8(decoder_2_out6),
    .in_9(decoder_2_out7), .in_10(decoder_2_out8), .in_11(decoder_2_out9), .in_12(decoder_2_out10),
    .in_13(decoder_2_out11), .in_14(decoder_2_out12), .in_15(decoder_2_out13), .in_16(decoder_2_out14),
    .in_17(decoder_2_out15), .out_19(out_8), .out_20(input_3_out_20));
  \input  input_4 (
    .in_1(decoder_1_out3), .in_18(in_3), .in_2(decoder_2_out0), .in_3(decoder_2_out1), .in_4(decoder_2_out2),
    .in_5(decoder_2_out3), .in_6(decoder_2_out4), .in_7(decoder_2_out5), .in_8(decoder_2_out6),
    .in_9(decoder_2_out7), .in_10(decoder_2_out8), .in_11(decoder_2_out9), .in_12(decoder_2_out10),
    .in_13(decoder_2_out11), .in_14(decoder_2_out12), .in_15(decoder_2_out13), .in_16(decoder_2_out14),
    .in_17(decoder_2_out15), .out_19(out_10), .out_20(input_4_out_20));
  \input  input_5 (
    .in_1(decoder_1_out4), .in_18(in_3), .in_2(decoder_2_out0), .in_3(decoder_2_out1), .in_4(decoder_2_out2),
    .in_5(decoder_2_out3), .in_6(decoder_2_out4), .in_7(decoder_2_out5), .in_8(decoder_2_out6),
    .in_9(decoder_2_out7), .in_10(decoder_2_out8), .in_11(decoder_2_out9), .in_12(decoder_2_out10),
    .in_13(decoder_2_out11), .in_14(decoder_2_out12), .in_15(decoder_2_out13), .in_16(decoder_2_out14),
    .in_17(decoder_2_out15), .out_19(out_12), .out_20(input_5_out_20));
  \input  input_6 (
    .in_1(decoder_1_out5), .in_18(in_3), .in_2(decoder_2_out0), .in_3(decoder_2_out1), .in_4(decoder_2_out2),
    .in_5(decoder_2_out3), .in_6(decoder_2_out4), .in_7(decoder_2_out5), .in_8(decoder_2_out6),
    .in_9(decoder_2_out7), .in_10(decoder_2_out8), .in_11(decoder_2_out9), .in_12(decoder_2_out10),
    .in_13(decoder_2_out11), .in_14(decoder_2_out12), .in_15(decoder_2_out13), .in_16(decoder_2_out14),
    .in_17(decoder_2_out15), .out_19(out_14), .out_20(input_6_out_20));
  \input  input_7 (
    .in_1(decoder_1_out6), .in_18(in_3), .in_2(decoder_2_out0), .in_3(decoder_2_out1), .in_4(decoder_2_out2),
    .in_5(decoder_2_out3), .in_6(decoder_2_out4), .in_7(decoder_2_out5), .in_8(decoder_2_out6),
    .in_9(decoder_2_out7), .in_10(decoder_2_out8), .in_11(decoder_2_out9), .in_12(decoder_2_out10),
    .in_13(decoder_2_out11), .in_14(decoder_2_out12), .in_15(decoder_2_out13), .in_16(decoder_2_out14),
    .in_17(decoder_2_out15), .out_19(out_16), .out_20(input_7_out_20));
  \input  input_8 (
    .in_1(decoder_1_out7), .in_18(in_3), .in_2(decoder_2_out0), .in_3(decoder_2_out1), .in_4(decoder_2_out2),
    .in_5(decoder_2_out3), .in_6(decoder_2_out4), .in_7(decoder_2_out5), .in_8(decoder_2_out6),
    .in_9(decoder_2_out7), .in_10(decoder_2_out8), .in_11(decoder_2_out9), .in_12(decoder_2_out10),
    .in_13(decoder_2_out11), .in_14(decoder_2_out12), .in_15(decoder_2_out13), .in_16(decoder_2_out14),
    .in_17(decoder_2_out15), .out_19(out_18), .out_20(input_8_out_20));
  \input  input_9 (
    .in_1(decoder_1_out8), .in_18(in_3), .in_2(decoder_2_out0), .in_3(decoder_2_out1), .in_4(decoder_2_out2),
    .in_5(decoder_2_out3), .in_6(decoder_2_out4), .in_7(decoder_2_out5), .in_8(decoder_2_out6),
    .in_9(decoder_2_out7), .in_10(decoder_2_out8), .in_11(decoder_2_out9), .in_12(decoder_2_out10),
    .in_13(decoder_2_out11), .in_14(decoder_2_out12), .in_15(decoder_2_out13), .in_16(decoder_2_out14),
    .in_17(decoder_2_out15), .out_19(out_20), .out_20(input_9_out_20));
  \input  input_10 (
    .in_1(decoder_1_out9), .in_18(in_3), .in_2(decoder_2_out0), .in_3(decoder_2_out1), .in_4(decoder_2_out2),
    .in_5(decoder_2_out3), .in_6(decoder_2_out4), .in_7(decoder_2_out5), .in_8(decoder_2_out6),
    .in_9(decoder_2_out7), .in_10(decoder_2_out8), .in_11(decoder_2_out9), .in_12(decoder_2_out10),
    .in_13(decoder_2_out11), .in_14(decoder_2_out12), .in_15(decoder_2_out13), .in_16(decoder_2_out14),
    .in_17(decoder_2_out15), .out_19(out_22), .out_20(input_10_out_20));
  \input  input_11 (
    .in_1(decoder_1_out10), .in_18(in_3), .in_2(decoder_2_out0), .in_3(decoder_2_out1),
    .in_4(decoder_2_out2), .in_5(decoder_2_out3), .in_6(decoder_2_out4), .in_7(decoder_2_out5),
    .in_8(decoder_2_out6), .in_9(decoder_2_out7), .in_10(decoder_2_out8), .in_11(decoder_2_out9),
    .in_12(decoder_2_out10), .in_13(decoder_2_out11), .in_14(decoder_2_out12), .in_15(decoder_2_out13),
    .in_16(decoder_2_out14), .in_17(decoder_2_out15), .out_19(out_24), .out_20(input_11_out_20));
  \input  input_12 (
    .in_1(decoder_1_out11), .in_18(in_3), .in_2(decoder_2_out0), .in_3(decoder_2_out1),
    .in_4(decoder_2_out2), .in_5(decoder_2_out3), .in_6(decoder_2_out4), .in_7(decoder_2_out5),
    .in_8(decoder_2_out6), .in_9(decoder_2_out7), .in_10(decoder_2_out8), .in_11(decoder_2_out9),
    .in_12(decoder_2_out10), .in_13(decoder_2_out11), .in_14(decoder_2_out12), .in_15(decoder_2_out13),
    .in_16(decoder_2_out14), .in_17(decoder_2_out15), .out_19(out_26), .out_20(input_12_out_20));
  \input  input_13 (
    .in_1(decoder_1_out12), .in_18(in_3), .in_2(decoder_2_out0), .in_3(decoder_2_out1),
    .in_4(decoder_2_out2), .in_5(decoder_2_out3), .in_6(decoder_2_out4), .in_7(decoder_2_out5),
    .in_8(decoder_2_out6), .in_9(decoder_2_out7), .in_10(decoder_2_out8), .in_11(decoder_2_out9),
    .in_12(decoder_2_out10), .in_13(decoder_2_out11), .in_14(decoder_2_out12), .in_15(decoder_2_out13),
    .in_16(decoder_2_out14), .in_17(decoder_2_out15), .out_19(out_28), .out_20(input_13_out_20));
  \input  input_14 (
    .in_1(decoder_1_out13), .in_18(in_3), .in_2(decoder_2_out0), .in_3(decoder_2_out1),
    .in_4(decoder_2_out2), .in_5(decoder_2_out3), .in_6(decoder_2_out4), .in_7(decoder_2_out5),
    .in_8(decoder_2_out6), .in_9(decoder_2_out7), .in_10(decoder_2_out8), .in_11(decoder_2_out9),
    .in_12(decoder_2_out10), .in_13(decoder_2_out11), .in_14(decoder_2_out12), .in_15(decoder_2_out13),
    .in_16(decoder_2_out14), .in_17(decoder_2_out15), .out_19(out_30), .out_20(input_14_out_20));
  \input  input_15 (
    .in_1(decoder_1_out14), .in_18(in_3), .in_2(decoder_2_out0), .in_3(decoder_2_out1),
    .in_4(decoder_2_out2), .in_5(decoder_2_out3), .in_6(decoder_2_out4), .in_7(decoder_2_out5),
    .in_8(decoder_2_out6), .in_9(decoder_2_out7), .in_10(decoder_2_out8), .in_11(decoder_2_out9),
    .in_12(decoder_2_out10), .in_13(decoder_2_out11), .in_14(decoder_2_out12), .in_15(decoder_2_out13),
    .in_16(decoder_2_out14), .in_17(decoder_2_out15), .out_19(out_32), .out_20(input_15_out_20));
  \input  input_16 (
    .in_1(decoder_1_out15), .in_18(in_3), .in_2(decoder_2_out0), .in_3(decoder_2_out1),
    .in_4(decoder_2_out2), .in_5(decoder_2_out3), .in_6(decoder_2_out4), .in_7(decoder_2_out5),
    .in_8(decoder_2_out6), .in_9(decoder_2_out7), .in_10(decoder_2_out8), .in_11(decoder_2_out9),
    .in_12(decoder_2_out10), .in_13(decoder_2_out11), .in_14(decoder_2_out12), .in_15(decoder_2_out13),
    .in_16(decoder_2_out14), .in_17(decoder_2_out15), .out_19(out_34), .out_20(input_16_out_20));
  not not_1 (not_1_out, input_1_out_20);
  not not_2 (not_2_out, not_4_out);
  not not_3 (not_3_out, not_2_out);
  not not_4 (not_4_out, not_1_out);
  not not_5 (not_5_out, not_8_out);
  not not_6 (not_6_out, not_7_out);
  not not_7 (not_7_out, not_5_out);
  not not_8 (not_8_out, input_2_out_20);
  not not_9 (not_9_out, input_3_out_20);
  not not_10 (not_10_out, not_11_out);
  not not_11 (not_11_out, not_9_out);
  not not_12 (not_12_out, not_10_out);
  not not_13 (not_13_out, not_15_out);
  not not_14 (not_14_out, not_13_out);
  not not_15 (not_15_out, not_16_out);
  not not_16 (not_16_out, input_4_out_20);
  not not_17 (not_17_out, input_5_out_20);
  not not_18 (not_18_out, not_20_out);
  not not_19 (not_19_out, not_17_out);
  not not_20 (not_20_out, not_19_out);
  not not_21 (not_21_out, not_23_out);
  not not_22 (not_22_out, not_24_out);
  not not_23 (not_23_out, not_22_out);
  not not_24 (not_24_out, input_6_out_20);
  not not_25 (not_25_out, not_26_out);
  not not_26 (not_26_out, not_27_out);
  not not_27 (not_27_out, input_7_out_20);
  not not_28 (not_28_out, not_25_out);
  not not_29 (not_29_out, not_30_out);
  not not_30 (not_30_out, input_8_out_20);
  not not_31 (not_31_out, not_32_out);
  not not_32 (not_32_out, not_29_out);
  not not_33 (not_33_out, not_35_out);
  not not_34 (not_34_out, not_33_out);
  not not_35 (not_35_out, not_36_out);
  not not_36 (not_36_out, input_9_out_20);
  not not_37 (not_37_out, not_38_out);
  not not_38 (not_38_out, not_39_out);
  not not_39 (not_39_out, input_10_out_20);
  not not_40 (not_40_out, not_37_out);
  not not_41 (not_41_out, not_44_out);
  not not_42 (not_42_out, not_43_out);
  not not_43 (not_43_out, not_41_out);
  not not_44 (not_44_out, input_11_out_20);
  not not_45 (not_45_out, not_48_out);
  not not_46 (not_46_out, input_12_out_20);
  not not_47 (not_47_out, not_45_out);
  not not_48 (not_48_out, not_46_out);
  not not_49 (not_49_out, not_50_out);
  not not_50 (not_50_out, not_52_out);
  not not_51 (not_51_out, input_13_out_20);
  not not_52 (not_52_out, not_51_out);
  not not_53 (not_53_out, not_54_out);
  not not_54 (not_54_out, not_56_out);
  not not_55 (not_55_out, not_53_out);
  not not_56 (not_56_out, input_14_out_20);
  not not_57 (not_57_out, not_59_out);
  not not_58 (not_58_out, input_15_out_20);
  not not_59 (not_59_out, not_60_out);
  not not_60 (not_60_out, not_58_out);
  not not_61 (not_61_out, not_62_out);
  not not_62 (not_62_out, not_64_out);
  not not_63 (not_63_out, input_16_out_20);
  not not_64 (not_64_out, not_63_out);
  not not_65 (not_65_out, not_3_out);
  not not_66 (out_5, not_67_out);
  not not_67 (not_67_out, not_68_out);
  not not_68 (not_68_out, not_65_out);
  not not_69 (not_69_out, not_70_out);
  not not_70 (not_70_out, not_72_out);
  not not_71 (out_7, not_69_out);
  not not_72 (not_72_out, not_6_out);
  not not_73 (not_73_out, not_75_out);
  not not_74 (out_9, not_73_out);
  not not_75 (not_75_out, not_76_out);
  not not_76 (not_76_out, not_12_out);
  not not_77 (not_77_out, not_14_out);
  not not_78 (not_78_out, not_77_out);
  not not_79 (out_11, not_80_out);
  not not_80 (not_80_out, not_78_out);
  not not_81 (out_13, not_82_out);
  not not_82 (not_82_out, not_83_out);
  not not_83 (not_83_out, not_84_out);
  not not_84 (not_84_out, not_18_out);
  not not_85 (not_85_out, not_88_out);
  not not_86 (not_86_out, not_85_out);
  not not_87 (out_15, not_86_out);
  not not_88 (not_88_out, not_21_out);
  not not_89 (out_17, not_92_out);
  not not_90 (not_90_out, not_28_out);
  not not_91 (not_91_out, not_90_out);
  not not_92 (not_92_out, not_91_out);
  not not_93 (out_19, not_96_out);
  not not_94 (not_94_out, not_95_out);
  not not_95 (not_95_out, not_31_out);
  not not_96 (not_96_out, not_94_out);
  not not_97 (not_97_out, not_98_out);
  not not_98 (not_98_out, not_99_out);
  not not_99 (not_99_out, not_34_out);
  not not_100 (out_21, not_97_out);
  not not_101 (not_101_out, not_104_out);
  not not_102 (out_23, not_101_out);
  not not_103 (not_103_out, not_40_out);
  not not_104 (not_104_out, not_103_out);
  not not_105 (not_105_out, not_108_out);
  not not_106 (out_25, not_105_out);
  not not_107 (not_107_out, not_42_out);
  not not_108 (not_108_out, not_107_out);
  not not_109 (not_109_out, not_111_out);
  not not_110 (out_27, not_109_out);
  not not_111 (not_111_out, not_112_out);
  not not_112 (not_112_out, not_47_out);
  not not_113 (not_113_out, not_49_out);
  not not_114 (out_29, not_115_out);
  not not_115 (not_115_out, not_116_out);
  not not_116 (not_116_out, not_113_out);
  not not_117 (not_117_out, not_119_out);
  not not_118 (out_31, not_117_out);
  not not_119 (not_119_out, not_120_out);
  not not_120 (not_120_out, not_55_out);
  not not_121 (not_121_out, not_122_out);
  not not_122 (not_122_out, not_57_out);
  not not_123 (out_33, not_124_out);
  not not_124 (not_124_out, not_121_out);
  not not_125 (out_35, not_127_out);
  not not_126 (not_126_out, not_61_out);
  not not_127 (not_127_out, not_128_out);
  not not_128 (not_128_out, not_126_out);

  // Other names for the same wires on the sheet: set_prime = in_3
endmodule

module \input  (
  input  in_1,
  input  in_2,
  input  in_3,
  input  in_4,
  input  in_5,
  input  in_6,
  input  in_7,
  input  in_8,
  input  in_9,
  input  in_10,
  input  in_11,
  input  in_12,
  input  in_13,
  input  in_14,
  input  in_15,
  input  in_16,
  input  in_17,
  input  in_18,
  output [15:0] out_19,
  output out_20
);

  wire or_1_out;

  and and_1 (out_19[15], in_1, in_2);
  and and_2 (out_19[13], in_1, in_4);
  and and_3 (out_19[14], in_1, in_3);
  and and_4 (out_19[12], in_1, in_5);
  and and_5 (out_19[11], in_1, in_6);
  and and_6 (out_19[10], in_1, in_7);
  and and_7 (out_19[9], in_1, in_8);
  and and_8 (out_19[8], in_1, in_9);
  and and_9 (out_19[7], in_1, in_10);
  and and_10 (out_19[5], in_1, in_12);
  and and_11 (out_19[6], in_1, in_11);
  and and_12 (out_19[3], in_1, in_14);
  and and_13 (out_19[4], in_1, in_13);
  and and_14 (out_19[2], in_1, in_15);
  and and_15 (out_19[1], in_1, in_16);
  and and_16 (out_19[0], in_1, in_17);
  or or_1 (or_1_out, out_19[0], out_19[1], out_19[2], out_19[3], out_19[4], out_19[5], out_19[6], out_19[7], out_19[8], out_19[9], out_19[10], out_19[11], out_19[12], out_19[13], out_19[14], out_19[15], 1'b0);
  and and_17 (out_20, or_1_out, in_18);

  // Notes on the sheet:
  //   out_19: pull=down
endmodule

module convert_16_to_18 (
  input  [15:0] in_1,
  output [17:0] out_2
);


  assign out_2 = {in_1[0], in_1, in_1[15]};

  // Notes on the sheet:
  //   Перевожу в 18 битную строку, чтобы зациклить поле.
  //   Делаю первый и последний столбик соседями
endmodule

module get_new_state_for_one_string_of_Matrix (
  input  [17:0] in_1,
  input  [17:0] in_2,
  input  [17:0] in_3,
  output [15:0] out_4
);

  get_new_state_for_one_element get_new_state_for_one_element_1 (
    .in_1(in_1[0]), .in_2(in_1[1]), .in_3(in_1[2]), .in_4(in_2[0]), .in_5(in_2[2]), .current(in_2[1]),
    .in_7(in_3[0]), .in_8(in_3[1]), .in_9(in_3[2]), .out_10(out_4[0]));
  get_new_state_for_one_element get_new_state_for_one_element_2 (
    .in_1(in_1[1]), .in_2(in_1[2]), .in_3(in_1[3]), .in_4(in_2[1]), .in_5(in_2[3]), .current(in_2[2]),
    .in_7(in_3[1]), .in_8(in_3[2]), .in_9(in_3[3]), .out_10(out_4[1]));
  get_new_state_for_one_element get_new_state_for_one_element_3 (
    .in_1(in_1[2]), .in_2(in_1[3]), .in_3(in_1[4]), .in_4(in_2[2]), .in_5(in_2[4]), .current(in_2[3]),
    .in_7(in_3[2]), .in_8(in_3[3]), .in_9(in_3[4]), .out_10(out_4[2]));
  get_new_state_for_one_element get_new_state_for_one_element_4 (
    .in_1(in_1[3]), .in_2(in_1[4]), .in_3(in_1[5]), .in_4(in_2[3]), .in_5(in_2[5]), .current(in_2[4]),
    .in_7(in_3[3]), .in_8(in_3[4]), .in_9(in_3[5]), .out_10(out_4[3]));
  get_new_state_for_one_element get_new_state_for_one_element_5 (
    .in_1(in_1[4]), .in_2(in_1[5]), .in_3(in_1[6]), .in_4(in_2[4]), .in_5(in_2[6]), .current(in_2[5]),
    .in_7(in_3[4]), .in_8(in_3[5]), .in_9(in_3[6]), .out_10(out_4[4]));
  get_new_state_for_one_element get_new_state_for_one_element_6 (
    .in_1(in_1[5]), .in_2(in_1[6]), .in_3(in_1[7]), .in_4(in_2[5]), .in_5(in_2[7]), .current(in_2[6]),
    .in_7(in_3[5]), .in_8(in_3[6]), .in_9(in_3[7]), .out_10(out_4[5]));
  get_new_state_for_one_element get_new_state_for_one_element_7 (
    .in_1(in_1[6]), .in_2(in_1[7]), .in_3(in_1[8]), .in_4(in_2[6]), .in_5(in_2[8]), .current(in_2[7]),
    .in_7(in_3[6]), .in_8(in_3[7]), .in_9(in_3[8]), .out_10(out_4[6]));
  get_new_state_for_one_element get_new_state_for_one_element_8 (
    .in_1(in_1[7]), .in_2(in_1[8]), .in_3(in_1[9]), .in_4(in_2[7]), .in_5(in_2[9]), .current(in_2[8]),
    .in_7(in_3[7]), .in_8(in_3[8]), .in_9(in_3[9]), .out_10(out_4[7]));
  get_new_state_for_one_element get_new_state_for_one_element_9 (
    .in_1(in_1[8]), .in_2(in_1[9]), .in_3(in_1[10]), .in_4(in_2[8]), .in_5(in_2[10]), .current(in_2[9]),
    .in_7(in_3[8]), .in_8(in_3[9]), .in_9(in_3[10]), .out_10(out_4[8]));
  get_new_state_for_one_element get_new_state_for_one_element_10 (
    .in_1(in_1[9]), .in_2(in_1[10]), .in_3(in_1[11]), .in_4(in_2[9]), .in_5(in_2[11]), .current(in_2[10]),
    .in_7(in_3[9]), .in_8(in_3[10]), .in_9(in_3[11]), .out_10(out_4[9]));
  get_new_state_for_one_element get_new_state_for_one_element_11 (
    .in_1(in_1[10]), .in_2(in_1[11]), .in_3(in_1[12]), .in_4(in_2[10]), .in_5(in_2[12]), .current(in_2[11]),
    .in_7(in_3[10]), .in_8(in_3[11]), .in_9(in_3[12]), .out_10(out_4[10]));
  get_new_state_for_one_element get_new_state_for_one_element_12 (
    .in_1(in_1[11]), .in_2(in_1[12]), .in_3(in_1[13]), .in_4(in_2[11]), .in_5(in_2[13]), .current(in_2[12]),
    .in_7(in_3[11]), .in_8(in_3[12]), .in_9(in_3[13]), .out_10(out_4[11]));
  get_new_state_for_one_element get_new_state_for_one_element_13 (
    .in_1(in_1[12]), .in_2(in_1[13]), .in_3(in_1[14]), .in_4(in_2[12]), .in_5(in_2[14]), .current(in_2[13]),
    .in_7(in_3[12]), .in_8(in_3[13]), .in_9(in_3[14]), .out_10(out_4[12]));
  get_new_state_for_one_element get_new_state_for_one_element_14 (
    .in_1(in_1[13]), .in_2(in_1[14]), .in_3(in_1[15]), .in_4(in_2[13]), .in_5(in_2[15]), .current(in_2[14]),
    .in_7(in_3[13]), .in_8(in_3[14]), .in_9(in_3[15]), .out_10(out_4[13]));
  get_new_state_for_one_element get_new_state_for_one_element_15 (
    .in_1(in_1[14]), .in_2(in_1[15]), .in_3(in_1[16]), .in_4(in_2[14]), .in_5(in_2[16]), .current(in_2[15]),
    .in_7(in_3[14]), .in_8(in_3[15]), .in_9(in_3[16]), .out_10(out_4[14]));
  get_new_state_for_one_element get_new_state_for_one_element_16 (
    .in_1(in_1[15]), .in_2(in_1[16]), .in_3(in_1[17]), .in_4(in_2[15]), .in_5(in_2[17]), .current(in_2[16]),
    .in_7(in_3[15]), .in_8(in_3[16]), .in_9(in_3[17]), .out_10(out_4[15]));

  // Other names for the same wires on the sheet: _1[2:0] = in_2[2:0]; _1d[2:0] = in_3[2:0]; _1u[2:0] = in_1[2:0];
  //   _2[2:0] = in_2[3:1]; _2d[2:0] = in_3[3:1]; _2u[2:0] = in_1[3:1]; _3[2:0] = in_2[4:2]; _4[2:0] = in_2[5:3];
  //   _5[2:0] = in_2[6:4]; _3d[2:0] = in_3[4:2]; _4d[2:0] = in_3[5:3]; _5d[2:0] = in_3[6:4]; _3u[2:0] = in_1[4:2];
  //   _4u[2:0] = in_1[5:3]; _5u[2:0] = in_1[6:4]; _6[2:0] = in_2[7:5]; _6d[2:0] = in_3[7:5]; _6u[2:0] = in_1[7:5];
  //   _7[2:0] = in_2[8:6]; _7d[2:0] = in_3[8:6]; _7u[2:0] = in_1[8:6]; _8[2:0] = in_2[9:7]; _8d[2:0] = in_3[9:7];
  //   _8u[2:0] = in_1[9:7]; _9[2:0] = in_2[10:8]; _9d[2:0] = in_3[10:8]; _9u[2:0] = in_1[10:8]; _10[2:0] = in_2[11:9];
  //   _10d[2:0] = in_3[11:9]; _10u[2:0] = in_1[11:9]; _11[2:0] = in_2[12:10]; _12[2:0] = in_2[13:11];
  //   _13[2:0] = in_2[14:12]; _11d[2:0] = in_3[12:10]; _12d[2:0] = in_3[13:11]; _13d[2:0] = in_3[14:12];
  //   _11u[2:0] = in_1[12:10]; _12u[2:0] = in_1[13:11]; _13u[2:0] = in_1[14:12]; _14[2:0] = in_2[15:13];
  //   _14d[2:0] = in_3[15:13]; _14u[2:0] = in_1[15:13]; _15[2:0] = in_2[16:14]; _15d[2:0] = in_3[16:14];
  //   _15u[2:0] = in_1[16:14]; _16[2:0] = in_2[17:15]; _16d[2:0] = in_3[17:15]; _16u[2:0] = in_1[17:15]
endmodule

module get_new_state_for_one_element (
  input  in_1,
  input  in_2,
  input  in_3,
  input  in_4,
  input  in_5,
  input  current,
  input  in_7,
  input  in_8,
  input  in_9,
  output out_10
);

  wire comparator_1_eq, comparator_1_gt, comparator_2_eq, comparator_2_gt;
  wire [1:0] adder_1_out, adder_2_out, adder_3_out, adder_4_out, adder_5_out, adder_6_out;
  wire [2:0] adder_7_out;
  wire [2:2] adder_5_cout, adder_6_cout;
  wire [3:3] adder_7_cout;

  Adder #(.width(1)) adder_1 (.a(in_1), .b(in_2), .out(adder_1_out[0]), .cout(adder_1_out[1]));  // open: cin
  Adder #(.width(1)) adder_2 (.a(in_3), .b(in_4), .out(adder_2_out[0]), .cout(adder_2_out[1]));  // open: cin
  Adder #(.width(1)) adder_3 (.a(in_5), .b(in_7), .out(adder_3_out[0]), .cout(adder_3_out[1]));  // open: cin
  Adder #(.width(1)) adder_4 (.a(in_8), .b(in_9), .out(adder_4_out[0]), .cout(adder_4_out[1]));  // open: cin
  Adder #(.width(2)) adder_5 (
    .a(adder_1_out), .b(adder_2_out), .out(adder_5_out), .cout(adder_5_cout[2]));  // open: cin
  Adder #(.width(2)) adder_6 (
    .a(adder_3_out), .b(adder_4_out), .out(adder_6_out), .cout(adder_6_cout[2]));  // open: cin
  Adder #(.width(3)) adder_7 (
    .a({adder_5_cout[2], adder_5_out}), .b({adder_6_cout[2], adder_6_out}), .out(adder_7_out),
    .cout(adder_7_cout[3]));  // open: cin
  Comparator #(.width(4), .mode("unsigned")) comparator_1 (
    .a({adder_7_cout[3], adder_7_out}), .b(4'b0011), .gt(comparator_1_gt), .eq(comparator_1_eq));  // open: lt
  Comparator #(.width(4), .mode("unsigned")) comparator_2 (
    .a(4'b0010), .b({adder_7_cout[3], adder_7_out}), .gt(comparator_2_gt), .eq(comparator_2_eq));  // open: lt
  assign out_10 = comparator_1_gt ? 1'b0 : 1'bz;  // Controlled_Buffer controlled_buffer_1
  assign out_10 = comparator_1_eq ? 1'b1 : 1'bz;  // Controlled_Buffer controlled_buffer_2
  assign out_10 = comparator_2_gt ? 1'b0 : 1'bz;  // Controlled_Buffer controlled_buffer_3
  assign out_10 = comparator_2_eq ? current : 1'bz;  // Controlled_Buffer controlled_buffer_4
endmodule

module speed_changer (
  input  in_1,
  input  in_2,
  input  in_3,
  output out_4
);

  wire clock_1_out, clock_2_out, clock_3_out, clock_4_out;
  wire [1:0] a, adder_1_out, adder_2_out, adder_3_out, b, c;

  Transistor #(.width(2)) transistor_1 (.in(2'b01), .out(a), .gate(in_1));
  Transistor #(.width(2)) transistor_2 (.in(2'b01), .out(b), .gate(in_2));
  Transistor #(.width(2)) transistor_3 (.in(2'b01), .out(c), .gate(in_3));
  Transistor #(.\type ("n"), .width(2)) transistor_4 (.in(2'b00), .out(a), .gate(in_1));
  Transistor #(.\type ("n"), .width(2)) transistor_5 (.in(2'b00), .out(b), .gate(in_2));
  Transistor #(.\type ("n"), .width(2)) transistor_6 (.in(2'b00), .out(c), .gate(in_3));
  Adder #(.width(2)) adder_1 (.a(2'b00), .b(a), .out(adder_1_out));  // open: cin, cout
  Adder #(.width(2)) adder_2 (.a(adder_1_out), .b(b), .out(adder_2_out));  // open: cin, cout
  Clock #(.highDuration(5), .lowDuration(5)) clock_1 (.out(clock_1_out));
  Adder #(.width(2)) adder_3 (.a(adder_2_out), .b(c), .out(adder_3_out));  // open: cin, cout
  Clock #(.highDuration(10), .lowDuration(10)) clock_2 (.out(clock_2_out));
  Clock #(.highDuration(30), .lowDuration(30)) clock_3 (.out(clock_3_out));
  Clock #(.highDuration(40), .lowDuration(40)) clock_4 (.out(clock_4_out));
  Multiplexer #(.select(2), .enable("false")) multiplexer_1 (
    .in0(clock_1_out), .in1(clock_2_out), .in2(clock_3_out), .in3(clock_4_out), .out(out_4), .sel(adder_3_out));

  // Notes on the sheet:
  //   Колво включенных пинов
  //   3
  //   2
  //   1
  //   0
endmodule
