// Logisim project GameOfLifeHardware.circ as structural Verilog
module \input  (
  input  in_1,
  input  in_2,
  input  in_3,
  input  in_4,
  input  in_5,
  input  in_6,
  input  in_7,
  input  in_8,
  output [7:0] out_9,
  output out_10
);

  or or_1 (out_10, in_8, in_7, in_6, in_5, in_4, in_3, in_2, in_1);

  assign out_9 = {in_1, in_2, in_3, in_4, in_5, in_6, in_7, in_8};
endmodule

module get_new_state_for_all_elements_of_Matrix (
  input  [15:0] in_1,
  input  [15:0] in_2,
  input  [15:0] in_3,
  input  [15:0] in_4,
  input  [15:0] in_5,
  input  [15:0] in_6,
  input  [15:0] in_7,
  input  [15:0] in_8,
  input  [15:0] in_9,
  input  [15:0] in_10,
  input  [15:0] in_11,
  input  [15:0] in_12,
  input  [15:0] in_13,
  input  [15:0] in_14,
  input  [15:0] in_15,
  input  [15:0] in_16,
  output [15:0] out_17,
  output [15:0] out_18,
  output [15:0] out_19,
  output [15:0] out_20,
  output [15:0] out_21,
  output [15:0] out_22,
  output [15:0] out_23,
  output [15:0] out_24,
  output [15:0] out_25,
  output [15:0] out_26,
  output [15:0] out_27,
  output [15:0] out_28,
  output [15:0] out_29,
  output [15:0] out_30,
  output [15:0] out_31,
  output [15:0] out_32
);

  wire [17:0] convert_16_to_18_1_out_2, convert_16_to_18_2_out_2, convert_16_to_18_3_out_2,
       convert_16_to_18_4_out_2, convert_16_to_18_5_out_2, convert_16_to_18_6_out_2,
       convert_16_to_18_7_out_2, convert_16_to_18_8_out_2, convert_16_to_18_9_out_2,
       convert_16_to_18_10_out_2, convert_16_to_18_11_out_2, convert_16_to_18_12_out_2,
       convert_16_to_18_13_out_2, convert_16_to_18_14_out_2, convert_16_to_18_15_out_2,
       convert_16_to_18_16_out_2;

  convert_16_to_18 convert_16_to_18_1 (.in_1(in_1), .out_2(convert_16_to_18_1_out_2));
  convert_16_to_18 convert_16_to_18_2 (.in_1(in_2), .out_2(convert_16_to_18_2_out_2));
  convert_16_to_18 convert_16_to_18_3 (.in_1(in_3), .out_2(convert_16_to_18_3_out_2));
  convert_16_to_18 convert_16_to_18_4 (.in_1(in_4), .out_2(convert_16_to_18_4_out_2));
  convert_16_to_18 convert_16_to_18_5 (.in_1(in_5), .out_2(convert_16_to_18_5_out_2));
  convert_16_to_18 convert_16_to_18_6 (.in_1(in_6), .out_2(convert_16_to_18_6_out_2));
  convert_16_to_18 convert_16_to_18_7 (.in_1(in_7), .out_2(convert_16_to_18_7_out_2));
  convert_16_to_18 convert_16_to_18_8 (.in_1(in_8), .out_2(convert_16_to_18_8_out_2));
  convert_16_to_18 convert_16_to_18_9 (.in_1(in_9), .out_2(convert_16_to_18_9_out_2));
  convert_16_to_18 convert_16_to_18_10 (.in_1(in_10), .out_2(convert_16_to_18_10_out_2));
  convert_16_to_18 convert_16_to_18_11 (.in_1(in_11), .out_2(convert_16_to_18_11_out_2));
  convert_16_to_18 convert_16_to_18_12 (.in_1(in_12), .out_2(convert_16_to_18_12_out_2));
  convert_16_to_18 convert_16_to_18_13 (.in_1(in_13), .out_2(convert_16_to_18_13_out_2));
  convert_16_to_18 convert_16_to_18_14 (.in_1(in_14), .out_2(convert_16_to_18_14_out_2));
  convert_16_to_18 convert_16_to_18_15 (.in_1(in_15), .out_2(convert_16_to_18_15_out_2));
  convert_16_to_18 convert_16_to_18_16 (.in_1(in_16), .out_2(convert_16_to_18_16_out_2));
  get_new_state_for_one_string_of_Matrix get_new_state_for_one_string_of_matrix_1 (
    .in_1(convert_16_to_18_16_out_2), .in_2(convert_16_to_18_1_out_2), .in_3(convert_16_to_18_2_out_2),
    .out_4(out_17));
  get_new_state_for_one_string_of_Matrix get_new_state_for_one_string_of_matrix_2 (
    .in_1(convert_16_to_18_1_out_2), .in_2(convert_16_to_18_2_out_2), .in_3(convert_16_to_18_3_out_2),
    .out_4(out_18));
  get_new_state_for_one_string_of_Matrix get_new_state_for_one_string_of_matrix_3 (
    .in_1(convert_16_to_18_2_out_2), .in_2(convert_16_to_18_3_out_2), .in_3(convert_16_to_18_4_out_2),
    .out_4(out_19));
  get_new_state_for_one_string_of_Matrix get_new_state_for_one_string_of_matrix_4 (
    .in_1(convert_16_to_18_3_out_2), .in_2(convert_16_to_18_4_out_2), .in_3(convert_16_to_18_5_out_2),
    .out_4(out_20));
  get_new_state_for_one_string_of_Matrix get_new_state_for_one_string_of_matrix_5 (
    .in_1(convert_16_to_18_4_out_2), .in_2(convert_16_to_18_5_out_2), .in_3(convert_16_to_18_6_out_2),
    .out_4(out_21));
  get_new_state_for_one_string_of_Matrix get_new_state_for_one_string_of_matrix_6 (
    .in_1(convert_16_to_18_5_out_2), .in_2(convert_16_to_18_6_out_2), .in_3(convert_16_to_18_7_out_2),
    .out_4(out_22));
  get_new_state_for_one_string_of_Matrix get_new_state_for_one_string_of_matrix_7 (
    .in_1(convert_16_to_18_6_out_2), .in_2(convert_16_to_18_7_out_2), .in_3(convert_16_to_18_8_out_2),
    .out_4(out_23));
  get_new_state_for_one_string_of_Matrix get_new_state_for_one_string_of_matrix_8 (
    .in_1(convert_16_to_18_7_out_2), .in_2(convert_16_to_18_8_out_2), .in_3(convert_16_to_18_9_out_2),
    .out_4(out_24));
  get_new_state_for_one_string_of_Matrix get_new_state_for_one_string_of_matrix_9 (
    .in_1(convert_16_to_18_8_out_2), .in_2(convert_16_to_18_9_out_2), .in_3(convert_16_to_18_10_out_2),
    .out_4(out_25));
  get_new_state_for_one_string_of_Matrix get_new_state_for_one_string_of_matrix_10 (
    .in_1(convert_16_to_18_9_out_2), .in_2(convert_16_to_18_10_out_2), .in_3(convert_16_to_18_11_out_2),
    .out_4(out_26));
  get_new_state_for_one_string_of_Matrix get_new_state_for_one_string_of_matrix_11 (
    .in_1(convert_16_to_18_10_out_2), .in_2(convert_16_to_18_11_out_2), .in_3(convert_16_to_18_12_out_2),
    .out_4(out_27));
  get_new_state_for_one_string_of_Matrix get_new_state_for_one_string_of_matrix_12 (
    .in_1(convert_16_to_18_11_out_2), .in_2(convert_16_to_18_12_out_2), .in_3(convert_16_to_18_13_out_2),
    .out_4(out_28));
  get_new_state_for_one_string_of_Matrix get_new_state_for_one_string_of_matrix_13 (
    .in_1(convert_16_to_18_12_out_2), .in_2(convert_16_to_18_13_out_2), .in_3(convert_16_to_18_14_out_2),
    .out_4(out_29));
  get_new_state_for_one_string_of_Matrix get_new_state_for_one_string_of_matrix_14 (
    .in_1(convert_16_to_18_13_out_2), .in_2(convert_16_to_18_14_out_2), .in_3(convert_16_to_18_15_out_2),
    .out_4(out_30));
  get_new_state_for_one_string_of_Matrix get_new_state_for_one_string_of_matrix_15 (
    .in_1(convert_16_to_18_14_out_2), .in_2(convert_16_to_18_15_out_2), .in_3(convert_16_to_18_16_out_2),
    .out_4(out_31));
  get_new_state_for_one_string_of_Matrix get_new_state_for_one_string_of_matrix_16 (
    .in_1(convert_16_to_18_15_out_2), .in_2(convert_16_to_18_16_out_2), .in_3(convert_16_to_18_1_out_2),
    .out_4(out_32));
endmodule

module convert_16_to_18 (
  input  [15:0] in_1,
  output [17:0] out_2
);


  assign out_2 = {in_1[0], in_1, in_1[15]};
endmodule

module get_new_state_for_one_string_of_Matrix (
  input  [17:0] in_1,
  input  [17:0] in_2,
  input  [17:0] in_3,
  output [15:0] out_4
);

  get_new_state_for_one_element get_new_state_for_one_element_1 (
    .in_1(in_1[0]), .in_2(in_1[1]), .in_3(in_1[2]), .in_4(in_2[0]), .current(in_2[1]), .in_6(in_2[2]),
    .in_7(in_3[0]), .in_8(in_3[1]), .in_9(in_3[2]), .out_10(out_4[0]));
  get_new_state_for_one_element get_new_state_for_one_element_2 (
    .in_1(in_1[1]), .in_2(in_1[2]), .in_3(in_1[3]), .in_4(in_2[1]), .current(in_2[2]), .in_6(in_2[3]),
    .in_7(in_3[1]), .in_8(in_3[2]), .in_9(in_3[3]), .out_10(out_4[1]));
  get_new_state_for_one_element get_new_state_for_one_element_3 (
    .in_1(in_1[2]), .in_2(in_1[3]), .in_3(in_1[4]), .in_4(in_2[2]), .current(in_2[3]), .in_6(in_2[4]),
    .in_7(in_3[2]), .in_8(in_3[3]), .in_9(in_3[4]), .out_10(out_4[2]));
  get_new_state_for_one_element get_new_state_for_one_element_4 (
    .in_1(in_1[3]), .in_2(in_1[4]), .in_3(in_1[5]), .in_4(in_2[3]), .current(in_2[4]), .in_6(in_2[5]),
    .in_7(in_3[3]), .in_8(in_3[4]), .in_9(in_3[5]), .out_10(out_4[3]));
  get_new_state_for_one_element get_new_state_for_one_element_5 (
    .in_1(in_1[4]), .in_2(in_1[5]), .in_3(in_1[6]), .in_4(in_2[4]), .current(in_2[5]), .in_6(in_2[6]),
    .in_7(in_3[4]), .in_8(in_3[5]), .in_9(in_3[6]), .out_10(out_4[4]));
  get_new_state_for_one_element get_new_state_for_one_element_6 (
    .in_1(in_1[5]), .in_2(in_1[6]), .in_3(in_1[7]), .in_4(in_2[5]), .current(in_2[6]), .in_6(in_2[7]),
    .in_7(in_3[5]), .in_8(in_3[6]), .in_9(in_3[7]), .out_10(out_4[5]));
  get_new_state_for_one_element get_new_state_for_one_element_7 (
    .in_1(in_1[6]), .in_2(in_1[7]), .in_3(in_1[8]), .in_4(in_2[6]), .current(in_2[7]), .in_6(in_2[8]),
    .in_7(in_3[6]), .in_8(in_3[7]), .in_9(in_3[8]), .out_10(out_4[6]));
  get_new_state_for_one_element get_new_state_for_one_element_8 (
    .in_1(in_1[7]), .in_2(in_1[8]), .in_3(in_1[9]), .in_4(in_2[7]), .current(in_2[8]), .in_6(in_2[9]),
    .in_7(in_3[7]), .in_8(in_3[8]), .in_9(in_3[9]), .out_10(out_4[7]));
  get_new_state_for_one_element get_new_state_for_one_element_9 (
    .in_1(in_1[8]), .in_2(in_1[9]), .in_3(in_1[10]), .in_4(in_2[8]), .current(in_2[9]), .in_6(in_2[10]),
    .in_7(in_3[8]), .in_8(in_3[9]), .in_9(in_3[10]), .out_10(out_4[8]));
  get_new_state_for_one_element get_new_state_for_one_element_10 (
    .in_1(in_1[9]), .in_2(in_1[10]), .in_3(in_1[11]), .in_4(in_2[9]), .current(in_2[10]), .in_6(in_2[11]),
    .in_7(in_3[9]), .in_8(in_3[10]), .in_9(in_3[11]), .out_10(out_4[9]));
  get_new_state_for_one_element get_new_state_for_one_element_11 (
    .in_1(in_1[10]), .in_2(in_1[11]), .in_3(in_1[12]), .in_4(in_2[10]), .current(in_2[11]), .in_6(in_2[12]),
    .in_7(in_3[10]), .in_8(in_3[11]), .in_9(in_3[12]), .out_10(out_4[10]));
  get_new_state_for_one_element get_new_state_for_one_element_12 (
    .in_1(in_1[11]), .in_2(in_1[12]), .in_3(in_1[13]), .in_4(in_2[11]), .current(in_2[12]), .in_6(in_2[13]),
    .in_7(in_3[11]), .in_8(in_3[12]), .in_9(in_3[13]), .out_10(out_4[11]));
  get_new_state_for_one_element get_new_state_for_one_element_13 (
    .in_1(in_1[12]), .in_2(in_1[13]), .in_3(in_1[14]), .in_4(in_2[12]), .current(in_2[13]), .in_6(in_2[14]),
    .in_7(in_3[12]), .in_8(in_3[13]), .in_9(in_3[14]), .out_10(out_4[12]));
  get_new_state_for_one_element get_new_state_for_one_element_14 (
    .in_1(in_1[13]), .in_2(in_1[14]), .in_3(in_1[15]), .in_4(in_2[13]), .current(in_2[14]), .in_6(in_2[15]),
    .in_7(in_3[13]), .in_8(in_3[14]), .in_9(in_3[15]), .out_10(out_4[13]));
  get_new_state_for_one_element get_new_state_for_one_element_15 (
    .in_1(in_1[14]), .in_2(in_1[15]), .in_3(in_1[16]), .in_4(in_2[14]), .current(in_2[15]), .in_6(in_2[16]),
    .in_7(in_3[14]), .in_8(in_3[15]), .in_9(in_3[16]), .out_10(out_4[14]));
  get_new_state_for_one_element get_new_state_for_one_element_16 (
    .in_1(in_1[15]), .in_2(in_1[16]), .in_3(in_1[17]), .in_4(in_2[15]), .current(in_2[16]), .in_6(in_2[17]),
    .in_7(in_3[15]), .in_8(in_3[16]), .in_9(in_3[17]), .out_10(out_4[15]));

  // Other names for the same wires on the sheet: _1[2:0] = in_2[2:0]; _1d[2:0] = in_3[2:0]; _1u[2:0] = in_1[2:0];
  //   _2[2:0] = in_2[3:1]; _2d[2:0] = in_3[3:1]; _2u[2:0] = in_1[3:1]; _3[2:0] = in_2[4:2]; _4[2:0] = in_2[5:3];
  //   _5[2:0] = in_2[6:4]; _3d[2:0] = in_3[4:2]; _4d[2:0] = in_3[5:3]; _5d[2:0] = in_3[6:4]; _3u[2:0] = in_1[4:2];
  //   _4u[2:0] = in_1[5:3]; _5u[2:0] = in_1[6:4]; _6[2:0] = in_2[7:5]; _6d[2:0] = in_3[7:5]; _6u[2:0] = in_1[7:5];
  //   _7[2:0] = in_2[8:6]; _7d[2:0] = in_3[8:6]; _7u[2:0] = in_1[8:6]; _8[2:0] = in_2[9:7]; _8d[2:0] = in_3[9:7];
  //   _8u[2:0] = in_1[9:7]; _9[2:0] = in_2[10:8]; _9d[2:0] = in_3[10:8]; _9u[2:0] = in_1[10:8]; _10[2:0] = in_2[11:9];
  //   _10d[2:0] = in_3[11:9]; _10u[2:0] = in_1[11:9]; _11[2:0] = in_2[12:10]; _12[2:0] = in_2[13:11];
  //   _13[2:0] = in_2[14:12]; _11d[2:0] = in_3[12:10]; _12d[2:0] = in_3[13:11]; _13d[2:0] = in_3[14:12];
  //   _11u[2:0] = in_1[12:10]; _12u[2:0] = in_1[13:11]; _13u[2:0] = in_1[14:12]; _14[2:0] = in_2[15:13];
  //   _14d[2:0] = in_3[15:13]; _14u[2:0] = in_1[15:13]; _15[2:0] = in_2[16:14]; _15d[2:0] = in_3[16:14];
  //   _15u[2:0] = in_1[16:14]; _16[2:0] = in_2[17:15]; _16d[2:0] = in_3[17:15]; _16u[2:0] = in_1[17:15]
endmodule

module get_new_state_for_one_element (
  input  in_1,
  input  in_2,
  input  in_3,
  input  in_4,
  input  current,
  input  in_6,
  input  in_7,
  input  in_8,
  input  in_9,
  output out_10
);

  wire clock_1_out, comparator_1_eq, comparator_1_gt, comparator_2_eq, comparator_2_gt;
  wire [7:0] adder_1_out, adder_2_out, adder_3_out, adder_4_out, adder_5_out, adder_6_out, adder_7_out,
       counter_1_q, counter_2_q, counter_3_q, counter_4_q, counter_5_q, counter_6_q, counter_7_q, counter_8_q;

  Clock clock_1 (.out(clock_1_out));
  Counter counter_1 (.Q(counter_1_q), .clk(in_1), .clr(clock_1_out));  // open: load, D, count, carry
  Counter counter_2 (.Q(counter_2_q), .clk(in_2), .clr(clock_1_out));  // open: load, D, count, carry
  Counter counter_3 (.Q(counter_3_q), .clk(in_3), .clr(clock_1_out));  // open: load, D, count, carry
  Counter counter_4 (.Q(counter_4_q), .clk(in_4), .clr(clock_1_out));  // open: load, D, count, carry
  Counter counter_5 (.Q(counter_5_q), .clk(in_6), .clr(clock_1_out));  // open: load, D, count, carry
  Counter counter_6 (.Q(counter_6_q), .clk(in_7), .clr(clock_1_out));  // open: load, D, count, carry
  Counter counter_7 (.Q(counter_7_q), .clk(in_8), .clr(clock_1_out));  // open: load, D, count, carry
  Counter counter_8 (.Q(counter_8_q), .clk(in_9), .clr(clock_1_out));  // open: load, D, count, carry
  Adder adder_1 (.a(counter_1_q), .b(counter_2_q), .out(adder_1_out));  // open: cin, cout
  Adder adder_2 (.a(counter_3_q), .b(counter_4_q), .out(adder_2_out));  // open: cin, cout
  Adder adder_3 (.a(counter_5_q), .b(counter_6_q), .out(adder_3_out));  // open: cin, cout
  Adder adder_4 (.a(counter_7_q), .b(counter_8_q), .out(adder_4_out));  // open: cin, cout
  Adder adder_5 (.a(adder_1_out), .b(adder_2_out), .out(adder_5_out));  // open: cin, cout
  Adder adder_6 (.a(adder_3_out), .b(adder_4_out), .out(adder_6_out));  // open: cin, cout
  Adder adder_7 (.a(adder_5_out), .b(adder_6_out), .out(adder_7_out));  // open: cin, cout
  Comparator comparator_1 (.a(adder_7_out), .b(8'h3), .gt(comparator_1_gt), .eq(comparator_1_eq));  // open: lt
  Comparator comparator_2 (.a(8'h2), .b(adder_7_out), .gt(comparator_2_gt), .eq(comparator_2_eq));  // open: lt
  assign out_10 = comparator_1_gt ? 1'b0 : 1'bz;  // Controlled_Buffer controlled_buffer_1
  assign out_10 = comparator_1_eq ? 1'b1 : 1'bz;  // Controlled_Buffer controlled_buffer_2
  assign out_10 = comparator_2_gt ? 1'b0 : 1'bz;  // Controlled_Buffer controlled_buffer_3
  assign out_10 = comparator_2_eq ? current : 1'bz;  // Controlled_Buffer controlled_buffer_4
endmodule
