// Logisim project CdM-8-mark5-reduced.circ as structural Verilog: 11 circuits, main circuit CdM_8_mark5
module CdM_8_mark5 (
  input  [7:0] data_in,
  input  clock,
  output [7:0] r0,
  output [7:0] r2,
  output [7:0] PC,
  output [7:0] SP,
  output [3:0] PS,
  output [7:0] r1,
  output [7:0] r3,
  output [7:0] addr,
  output mem_cycle,
  output mem_read,
  output data_inst,
  output [7:0] data_out
);

  wire addsp, ALU2b1, alu_1, alu_2, and_1_out, and_2_out, and_3_out, and_4_out, and_5_out, and_6_out,
       and_7_out, and_8_out, and_12_out, and_13_out, and_14_out, and_15_out, asrtD, asrtS, br_nop, br_taken,
       branch_logic_1_go, CL, cmp, crc, CUT, decoder_1_out0, decoder_1_out1, decoder_1_out2, decoder_1_out3,
       decoder_2_out0, decoder_2_out1, decoder_2_out2, decoder_2_out3, decoder_3_out3, decoder_7_out0,
       decoder_8_out0, decoder_8_out1, decoder_8_out2, decoder_8_out3, err, extB, fetch, halt, inc3_1_c, jsr,
       latch, latchPC, latchPS, latchRX, latchSP, ldc, ldi, ldsa, m_ld, m_st, nor_1_out, not_1_out, or_1_out,
       or_2_out, or_3_out, or_4_out, or_6_out, or_7_out, or_8_out, PC2b0, PC2b1, PCinc, po,
       priority_encoder_1_gs, pu, register_7_q, register_13_q, RR2b1, rti, rts, RX2PC, setsp, SP2b0, SP2b1,
       SPoff2b1, SPoffset, SPstep, stop, up_down, \wait ;
  wire [1:0] extA, Rd, Rs;
  wire [2:0] fun, inc3_1_out, multiplexer_1_out, phase;
  wire [3:0] alu_1_n;
  wire [4:0] extC, priority_encoder_1_out;
  wire [7:0] adder_1_out, adder_2_out, alu_1_s, bus0, inc_1_out, incdec_1_out, multiplexer_4_out,
       multiplexer_5_out, register_9_q, register_11_q;
  wire [7:2] register_6_q;

  Decoder #(.select(2), .disabled(0), .enable("false")) decoder_1 (
    .out0(decoder_1_out0), .out1(decoder_1_out1), .out2(decoder_1_out2), .out3(decoder_1_out3), .sel(Rd));
  assign bus0 = decoder_2_out0 ? r0 : 8'bz;  // Controlled_Buffer controlled_buffer_1
  Register #(.trigger("falling")) register_1 (.D(data_out), .en(and_1_out), .Q(r0), .clk(CL));  // open: clr
  and and_1 (and_1_out, decoder_1_out0, latch);
  and and_2 (and_2_out, decoder_1_out0, asrtD);
  assign data_out = and_2_out ? r0 : 8'bz;  // Controlled_Buffer controlled_buffer_2
  assign bus0 = decoder_2_out1 ? r1 : 8'bz;  // Controlled_Buffer controlled_buffer_3
  Register #(.trigger("falling")) register_2 (.D(data_out), .en(and_4_out), .Q(r1), .clk(CL));  // open: clr
  and and_3 (and_3_out, decoder_1_out2, latch);
  and and_4 (and_4_out, decoder_1_out1, latch);
  and and_5 (and_5_out, decoder_1_out1, asrtD);
  assign data_out = and_5_out ? r1 : 8'bz;  // Controlled_Buffer controlled_buffer_4
  Register #(.width(3), .trigger("falling")) register_3 (
    .D(multiplexer_1_out), .en(1'b1), .Q(phase), .clk(CL));  // open: clr
  Multiplexer #(.width(3), .enable("false")) multiplexer_1 (
    .in0(inc3_1_out), .in1(3'b000), .out(multiplexer_1_out), .sel(CUT));
  assign bus0 = decoder_2_out2 ? r2 : 8'bz;  // Controlled_Buffer controlled_buffer_5
  Register #(.trigger("falling")) register_4 (.D(data_out), .en(and_3_out), .Q(r2), .clk(CL));  // open: clr
  and and_6 (and_6_out, decoder_1_out3, latch);
  and and_7 (and_7_out, decoder_1_out2, asrtD);
  and and_8 (and_8_out, decoder_1_out3, asrtD);
  assign data_out = and_7_out ? r2 : 8'bz;  // Controlled_Buffer controlled_buffer_6
  nor nor_1 (nor_1_out, phase[0], phase[1], phase[2]);
  inc3 inc3_1 (.in(phase), .out(inc3_1_out), .C(inc3_1_c));
  or or_1 (or_1_out, inc3_1_c, CUT);
  assign bus0 = decoder_2_out3 ? r3 : 8'bz;  // Controlled_Buffer controlled_buffer_7
  Register #(.trigger("falling")) register_5 (.D(data_out), .en(and_6_out), .Q(r3), .clk(CL));  // open: clr
  assign data_out = and_8_out ? r3 : 8'bz;  // Controlled_Buffer controlled_buffer_8
  and and_9 (fetch, nor_1_out, not_1_out);
  Decoder #(.select(2), .disabled(0)) decoder_2 (
    .out0(decoder_2_out0), .out1(decoder_2_out1), .out2(decoder_2_out2), .out3(decoder_2_out3), .sel(Rs),
    .en(asrtS));
  Register #(.trigger("falling")) register_6 (.D(data_out), .en(fetch), .Q({register_6_q, Rd}), .clk(CL));  // open: clr
  Register #(.width(1), .trigger("falling")) register_7 (
    .D(not_1_out), .en(or_1_out), .Q(register_7_q), .clk(CL));  // open: clr
  not not_1 (not_1_out, register_7_q);
  Multiplexer #(.width(2), .disabled(0), .enable("false")) multiplexer_2 (
    .in0(register_6_q[3:2]), .in1(Rd), .out(Rs), .sel(or_3_out));
  Multiplexer #(.width(3), .enable("false")) multiplexer_3 (
    .in0(register_6_q[6:4]), .in1(register_6_q[4:2]), .out(fun), .sel(alu_1));
  Register #(.trigger("falling")) register_8 (.D(multiplexer_4_out), .en(or_2_out), .Q(PC), .clk(CL));  // open: clr
  or or_2 (or_2_out, latchPC, PCinc, RX2PC);
  or or_3 (or_3_out, alu_1, ldsa);
  and and_10 (cmp, ~register_6_q[7], register_6_q[6], register_6_q[5], register_6_q[4]);  // AND_Gate
  and and_11 (alu_1, register_6_q[7], ~register_6_q[6], ~register_6_q[5]);  // AND_Gate
  not not_2 (alu_2, register_6_q[7]);
  assign bus0 = PC2b0 ? PC : 8'bz;  // Controlled_Buffer controlled_buffer_9
  inc inc_1 (.in(PC), .out(inc_1_out));
  Register #(.trigger("falling")) register_9 (.D(data_out), .en(latchRX), .Q(register_9_q), .clk(CL));  // open: clr
  assign data_out = PC2b1 ? PC : 8'bz;  // Controlled_Buffer controlled_buffer_10
  Decoder #(.select(2), .disabled(0)) decoder_3 (
    .out0(pu), .out1(po), .out2(ldsa), .out3(decoder_3_out3), .sel(register_6_q[3:2]), .en(and_12_out));
  and and_12 (and_12_out, register_6_q[7], register_6_q[6], ~register_6_q[5], ~register_6_q[4]);  // AND_Gate
  and and_13 (and_13_out, register_6_q[7], ~register_6_q[6], register_6_q[5]);  // AND_Gate
  Decoder #(.disabled(0)) decoder_4 (.out0(m_st), .out1(m_ld), .sel(register_6_q[4]), .en(and_13_out));
  Multiplexer #(.select(2), .width(8), .enable("false")) multiplexer_4 (
    .in0(data_out), .in1(inc_1_out), .in2(register_9_q), .out(multiplexer_4_out), .sel({RX2PC, PCinc}));  // open: in3
  Decoder #(.select(2), .disabled(0)) decoder_5 (
    .out0(addsp), .out1(setsp), .out2(extA[0]), .out3(extA[1]), .sel(Rd), .en(decoder_3_out3));
  and and_14 (and_14_out, register_6_q[5], register_6_q[6], register_6_q[7]);
  Decoder #(.disabled(0)) decoder_6 (.out0(br_nop), .out1(br_taken), .sel(branch_logic_1_go), .en(decoder_7_out0));
  and and_15 (and_15_out, register_6_q[7], register_6_q[6], ~register_6_q[5], register_6_q[4]);  // AND_Gate
  Decoder #(.disabled(0)) decoder_7 (.out0(decoder_7_out0), .out1(ldc), .sel(register_6_q[4]), .en(and_14_out));
  branch_logic branch_logic_1 (.cccc({register_6_q[3:2], Rd}), .CVZN(PS), .go(branch_logic_1_go));
  or or_4 (or_4_out, latchSP, SPstep, SPoffset);
  Decoder #(.select(4), .disabled(0)) decoder_8 (
    .out0(decoder_8_out0), .out1(decoder_8_out1), .out2(decoder_8_out2), .out3(decoder_8_out3), .out4(halt),
    .out5(\wait ), .out6(jsr), .out7(rts), .out8(extB), .out9(rti), .out10(crc), .out11(extC[0]),
    .out12(extC[1]), .out13(extC[2]), .out14(extC[3]), .out15(extC[4]), .sel({register_6_q[3:2], Rd}),
    .en(and_15_out));
  assign bus0 = SP2b0 ? SP : 8'bz;  // Controlled_Buffer controlled_buffer_11
  Register #(.trigger("falling")) register_10 (.D(multiplexer_5_out), .en(or_4_out), .Q(SP), .clk(CL));  // open: clr
  assign data_out = SP2b1 ? SP : 8'bz;  // Controlled_Buffer controlled_buffer_12
  or or_5 (ldi, decoder_8_out0, decoder_8_out1, decoder_8_out2, decoder_8_out3);
  Adder adder_1 (.a(bus0), .b(SP), .out(adder_1_out));  // open: cin, cout
  assign data_out = SPoff2b1 ? adder_1_out : 8'bz;  // Controlled_Buffer controlled_buffer_13
  incdec incdec_1 (.in(SP), .out(incdec_1_out), .up_down(up_down));
  Adder adder_2 (.a(SP), .b(data_out), .out(adder_2_out));  // open: cin, cout
  Multiplexer #(.select(2), .width(8), .enable("false")) multiplexer_5 (
    .in0(data_out), .in1(incdec_1_out), .in2(adder_2_out), .out(multiplexer_5_out), .sel({SPoffset, SPstep}));  // open: in3
  ALU u_alu_1 (
    .C_in(PS[3]), .N(alu_1_n[0]), .\function ({alu_1, fun}), .A(bus0), .B(data_out), .Z(alu_1_n[1]),
    .S(alu_1_s), .C(alu_1_n[3]), .V(alu_1_n[2]));
  assign data_out = ALU2b1 ? alu_1_s : 8'bz;  // Controlled_Buffer controlled_buffer_14
  Priority_Encoder #(.select(5), .disabled(0)) priority_encoder_1 (
    .in0(alu_2), .in1(cmp), .in2(alu_1), .in3(m_ld), .in4(m_st), .in5(ldc), .in6(ldi), .in7(setsp),
    .in8(addsp), .in9(pu), .in10(po), .in11(ldsa), .in12(br_nop), .in13(br_taken), .in14(jsr), .in15(rts),
    .in16(crc), .in17(halt), .in18(fetch), .in19(1'b0), .in20(1'b0), .in21(1'b0), .in22(1'b0), .in23(1'b0),
    .in24(1'b0), .in25(1'b0), .in26(1'b0), .in27(1'b0), .in28(1'b0), .in29(1'b0), .in30(1'b0), .in31(1'b0),
    .out(priority_encoder_1_out), .gs(priority_encoder_1_gs));  // open: en_out, en_in
  Register #(.trigger("falling")) register_11 (.D(alu_1_s), .en(1'b1), .Q(register_11_q), .clk(CL));  // open: clr
  assign data_out = RR2b1 ? register_11_q : 8'bz;  // Controlled_Buffer controlled_buffer_15
  Register #(.width(4), .trigger("falling")) register_12 (.D(alu_1_n), .en(latchPS), .Q(PS), .clk(CL));  // open: clr
  assign data_out = mem_read ? data_in : 8'bz;  // Controlled_Buffer controlled_buffer_16
  or or_6 (or_6_out, extC[0], extC[1], extC[2], extC[3], extC[4]);
  or or_7 (or_7_out, extA[0], extA[1], extB);
  and and_16 (CL, clock, ~register_13_q);  // AND_Gate
  Register #(.width(1), .trigger("falling")) register_13 (
    .D(or_8_out), .en(1'b1), .Q(register_13_q), .clk(CL));  // open: clr
  or or_8 (or_8_out, err, stop);
  // Probe on data_out
  // Probe on data_in
  LED ERROR (.in(err));
  or or_9 (err, or_6_out, or_7_out);
  ROM #(.addrWidth(6), .dataWidth(24)) rom_1 (
    .addr({phase[0], priority_encoder_1_out}),
    .data({CUT, up_down, stop, mem_read, mem_cycle, latchSP, latchRX, latchPS, latchPC, latch, data_inst, asrtS, asrtD, SPstep, SPoffset, SPoff2b1, SP2b1, SP2b0, RX2PC, RR2b1, PCinc, PC2b1, PC2b0, ALU2b1}),
    .sel(priority_encoder_1_gs));
  Multiplexer #(.width(8), .enable("false")) multiplexer_6 (.in0({8{1'b0}}), .in1(bus0), .out(addr), .sel(mem_cycle));

  // Other names for the same wires on the sheet: data = data_inst; mem = mem_cycle; mem_ld = mem_read;
  //   bus1[7:0] = data_out; CVZN[3:0] = PS; fun[3] = alu_1

  // Notes on the sheet:
  //   destination
  //   r0
  //   Seq
  //   r1
  //   r2
  //   r3
  //   source
  //   fetch toggle
  //   IR
  //   RX
  //   Coco de Mer 8 (CdM-8) Mark 5 (basic core)
  //   ALU
  //   RR
  //   unimplemented
  //   PS
  //   contents of rom_1 (hex, n*v repeats v):
  //   11800 811800 815001 987000 883800 985000 98400a 9c000a 9c020a 400 d86440 18400a 800008 988002 1a040a
  //   d8a440 1a2040 a00000 98000a 13*0 804010 8*0 882840 0 805100 0 0 88a064 0 88a064
endmodule

module inc (
  input  [7:0] in,
  output [7:0] out
);

  wire [7:0] and_1_out;

  // Probe on in
  assign and_1_out = in & {and_1_out[6:0], 1'b1};  // AND_Gate and_1, 8 bits wide
  assign out = {and_1_out[6:0], 1'b1} ^ in;  // XOR_Gate xor_1, 8 bits wide
  // Probe on out

  // Notes on the sheet:
  //   x
  //   x
  //   +1
endmodule

module incdec (
  input  [7:0] in,
  input  up_down,
  output [7:0] out
);

  wire [7:0] xnor_1_out, xor_1_out;
  wire [7:1] and_1_out, or_1_out;
  wire [7:7] and_1_out_2, or_1_out_2;

  // Probe on in
  assign {or_1_out_2[7], or_1_out} = in | {or_1_out, 1'b0};  // OR_Gate or_1, 8 bits wide
  assign xnor_1_out = ~({or_1_out, 1'b0} ^ in);  // XNOR_Gate xnor_1, 8 bits wide
  assign {and_1_out_2[7], and_1_out} = in & {and_1_out, 1'b1};  // AND_Gate and_1, 8 bits wide
  assign xor_1_out = {and_1_out, 1'b1} ^ in;  // XOR_Gate xor_1, 8 bits wide
  // Probe on xnor_1_out
  // Probe on xor_1_out
  Multiplexer #(.width(8), .enable("false")) multiplexer_1 (
    .in0(xnor_1_out), .in1(xor_1_out), .out(out), .sel(up_down));

  // Notes on the sheet:
  //   x
  //   x
  //   â€“1
  //   x
  //   +1
endmodule

module ALU (
  input  C_in,
  input  [3:0] \function ,
  input  [7:0] A,
  input  [7:0] B,
  output N,
  output Z,
  output [7:0] S,
  output C,
  output V
);

  wire adder_v_1_c_out, adder_v_1_v, adder_v_2_c_out, adder_v_2_v, and_1_out, and_2_out, and_4_out,
       and_5_out, multiplexer_6_out, or_1_out, xor_2_out;
  wire [7:0] adder_v_1_s, adder_v_2_s, and_3_out, multiplexer_1_out, multiplexer_2_out, multiplexer_5_out,
       not_1_out, or_2_out, or_3_out, xnor_1_out, xor_1_out;

  Pull_Resistor pull_resistor_1 (.node(A[0]));
  Pull_Resistor pull_resistor_2 (.node(A[1]));
  Pull_Resistor pull_resistor_3 (.node(A[2]));
  Pull_Resistor pull_resistor_4 (.node(A[3]));
  Pull_Resistor pull_resistor_5 (.node(A[4]));
  Pull_Resistor pull_resistor_6 (.node(A[5]));
  Pull_Resistor pull_resistor_7 (.node(A[6]));
  Pull_Resistor pull_resistor_8 (.node(A[7]));
  // Probe on A
  Pull_Resistor pull_resistor_9 (.node(B[0]));
  Pull_Resistor pull_resistor_10 (.node(B[1]));
  Pull_Resistor pull_resistor_11 (.node(B[2]));
  Pull_Resistor pull_resistor_12 (.node(B[3]));
  Pull_Resistor pull_resistor_13 (.node(B[4]));
  Pull_Resistor pull_resistor_14 (.node(B[5]));
  Pull_Resistor pull_resistor_15 (.node(B[6]));
  Pull_Resistor pull_resistor_16 (.node(B[7]));
  // Probe on B
  assign not_1_out = ~B;  // NOT_Gate not_1, 8 bits wide
  and and_1 (and_1_out, \function [1], ~\function [0], C_in);  // AND_Gate
  or or_1 (or_1_out, and_1_out, and_2_out);
  Multiplexer #(.select(2), .width(8), .enable("false")) multiplexer_1 (
    .in0({8{1'b0}}), .in1(B), .in2(B), .in3(not_1_out), .out(multiplexer_1_out), .sel(\function [1:0]));
  and and_2 (and_2_out, \function [1], \function [0]);
  adder_V adder_v_1 (
    .A(A), .B(multiplexer_1_out), .S(adder_v_1_s), .C_in(or_1_out), .C_out(adder_v_1_c_out), .V(adder_v_1_v));
  assign and_3_out = A & B;  // AND_Gate and_3, 8 bits wide
  assign or_2_out = A | B;  // OR_Gate or_2, 8 bits wide
  and and_4 (and_4_out, \function [0], \function [1], adder_v_1_v);
  Multiplexer #(.select(2), .width(8), .enable("false")) multiplexer_2 (
    .in0(and_3_out), .in1(or_2_out), .in2(xor_1_out), .in3(adder_v_1_s), .out(multiplexer_2_out),
    .sel(\function [1:0]));
  assign xor_1_out = A ^ B;  // XOR_Gate xor_1, 8 bits wide
  or or_3 (or_3_out[0], \function [0], \function [1]);
  and dec (or_3_out[7], ~\function [0], \function [1]);  // AND_Gate
  Multiplexer #(.select(2), .enable("false")) multiplexer_3 (
    .in0(adder_v_1_c_out), .in1(1'b0), .in2(adder_v_2_c_out), .in3(multiplexer_6_out), .out(C),
    .sel(\function [3:2]));
  Multiplexer #(.select(2), .enable("false")) multiplexer_4 (
    .in0(adder_v_1_v), .in1(and_4_out), .in2(adder_v_2_v), .in3(and_5_out), .out(V), .sel(\function [3:2]));
  assign xnor_1_out = ~({8{\function [1]}} ^ A);  // XNOR_Gate xnor_1, 8 bits wide
  adder_V adder_v_2 (
    .A({{7{or_3_out[7]}}, or_3_out[0]}), .B(xnor_1_out), .S(adder_v_2_s), .C_in(1'b0),
    .C_out(adder_v_2_c_out), .V(adder_v_2_v));
  Multiplexer #(.select(2), .width(8), .enable("false")) multiplexer_5 (
    .in0({C_in, A[7:1]}), .in1({A[6:0], 1'b0}), .in2({{2{A[7]}}, A[6:1]}), .in3({A[3:0], A[7:4]}),
    .out(multiplexer_5_out), .sel(\function [1:0]));
  Multiplexer #(.select(2), .enable("false")) multiplexer_6 (
    .in0(A[0]), .in1(A[7]), .in2(A[0]), .in3(1'b0), .out(multiplexer_6_out), .sel(\function [1:0]));
  // Probe on {N, S[6:0]}
  Multiplexer #(.select(2), .width(8), .enable("false")) multiplexer_7 (
    .in0(adder_v_1_s), .in1(multiplexer_2_out), .in2(adder_v_2_s), .in3(multiplexer_5_out),
    .out({N, S[6:0]}), .sel(\function [3:2]));
  xor xor_2 (xor_2_out, A[7], A[6]);
  nor nor_1 (Z, S[0], S[1], S[2], S[3], S[4], S[5], S[6], N);
  and and_5 (and_5_out, \function [0], ~\function [1], xor_2_out);  // AND_Gate

  assign S[7] = N;

  // Notes on the sheet:
  //   to avoid undriven input to arith. devices
  //   to avoid undriven input to arith. devices
  //   move
  //   add
  //   addc
  //   sub
  //   addc
  //   sub/cmp
  //   cmp
  //   and
  //   or
  //   xor
  //   cmp
  //   not/neg
  //   dec/inc/neg
  //   shr
  //   shla
  //   shra
  //   swan
endmodule

module adder_V (
  input  C_in,
  input  [7:0] A,
  input  [7:0] B,
  output [7:0] S,
  output C_out,
  output V
);

  wire [7:0] and_1_out, and_2_out, and_3_out;
  wire [7:1] or_1_out;

  // Probe on A
  // Probe on B
  assign S = A ^ {or_1_out, C_in} ^ B;  // XOR_Gate xor_1, 8 bits wide
  assign and_1_out = B & A;  // AND_Gate and_1, 8 bits wide
  assign and_2_out = B & {or_1_out, C_in};  // AND_Gate and_2, 8 bits wide
  assign and_3_out = A & {or_1_out, C_in};  // AND_Gate and_3, 8 bits wide
  assign {C_out, or_1_out} = and_1_out | and_2_out | and_3_out;  // OR_Gate or_1, 8 bits wide
  // Probe on S
  xor xor_2 (V, or_1_out[7], C_out);
endmodule

module branch_logic (
  input  [3:0] cccc,
  input  [3:0] CVZN,
  output go
);

  wire and_1_out, and_2_out, and_3_out, and_4_out, and_5_out, and_6_out, and_7_out, decoder_1_out0,
       decoder_1_out1, decoder_1_out2, decoder_1_out3, decoder_2_out0, decoder_2_out1, decoder_2_out2,
       decoder_2_out3, not_1_out, not_2_out, or_1_out, xnor_1_out;

  not not_1 (not_1_out, cccc[3]);
  Decoder #(.select(2), .disabled(0)) decoder_1 (
    .out0(decoder_1_out0), .out1(decoder_1_out1), .out2(decoder_1_out2), .out3(decoder_1_out3),
    .sel(cccc[2:1]), .en(not_1_out));
  and and_1 (and_1_out, decoder_1_out0, CVZN[1]);
  and and_2 (and_2_out, decoder_1_out1, CVZN[3]);
  and and_3 (and_3_out, decoder_1_out2, CVZN[0]);
  and and_4 (and_4_out, decoder_1_out3, CVZN[2]);
  not not_2 (not_2_out, CVZN[1]);
  xnor xnor_1 (xnor_1_out, CVZN[0], CVZN[2]);
  Decoder #(.select(2), .disabled(0)) decoder_2 (
    .out0(decoder_2_out0), .out1(decoder_2_out1), .out2(decoder_2_out2), .out3(decoder_2_out3),
    .sel(cccc[2:1]), .en(cccc[3]));
  and and_5 (and_5_out, decoder_2_out0, not_2_out, CVZN[3]);
  and and_6 (and_6_out, xnor_1_out, decoder_2_out1);
  and and_7 (and_7_out, not_2_out, xnor_1_out, decoder_2_out2);
  or or_1 (or_1_out, and_1_out, and_2_out, and_3_out, and_4_out, and_5_out, and_6_out, and_7_out, decoder_2_out3);
  xor xor_1 (go, cccc[0], or_1_out);

  // Notes on the sheet:
  //   N
  //   Z
  //   V
  //   C
  //   EQ
  //   HS/CS
  //   MI
  //   VS
  //   N=V
  //   Z'
  //   HI
  //   GE
  //   GT
  //   <always>
endmodule

module inc3 (
  input  [2:0] in,
  output [2:0] out,
  output C
);

  wire [1:0] and_1_out;

  // Probe on in
  assign {C, and_1_out} = in & {and_1_out, 1'b1};  // AND_Gate and_1, 3 bits wide
  assign out = {and_1_out, 1'b1} ^ in;  // XOR_Gate xor_1, 3 bits wide
  // Probe on out

  // Notes on the sheet:
  //   x
  //   x
  //   +1
endmodule

module test_async (
);

  wire a_out, and_2_out, and_3_out, b_out, c_out, cdm_8_mark5_1_data_inst, cdm_8_mark5_1_mem_cycle, clk,
       d_out, decoder_1_out0, decoder_1_out1, decoder_2_out0, decoder_2_out1, IO_3_out, IOsel, nor_1_out,
       nor_2_out, not_1_out, not_2_out, not_3_out, not_4_out, not_5_out, READwrite, transistor_1_out;
  wire [3:0] cdm_8_mark5_1_ps, IOaddr, register_2_q, register_2_q_2;
  wire [6:0] controlled_buffer_1_out, register_1_q;
  wire [7:0] cdm_8_mark5_1_data_out, cdm_8_mark5_1_pc, cdm_8_mark5_1_r0, cdm_8_mark5_1_r1, cdm_8_mark5_1_r2,
       cdm_8_mark5_1_r3, cdm_8_mark5_1_sp, controlled_buffer_2_out, IOdat;
  wire [7:4] cdm_8_mark5_1_addr;
  wire [7:7] s_r_ff_1_qn;

  Clock clock_1 (.out(clk));
  // Probe on cdm_8_mark5_1_r0
  // Probe on cdm_8_mark5_1_r3
  // Probe on cdm_8_mark5_1_r2
  // Probe on cdm_8_mark5_1_r1
  // Probe on cdm_8_mark5_1_sp
  // Probe on cdm_8_mark5_1_pc
  Button a (.out(a_out));
  Transistor #(.\type ("n")) transistor_1 (.in(1'b0), .out(transistor_1_out), .gate(a_out));
  assign controlled_buffer_1_out = a_out ? 7'b1100001 : 7'bz;  // Controlled_Buffer controlled_buffer_1
  not not_1 (not_1_out, transistor_1_out);
  nor nor_1 (nor_1_out, not_1_out, transistor_1_out);
  not not_2 (not_2_out, and_3_out);
  nor nor_2 (nor_2_out, not_2_out, and_3_out);
  and and_1 (IOsel, cdm_8_mark5_1_addr[4], cdm_8_mark5_1_addr[5], cdm_8_mark5_1_addr[6], cdm_8_mark5_1_addr[7], decoder_1_out1);
  // Probe on cdm_8_mark5_1_ps
  Decoder #(.disabled(0)) decoder_1 (
    .out0(decoder_1_out0), .out1(decoder_1_out1), .sel(cdm_8_mark5_1_data_inst), .en(cdm_8_mark5_1_mem_cycle));
  CdM_8_mark5 cdm_8_mark5_1 (
    .clock(clk), .addr({cdm_8_mark5_1_addr, IOaddr}), .mem_read(READwrite),
    .mem_cycle(cdm_8_mark5_1_mem_cycle), .data_inst(cdm_8_mark5_1_data_inst),
    .data_out(cdm_8_mark5_1_data_out), .data_in(controlled_buffer_2_out), .r0(cdm_8_mark5_1_r0),
    .r1(cdm_8_mark5_1_r1), .r2(cdm_8_mark5_1_r2), .r3(cdm_8_mark5_1_r3), .PC(cdm_8_mark5_1_pc),
    .SP(cdm_8_mark5_1_sp), .PS(cdm_8_mark5_1_ps));
  not not_3 (not_3_out, READwrite);
  assign controlled_buffer_2_out = READwrite ? IOdat : 8'bz;  // Controlled_Buffer controlled_buffer_2
  Button b (.out(b_out));
  Transistor #(.\type ("n")) transistor_2 (.in(1'b0), .out(transistor_1_out), .gate(b_out));
  assign controlled_buffer_1_out = b_out ? 7'b1100010 : 7'bz;  // Controlled_Buffer controlled_buffer_3
  S_R_Flip_Flop #(.trigger("low")) s_r_ff_1 (
    .S(nor_1_out), .clk(1'b0), .R(nor_2_out), .Qn(s_r_ff_1_qn[7]));  // open: Q, preset, reset, en
  assign IOdat = not_3_out ? cdm_8_mark5_1_data_out : 8'bz;  // Controlled_Buffer controlled_buffer_4
  Button c (.out(c_out));
  Transistor #(.\type ("n")) transistor_3 (.in(1'b0), .out(transistor_1_out), .gate(c_out));
  assign controlled_buffer_1_out = c_out ? 7'b1100011 : 7'bz;  // Controlled_Buffer controlled_buffer_5
  // Probe on {cdm_8_mark5_1_addr, IOaddr}
  and and_2 (and_2_out, decoder_1_out1, ~IOsel);  // AND_Gate
  Button d (.out(d_out));
  Transistor #(.\type ("n")) transistor_4 (.in(1'b0), .out(transistor_1_out), .gate(d_out));
  assign controlled_buffer_1_out = d_out ? 7'b1100100 : 7'bz;  // Controlled_Buffer controlled_buffer_6
  Pull_Resistor #(.pull(1)) pull_resistor_1 (.node(transistor_1_out));
  Register #(.width(7), .trigger("falling")) register_1 (
    .D(controlled_buffer_1_out), .en(1'b1), .Q(register_1_q), .clk(not_4_out));  // open: clr
  not not_4 (not_4_out, not_5_out);
  not not_5 (not_5_out, transistor_1_out);
  // Probe on IOdat
  RAM ram_1 (
    .addr({cdm_8_mark5_1_addr, IOaddr}), .data(IOdat), .sel(and_2_out), .clk(clk), .ld(READwrite));  // open: clr
  ROM rom_1 (.addr({cdm_8_mark5_1_addr, IOaddr}), .data(IOdat), .sel(decoder_1_out0));
  assign IOdat = and_3_out ? {s_r_ff_1_qn[7], register_1_q} : 8'bz;  // Controlled_Buffer controlled_buffer_7
  and and_3 (and_3_out, decoder_2_out1, clk);
  Decoder #(.disabled(0)) decoder_2 (.out0(decoder_2_out0), .out1(decoder_2_out1), .sel(READwrite), .en(IO_3_out));
  and IO_3 (IO_3_out, IOsel, IOaddr[0], IOaddr[1], ~IOaddr[2], ~IOaddr[3]);  // AND_Gate
  Hex_Digit_Display hex_digit_display_1 (.value(register_2_q_2));  // open: dp
  Hex_Digit_Display hex_digit_display_2 (.value(register_2_q));  // open: dp
  Register #(.trigger("falling")) register_2 (
    .D(IOdat), .en(decoder_2_out0), .Q({register_2_q_2, register_2_q}), .clk(clk));  // open: clr

  // Notes on the sheet:
  //   contents of rom_1 (hex, n*v repeats v):
  //   cd f0 d0 f3 b1 5 e4 4 a1 ee 4
endmodule

module test_sync (
);

  wire a_out, and_2_out, b_out, c_out, cdm_8_mark5_1_data_inst, cdm_8_mark5_1_mem_cycle, clk, d_out,
       decoder_1_out0, decoder_1_out1, decoder_2_out0, decoder_2_out1, IO_3_out, IOsel, not_1_out, or_1_out,
       or_2_out, READwrite, register_2_q;
  wire [3:0] cdm_8_mark5_1_ps, IOaddr, register_3_q, register_3_q_2;
  wire [6:0] controlled_buffer_1_out, register_1_q;
  wire [7:0] cdm_8_mark5_1_data_out, cdm_8_mark5_1_pc, cdm_8_mark5_1_r0, cdm_8_mark5_1_r1, cdm_8_mark5_1_r2,
       cdm_8_mark5_1_r3, cdm_8_mark5_1_sp, controlled_buffer_2_out, IOdat;
  wire [7:4] cdm_8_mark5_1_addr;
  wire [7:7] not_2_out;

  Clock clock_1 (.out(clk));
  // Probe on cdm_8_mark5_1_r0
  or or_1 (or_1_out, d_out, c_out, b_out, a_out);
  // Probe on cdm_8_mark5_1_r3
  // Probe on cdm_8_mark5_1_r2
  // Probe on cdm_8_mark5_1_r1
  // Probe on cdm_8_mark5_1_pc
  // Probe on cdm_8_mark5_1_sp
  Button a (.out(a_out));
  assign controlled_buffer_1_out = a_out ? 7'b1100001 : 7'bz;  // Controlled_Buffer controlled_buffer_1
  and and_1 (IOsel, cdm_8_mark5_1_addr[4], cdm_8_mark5_1_addr[5], cdm_8_mark5_1_addr[6], cdm_8_mark5_1_addr[7], decoder_1_out1);
  // Probe on cdm_8_mark5_1_ps
  Decoder #(.disabled(0)) decoder_1 (
    .out0(decoder_1_out0), .out1(decoder_1_out1), .sel(cdm_8_mark5_1_data_inst), .en(cdm_8_mark5_1_mem_cycle));
  CdM_8_mark5 cdm_8_mark5_1 (
    .clock(clk), .addr({cdm_8_mark5_1_addr, IOaddr}), .mem_read(READwrite),
    .mem_cycle(cdm_8_mark5_1_mem_cycle), .data_inst(cdm_8_mark5_1_data_inst),
    .data_out(cdm_8_mark5_1_data_out), .data_in(controlled_buffer_2_out), .r0(cdm_8_mark5_1_r0),
    .r1(cdm_8_mark5_1_r1), .r2(cdm_8_mark5_1_r2), .r3(cdm_8_mark5_1_r3), .PC(cdm_8_mark5_1_pc),
    .SP(cdm_8_mark5_1_sp), .PS(cdm_8_mark5_1_ps));
  not not_1 (not_1_out, READwrite);
  assign controlled_buffer_2_out = READwrite ? IOdat : 8'bz;  // Controlled_Buffer controlled_buffer_2
  Button b (.out(b_out));
  assign controlled_buffer_1_out = b_out ? 7'b1100010 : 7'bz;  // Controlled_Buffer controlled_buffer_3
  assign IOdat = not_1_out ? cdm_8_mark5_1_data_out : 8'bz;  // Controlled_Buffer controlled_buffer_4
  Button c (.out(c_out));
  assign controlled_buffer_1_out = c_out ? 7'b1100011 : 7'bz;  // Controlled_Buffer controlled_buffer_5
  // Probe on {cdm_8_mark5_1_addr, IOaddr}
  and and_2 (and_2_out, decoder_1_out1, ~IOsel);  // AND_Gate
  Button d (.out(d_out));
  assign controlled_buffer_1_out = d_out ? 7'b1100100 : 7'bz;  // Controlled_Buffer controlled_buffer_6
  or or_2 (or_2_out, or_1_out, decoder_2_out1);
  Register #(.width(7), .trigger("falling")) register_1 (
    .D(controlled_buffer_1_out), .en(or_1_out), .Q(register_1_q), .clk(clk));  // open: clr
  Register #(.width(1)) register_2 (.D(or_1_out), .en(or_2_out), .Q(register_2_q), .clk(clk));  // open: clr
  // Probe on IOdat
  RAM ram_1 (
    .addr({cdm_8_mark5_1_addr, IOaddr}), .data(IOdat), .sel(and_2_out), .clk(clk), .ld(READwrite));  // open: clr
  ROM rom_1 (.addr({cdm_8_mark5_1_addr, IOaddr}), .data(IOdat), .sel(decoder_1_out0));
  assign IOdat = decoder_2_out1 ? {not_2_out[7], register_1_q} : 8'bz;  // Controlled_Buffer controlled_buffer_7
  not not_2 (not_2_out[7], register_2_q);
  Decoder #(.disabled(0)) decoder_2 (.out0(decoder_2_out0), .out1(decoder_2_out1), .sel(READwrite), .en(IO_3_out));
  and IO_3 (IO_3_out, IOsel, IOaddr[0], IOaddr[1], ~IOaddr[2], ~IOaddr[3]);  // AND_Gate
  Hex_Digit_Display hex_digit_display_1 (.value(register_3_q_2));  // open: dp
  Hex_Digit_Display hex_digit_display_2 (.value(register_3_q));  // open: dp
  Register #(.trigger("falling")) register_3 (
    .D(IOdat), .en(decoder_2_out0), .Q({register_3_q_2, register_3_q}), .clk(clk));  // open: clr

  // Notes on the sheet:
  //   contents of rom_1 (hex, n*v repeats v):
  //   cd f0 d0 f3 b1 5 e4 4 a1 ee 4
  //   Ready
endmodule

module vonNeu (
);

  wire and_2_out, cdm_8_mark5_1_mem_cycle, clk, IOsel, not_1_out, READwrite;
  wire [3:0] cdm_8_mark5_1_ps, IOaddr;
  wire [7:0] cdm_8_mark5_1_data_out, cdm_8_mark5_1_pc, cdm_8_mark5_1_r0, cdm_8_mark5_1_r1, cdm_8_mark5_1_r2,
       cdm_8_mark5_1_r3, cdm_8_mark5_1_sp, controlled_buffer_1_out, IOdat;
  wire [7:4] cdm_8_mark5_1_addr;

  Clock clock_1 (.out(clk));
  // Probe on cdm_8_mark5_1_r3
  // Probe on cdm_8_mark5_1_r2
  // Probe on cdm_8_mark5_1_r1
  // Probe on cdm_8_mark5_1_r0
  // Probe on cdm_8_mark5_1_pc
  and and_1 (IOsel, cdm_8_mark5_1_addr[4], cdm_8_mark5_1_addr[5], cdm_8_mark5_1_addr[6], cdm_8_mark5_1_addr[7], cdm_8_mark5_1_mem_cycle);
  // Probe on cdm_8_mark5_1_sp
  // Probe on cdm_8_mark5_1_ps
  CdM_8_mark5 cdm_8_mark5_1 (
    .clock(clk), .addr({cdm_8_mark5_1_addr, IOaddr}), .mem_read(READwrite),
    .mem_cycle(cdm_8_mark5_1_mem_cycle), .data_out(cdm_8_mark5_1_data_out),
    .data_in(controlled_buffer_1_out), .r0(cdm_8_mark5_1_r0), .r1(cdm_8_mark5_1_r1), .r2(cdm_8_mark5_1_r2),
    .r3(cdm_8_mark5_1_r3), .PC(cdm_8_mark5_1_pc), .SP(cdm_8_mark5_1_sp), .PS(cdm_8_mark5_1_ps));  // open: data_inst
  not not_1 (not_1_out, READwrite);
  assign controlled_buffer_1_out = READwrite ? IOdat : 8'bz;  // Controlled_Buffer controlled_buffer_1
  assign IOdat = not_1_out ? cdm_8_mark5_1_data_out : 8'bz;  // Controlled_Buffer controlled_buffer_2
  // Probe on {cdm_8_mark5_1_addr, IOaddr}
  and and_2 (and_2_out, cdm_8_mark5_1_mem_cycle, ~IOsel);  // AND_Gate
  // Probe on IOdat
  RAM ram_1 (
    .addr({cdm_8_mark5_1_addr, IOaddr}), .data(IOdat), .sel(and_2_out), .clk(clk), .ld(READwrite));  // open: clr
endmodule

module basic (
);

  wire cdm_8_mark5_1_mem_cycle, cdm_8_mark5_1_mem_read, clk, not_1_out;
  wire [3:0] cdm_8_mark5_1_ps;
  wire [7:0] cdm_8_mark5_1_addr, cdm_8_mark5_1_data_out, cdm_8_mark5_1_pc, cdm_8_mark5_1_r0,
       cdm_8_mark5_1_r1, cdm_8_mark5_1_r2, cdm_8_mark5_1_r3, cdm_8_mark5_1_sp, controlled_buffer_1_out,
       controlled_buffer_2_out;

  // Probe on cdm_8_mark5_1_r1
  // Probe on cdm_8_mark5_1_r0
  Clock clock_1 (.out(clk));
  // Probe on cdm_8_mark5_1_r3
  // Probe on cdm_8_mark5_1_r2
  // Probe on cdm_8_mark5_1_sp
  // Probe on cdm_8_mark5_1_pc
  // Probe on cdm_8_mark5_1_ps
  CdM_8_mark5 cdm_8_mark5_1 (
    .clock(clk), .addr(cdm_8_mark5_1_addr), .mem_read(cdm_8_mark5_1_mem_read),
    .mem_cycle(cdm_8_mark5_1_mem_cycle), .data_out(cdm_8_mark5_1_data_out),
    .data_in(controlled_buffer_2_out), .r0(cdm_8_mark5_1_r0), .r1(cdm_8_mark5_1_r1), .r2(cdm_8_mark5_1_r2),
    .r3(cdm_8_mark5_1_r3), .PC(cdm_8_mark5_1_pc), .SP(cdm_8_mark5_1_sp), .PS(cdm_8_mark5_1_ps));  // open: data_inst
  not not_1 (not_1_out, cdm_8_mark5_1_mem_read);
  assign controlled_buffer_1_out = not_1_out ? cdm_8_mark5_1_data_out : 8'bz;  // Controlled_Buffer controlled_buffer_1
  assign controlled_buffer_2_out = cdm_8_mark5_1_mem_read ? controlled_buffer_1_out : 8'bz;  // Controlled_Buffer controlled_buffer_2
  // Probe on cdm_8_mark5_1_addr
  // Probe on controlled_buffer_1_out
  RAM ram_1 (
    .addr(cdm_8_mark5_1_addr), .data(controlled_buffer_1_out), .sel(cdm_8_mark5_1_mem_cycle), .clk(clk),
    .ld(cdm_8_mark5_1_mem_read));  // open: clr
endmodule
