// Logisim project GameOfLife.circ as structural Verilog: 13 circuits, main circuit Main
// V
module Main (
  input  in_1,
  input  in_2,
  input  in_3,
  input  Run
);

  wire button_1_out, button_2_out, button_3_out, button_4_out, cdm_1_change_state, Clear_out,
       inputstate_1_cell_change, inputstate_1_cell_change_2, inputstate_1_cell_change_3,
       inputstate_1_cell_change_4, inputstate_1_cell_change_5, inputstate_1_cell_change_6,
       inputstate_1_cell_change_7, inputstate_1_cell_change_8, inputstate_1_cell_change_9,
       inputstate_1_cell_change_10, inputstate_1_cell_change_11, inputstate_1_cell_change_12,
       inputstate_1_cell_change_13, inputstate_1_cell_change_14, inputstate_1_cell_change_15,
       inputstate_1_cell_change_16, keyboard_1_avail, speed_changer_1_game_speed, \time ;
  wire [3:0] X, Y;
  wire [6:0] keyboard_1_data;
  wire [15:0] inputstate_1_row, inputstate_1_row_2, inputstate_1_row_3, inputstate_1_row_4,
       inputstate_1_row_5, inputstate_1_row_6, inputstate_1_row_7, inputstate_1_row_8, inputstate_1_row_9,
       inputstate_1_row_10, inputstate_1_row_11, inputstate_1_row_12, inputstate_1_row_13,
       inputstate_1_row_14, inputstate_1_row_15, inputstate_1_row_16, memory_1_output_row,
       memory_1_output_row_2, memory_1_output_row_3, memory_1_output_row_4, memory_1_output_row_5,
       memory_1_output_row_6, memory_1_output_row_7, memory_1_output_row_8, memory_1_output_row_9,
       memory_1_output_row_10, memory_1_output_row_11, memory_1_output_row_12, memory_1_output_row_13,
       memory_1_output_row_14, memory_1_output_row_15, memory_1_output_row_16;

  Keyboard #(.buflen(1), .trigger("falling")) keyboard_1 (
    .clk(\time ), .re(1'b1), .clr(button_1_out), .avail(keyboard_1_avail), .data(keyboard_1_data));
  Button button_1 (.out(button_1_out));
  Button button_2 (.out(button_2_out));
  Button button_3 (.out(button_3_out));
  Button button_4 (.out(button_4_out));
  Cdm cdm_1 (
    .in_1(button_2_out), .in_2(button_3_out), .in_3(button_4_out), .Change_State(cdm_1_change_state),
    .Was_changed(keyboard_1_avail), .Input_key(keyboard_1_data), .X(X), .Y(Y));
  Memory memory_1 (
    .Input_row(inputstate_1_row), .Change_State(inputstate_1_cell_change), .Input_row_2(inputstate_1_row_2),
    .Change_State_2(inputstate_1_cell_change_2), .Input_row_3(inputstate_1_row_3),
    .Change_State_3(inputstate_1_cell_change_3), .Input_row_4(inputstate_1_row_4),
    .Change_State_4(inputstate_1_cell_change_4), .Input_row_5(inputstate_1_row_5),
    .Change_State_5(inputstate_1_cell_change_5), .Input_row_6(inputstate_1_row_6),
    .Change_State_6(inputstate_1_cell_change_6), .Input_row_7(inputstate_1_row_7),
    .Change_State_7(inputstate_1_cell_change_7), .Input_row_8(inputstate_1_row_8),
    .Change_State_8(inputstate_1_cell_change_8), .Input_row_9(inputstate_1_row_9),
    .Change_State_9(inputstate_1_cell_change_9), .Input_row_10(inputstate_1_row_10),
    .Change_State_10(inputstate_1_cell_change_10), .Input_row_11(inputstate_1_row_11),
    .Change_State_11(inputstate_1_cell_change_11), .Input_row_12(inputstate_1_row_12),
    .Change_State_12(inputstate_1_cell_change_12), .Input_row_13(inputstate_1_row_13),
    .Change_State_13(inputstate_1_cell_change_13), .Input_row_15(inputstate_1_row_15),
    .Change_State_15(inputstate_1_cell_change_15), .Input_row_14(inputstate_1_row_14),
    .Change_State_14(inputstate_1_cell_change_14), .Input_row_16(inputstate_1_row_16),
    .Change_State_16(inputstate_1_cell_change_16), .Run(Run), .Output_row(memory_1_output_row),
    .Output_row_2(memory_1_output_row_2), .Output_row_3(memory_1_output_row_3),
    .Output_row_4(memory_1_output_row_4), .Output_row_5(memory_1_output_row_5),
    .Output_row_6(memory_1_output_row_6), .Output_row_7(memory_1_output_row_7),
    .Output_row_8(memory_1_output_row_8), .Output_row_9(memory_1_output_row_9),
    .Output_row_10(memory_1_output_row_10), .Output_row_11(memory_1_output_row_11),
    .Output_row_12(memory_1_output_row_12), .Output_row_13(memory_1_output_row_13),
    .Output_row_14(memory_1_output_row_14), .Output_row_15(memory_1_output_row_15),
    .Output_row_16(memory_1_output_row_16), .Pointer_clock(\time ), .Game_clock(speed_changer_1_game_speed),
    .in_4(Clear_out));
  Speed_changer speed_changer_1 (
    .Game_speed(speed_changer_1_game_speed), .Pin_2(in_1), .Pin_3(in_2), .Pin_1(in_3), .Pointer_speed(\time ));
  InputState inputstate_1 (
    .X(X), .Y(Y), .Change_State(cdm_1_change_state), .Cell_change(inputstate_1_cell_change),
    .Cell_change_2(inputstate_1_cell_change_2), .Cell_change_3(inputstate_1_cell_change_3),
    .Cell_change_4(inputstate_1_cell_change_4), .Cell_change_5(inputstate_1_cell_change_5),
    .Cell_change_6(inputstate_1_cell_change_6), .Cell_change_7(inputstate_1_cell_change_7),
    .Cell_change_8(inputstate_1_cell_change_8), .Cell_change_9(inputstate_1_cell_change_9),
    .Cell_change_10(inputstate_1_cell_change_10), .Cell_change_11(inputstate_1_cell_change_11),
    .Cell_change_12(inputstate_1_cell_change_12), .Cell_change_13(inputstate_1_cell_change_13),
    .Cell_change_14(inputstate_1_cell_change_14), .Cell_change_15(inputstate_1_cell_change_15),
    .Cell_change_16(inputstate_1_cell_change_16), .Row(inputstate_1_row), .Row_2(inputstate_1_row_2),
    .Row_3(inputstate_1_row_3), .Row_4(inputstate_1_row_4), .Row_5(inputstate_1_row_5),
    .Row_6(inputstate_1_row_6), .Row_7(inputstate_1_row_7), .Row_8(inputstate_1_row_8),
    .Row_9(inputstate_1_row_9), .Row_10(inputstate_1_row_10), .Row_11(inputstate_1_row_11),
    .Row_12(inputstate_1_row_12), .Row_13(inputstate_1_row_13), .Row_14(inputstate_1_row_14),
    .Row_15(inputstate_1_row_15), .Row_16(inputstate_1_row_16));
  DotMatrix #(.inputtype("row"), .matrixcols(16), .matrixrows(16)) dotmatrix_1 (
    .row0(memory_1_output_row), .row1(memory_1_output_row_2), .row2(memory_1_output_row_3),
    .row3(memory_1_output_row_4), .row4(memory_1_output_row_5), .row5(memory_1_output_row_6),
    .row6(memory_1_output_row_7), .row7(memory_1_output_row_8), .row8(memory_1_output_row_9),
    .row9(memory_1_output_row_10), .row10(memory_1_output_row_11), .row11(memory_1_output_row_12),
    .row12(memory_1_output_row_13), .row13(memory_1_output_row_14), .row14(memory_1_output_row_15),
    .row15(memory_1_output_row_16));
  // Probe on X
  Button Clear (.out(Clear_out));
  // Probe on Y
endmodule

module Cdm (
  input  in_1,
  input  in_2,
  input  in_3,
  input  Was_changed,
  input  [6:0] Input_key,
  output [3:0] X,
  output [3:0] Y,
  output Change_State
);

  wire and_2_out, and_3_out, and_4_out, cdm_8_mark5_1_data_inst, cdm_8_mark5_1_mem_cycle, clk,
       controlled_buffer_12_out, controlled_buffer_13_out, decoder_1_out0, decoder_1_out1, decoder_2_out0,
       decoder_2_out1, \default , \end , IOsel, nor_1_out, nor_2_out, not_1_out, not_2_out, not_3_out, one,
       READwrite, three, transistor_1_out, transistor_3_out, two;
  wire [1:0] controlled_buffer_2_out, register_2_q;
  wire [3:0] cdm_8_mark5_1_ps, IOaddr;
  wire [6:0] controlled_buffer_1_out, register_1_q;
  wire [7:0] cdm_8_mark5_1_data_out, cdm_8_mark5_1_pc, cdm_8_mark5_1_r0, cdm_8_mark5_1_r1, cdm_8_mark5_1_r2,
       cdm_8_mark5_1_r3, controlled_buffer_5_out, IOdat, rom_1_data, rom_2_data, rom_3_data, rom_4_data;
  wire [7:4] cdm_8_mark5_1_addr;
  wire [7:7] s_r_ff_1_qn;

  Transistor #(.\type ("n"), .gate("br")) transistor_1 (.in(1'b1), .out(transistor_1_out), .gate(in_1));
  Pull_Resistor pull_resistor_1 (.node(transistor_1_out));
  assign controlled_buffer_1_out = Was_changed ? Input_key : 7'bz;  // Controlled_Buffer controlled_buffer_1
  not not_1 (not_1_out, transistor_3_out);
  not not_2 (not_2_out, decoder_2_out1);
  assign controlled_buffer_2_out = in_1 ? 2'b01 : 2'bz;  // Controlled_Buffer controlled_buffer_2
  Transistor #(.\type ("n"), .gate("br")) transistor_2 (.in(1'b1), .out(transistor_1_out), .gate(in_2));
  Clock clock_1 (.out(clk));
  Transistor #(.\type ("n")) transistor_3 (.in(1'b0), .out(transistor_3_out), .gate(Was_changed));
  nor nor_1 (nor_1_out, not_1_out, transistor_3_out);
  nor nor_2 (nor_2_out, not_2_out, decoder_2_out1);
  assign controlled_buffer_2_out = in_3 ? 2'b11 : 2'bz;  // Controlled_Buffer controlled_buffer_3
  assign controlled_buffer_2_out = in_2 ? 2'b10 : 2'bz;  // Controlled_Buffer controlled_buffer_4
  Transistor #(.\type ("n"), .gate("br")) transistor_4 (.in(1'b1), .out(transistor_1_out), .gate(in_3));
  // Probe on cdm_8_mark5_1_r0
  // Probe on cdm_8_mark5_1_r2
  // Probe on cdm_8_mark5_1_pc
  // Probe on cdm_8_mark5_1_r1
  // Probe on cdm_8_mark5_1_r3
  Pull_Resistor #(.pull(1)) pull_resistor_2 (.node(transistor_3_out));
  Register #(.width(7), .trigger("falling")) register_1 (
    .D(controlled_buffer_1_out), .en(1'b1), .Q(register_1_q), .clk(transistor_3_out));  // open: clr
  S_R_Flip_Flop #(.trigger("low")) s_r_ff_1 (
    .S(nor_1_out), .clk(1'b0), .R(nor_2_out), .Qn(s_r_ff_1_qn[7]));  // open: Q, preset, reset, en
  Register #(.width(2)) register_2 (
    .D(controlled_buffer_2_out), .Q(register_2_q), .clk(transistor_1_out), .clr(\end ));  // open: en
  // Probe on cdm_8_mark5_1_ps
  Decoder #(.disabled(0)) decoder_1 (
    .out0(decoder_1_out0), .out1(decoder_1_out1), .sel(cdm_8_mark5_1_data_inst), .en(cdm_8_mark5_1_mem_cycle));
  CdM_8_mark5 cdm_8_mark5_1 (
    .clock(clk), .addr({cdm_8_mark5_1_addr, IOaddr}), .mem_read(READwrite),
    .mem_cycle(cdm_8_mark5_1_mem_cycle), .data_inst(cdm_8_mark5_1_data_inst),
    .data_out(cdm_8_mark5_1_data_out), .data_in(controlled_buffer_5_out), .r0(cdm_8_mark5_1_r0),
    .r1(cdm_8_mark5_1_r1), .r2(cdm_8_mark5_1_r2), .r3(cdm_8_mark5_1_r3), .PC(cdm_8_mark5_1_pc),
    .PS(cdm_8_mark5_1_ps));  // open: SP
  not not_3 (not_3_out, READwrite);
  assign controlled_buffer_5_out = READwrite ? IOdat : 8'bz;  // Controlled_Buffer controlled_buffer_5
  assign IOdat = decoder_2_out1 ? {s_r_ff_1_qn[7], register_1_q} : 8'bz;  // Controlled_Buffer controlled_buffer_6
  Demultiplexer #(.select(2), .enable("false")) demultiplexer_1 (
    .out0(\default ), .out1(one), .out2(two), .out3(three), .in(decoder_1_out0), .sel(register_2_q));
  assign IOdat = not_3_out ? cdm_8_mark5_1_data_out : 8'bz;  // Controlled_Buffer controlled_buffer_7
  Register #(.trigger("falling")) register_3 (.D(IOdat), .en(decoder_2_out0), .Q({X, Y}), .clk(clk));  // open: clr
  Decoder #(.disabled(0)) decoder_2 (.out0(decoder_2_out0), .out1(decoder_2_out1), .sel(READwrite), .en(and_2_out));
  and and_1 (IOsel, decoder_1_out1, cdm_8_mark5_1_addr[7], cdm_8_mark5_1_addr[6], cdm_8_mark5_1_addr[5], cdm_8_mark5_1_addr[4]);
  and and_2 (and_2_out, IOsel, IOaddr[0], IOaddr[1], ~IOaddr[2], ~IOaddr[3]);  // AND_Gate
  ROM rom_1 (.addr({cdm_8_mark5_1_addr, IOaddr}), .data(rom_1_data), .sel(three));
  ROM rom_2 (.addr({cdm_8_mark5_1_addr, IOaddr}), .data(rom_2_data), .sel(two));
  ROM rom_3 (.addr({cdm_8_mark5_1_addr, IOaddr}), .data(rom_3_data), .sel(one));
  ROM rom_4 (.addr({cdm_8_mark5_1_addr, IOaddr}), .data(rom_4_data), .sel(\default ));
  assign IOdat = three ? rom_1_data : 8'bz;  // Controlled_Buffer controlled_buffer_8
  assign IOdat = two ? rom_2_data : 8'bz;  // Controlled_Buffer controlled_buffer_9
  assign IOdat = one ? rom_3_data : 8'bz;  // Controlled_Buffer controlled_buffer_10
  assign IOdat = \default  ? rom_4_data : 8'bz;  // Controlled_Buffer controlled_buffer_11
  and and_3 (and_3_out, IOsel, IOaddr[0], IOaddr[1], IOaddr[2], ~IOaddr[3]);  // AND_Gate
  and and_4 (and_4_out, IOsel, IOaddr[0], ~IOaddr[1], ~IOaddr[2], ~IOaddr[3]);  // AND_Gate
  assign controlled_buffer_12_out = READwrite ? and_3_out : 1'bz;  // Controlled_Buffer controlled_buffer_12
  BitSelector #(.width(2)) bitselector_1 (.in(2'b10), .out(\end ), .sel(controlled_buffer_12_out));
  Pull_Resistor pull_resistor_3 (.node(\end ));
  assign controlled_buffer_13_out = READwrite ? and_4_out : 1'bz;  // Controlled_Buffer controlled_buffer_13
  BitSelector #(.width(2)) bitselector_2 (.in(2'b10), .out(Change_State), .sel(controlled_buffer_13_out));
  Pull_Resistor pull_resistor_4 (.node(Change_State));

  // Notes on the sheet:
  //   Current position of pointer
  //   contents of rom_1 (hex, n*v repeats v):
  //   d1 f7 a7 ee 20 27*0 d0 f3 d2 10 d3 0 6*1b 8f 8f 8f d1 3 5 e4 3e a3 d0 f1 a0 d0 f3 1b 89 ee 31 1b 8f
  //   8f 86 d1 7 5 e4 51 a3 d0 f1 a0 d0 f3 1b 89 ee 44 1b 8f 8f 86 d1 b 5 e4 64 a3 d0 f1 a0 d0 f3 1b 89 ee
  //   57 8f 8f 86 1b 1b 1b d1 7 5 e4 79 a3 d0 f1 a0 d0 f3 1b 89 ee 6c 8f 8f 86 1b 1b 1b d1 3 5 e4 8e a3 d0
  //   f1 a0 d0 f3 1b 89 ee 81 ee
  //   contents of rom_2 (hex, n*v repeats v):
  //   d1 f7 a7 ee 20 27*0 d0 f3 d2 10 d3 0 6*1b 8f 8f 8f d1 4 5 e4 3e a3 d0 f1 a0 d0 f3 1b 89 ee 31 1b 8f
  //   8f 86 d1 8 5 e4 51 a3 d0 f1 a0 d0 f3 1b 89 ee 44 1b 8f 8f 86 d1 c 5 e4 64 a3 d0 f1 a0 d0 f3 1b 89 ee
  //   57 8f 8f 86 1b 1b 1b d1 8 5 e4 79 a3 d0 f1 a0 d0 f3 1b 89 ee 6c 8f 8f 86 1b 1b 1b d1 4 5 e4 8e a3 d0
  //   f1 a0 d0 f3 1b 89 ee 81 ee
  //   contents of rom_3 (hex, n*v repeats v):
  //   d1 f7 a7 ee 20 27*0 d0 f3 d2 10 d3 0 8f 8f 8f 1b 1b a3 d0 f1 a0 d0 f3 8f a3 d0 f1 a0 d0 f3 8f a3 d0
  //   f1 a0 d0 f3 1b a3 d0 f1 a0 d0 f3 8b 1b a3 d0 f1 a0 d0 f3 ee
  //   contents of rom_4 (hex, n*v repeats v):
  //   d3 0 d2 1 d0 f3 b1 5 e4 6 d2 a 76 e1 16 d0 f1 a0 d0 f3 ee 6 d2 64 76 e1 21 d2 10 1b a3 ee 6 d2 61 76
  //   e1 2c d2 f0 1b a3 ee 6 d2 77 76 e1 40 e 4*96 a e1 3c d2 10 1b 8b a3 ee 6 d2 73 76 e1 56 e 4*96 d1 f0
  //   79 e1 52 d2 f0 1b 8f a3 ee 6 ee 6
endmodule

module InputState (
  input  [3:0] X,
  input  [3:0] Y,
  input  Change_State,
  output [15:0] Row,
  output Cell_change,
  output [15:0] Row_2,
  output Cell_change_2,
  output [15:0] Row_3,
  output Cell_change_3,
  output [15:0] Row_4,
  output Cell_change_4,
  output [15:0] Row_5,
  output Cell_change_5,
  output [15:0] Row_6,
  output Cell_change_6,
  output [15:0] Row_7,
  output Cell_change_7,
  output [15:0] Row_8,
  output Cell_change_8,
  output [15:0] Row_9,
  output Cell_change_9,
  output [15:0] Row_10,
  output Cell_change_10,
  output [15:0] Row_11,
  output Cell_change_11,
  output [15:0] Row_12,
  output Cell_change_12,
  output [15:0] Row_13,
  output Cell_change_13,
  output [15:0] Row_14,
  output Cell_change_14,
  output [15:0] Row_15,
  output Cell_change_15,
  output [15:0] Row_16,
  output Cell_change_16
);

  wire decoder_1_out0, decoder_1_out1, decoder_1_out2, decoder_1_out3, decoder_1_out4, decoder_1_out5,
       decoder_1_out6, decoder_1_out7, decoder_1_out8, decoder_1_out9, decoder_1_out10, decoder_1_out11,
       decoder_1_out12, decoder_1_out13, decoder_1_out14, decoder_1_out15, decoder_2_out0, decoder_2_out1,
       decoder_2_out2, decoder_2_out3, decoder_2_out4, decoder_2_out5, decoder_2_out6, decoder_2_out7,
       decoder_2_out8, decoder_2_out9, decoder_2_out10, decoder_2_out11, decoder_2_out12, decoder_2_out13,
       decoder_2_out14, decoder_2_out15;

  Decoder #(.select(4), .enable("false")) decoder_1 (
    .out0(decoder_1_out0), .out1(decoder_1_out1), .out2(decoder_1_out2), .out3(decoder_1_out3),
    .out4(decoder_1_out4), .out5(decoder_1_out5), .out6(decoder_1_out6), .out7(decoder_1_out7),
    .out8(decoder_1_out8), .out9(decoder_1_out9), .out10(decoder_1_out10), .out11(decoder_1_out11),
    .out12(decoder_1_out12), .out13(decoder_1_out13), .out14(decoder_1_out14), .out15(decoder_1_out15),
    .sel(Y));
  Decoder #(.select(4), .enable("false")) decoder_2 (
    .out0(decoder_2_out0), .out1(decoder_2_out1), .out2(decoder_2_out2), .out3(decoder_2_out3),
    .out4(decoder_2_out4), .out5(decoder_2_out5), .out6(decoder_2_out6), .out7(decoder_2_out7),
    .out8(decoder_2_out8), .out9(decoder_2_out9), .out10(decoder_2_out10), .out11(decoder_2_out11),
    .out12(decoder_2_out12), .out13(decoder_2_out13), .out14(decoder_2_out14), .out15(decoder_2_out15),
    .sel(X));
  Input input_1 (
    .Y(decoder_1_out0), .Change_State(Change_State), .Row(Row), .out_20(Cell_change), .X(decoder_2_out0),
    .X_2(decoder_2_out1), .X_3(decoder_2_out2), .X_4(decoder_2_out3), .X_5(decoder_2_out4),
    .X_6(decoder_2_out5), .X_7(decoder_2_out6), .X_8(decoder_2_out7), .X_9(decoder_2_out8),
    .X_10(decoder_2_out9), .X_11(decoder_2_out10), .X_12(decoder_2_out11), .X_13(decoder_2_out12),
    .X_14(decoder_2_out13), .X_15(decoder_2_out14), .X_16(decoder_2_out15));
  Input input_2 (
    .Y(decoder_1_out1), .Change_State(Change_State), .Row(Row_2), .out_20(Cell_change_2), .X(decoder_2_out0),
    .X_2(decoder_2_out1), .X_3(decoder_2_out2), .X_4(decoder_2_out3), .X_5(decoder_2_out4),
    .X_6(decoder_2_out5), .X_7(decoder_2_out6), .X_8(decoder_2_out7), .X_9(decoder_2_out8),
    .X_10(decoder_2_out9), .X_11(decoder_2_out10), .X_12(decoder_2_out11), .X_13(decoder_2_out12),
    .X_14(decoder_2_out13), .X_15(decoder_2_out14), .X_16(decoder_2_out15));
  Input input_3 (
    .Y(decoder_1_out2), .Change_State(Change_State), .Row(Row_3), .out_20(Cell_change_3), .X(decoder_2_out0),
    .X_2(decoder_2_out1), .X_3(decoder_2_out2), .X_4(decoder_2_out3), .X_5(decoder_2_out4),
    .X_6(decoder_2_out5), .X_7(decoder_2_out6), .X_8(decoder_2_out7), .X_9(decoder_2_out8),
    .X_10(decoder_2_out9), .X_11(decoder_2_out10), .X_12(decoder_2_out11), .X_13(decoder_2_out12),
    .X_14(decoder_2_out13), .X_15(decoder_2_out14), .X_16(decoder_2_out15));
  Input input_4 (
    .Y(decoder_1_out3), .Change_State(Change_State), .Row(Row_4), .out_20(Cell_change_4), .X(decoder_2_out0),
    .X_2(decoder_2_out1), .X_3(decoder_2_out2), .X_4(decoder_2_out3), .X_5(decoder_2_out4),
    .X_6(decoder_2_out5), .X_7(decoder_2_out6), .X_8(decoder_2_out7), .X_9(decoder_2_out8),
    .X_10(decoder_2_out9), .X_11(decoder_2_out10), .X_12(decoder_2_out11), .X_13(decoder_2_out12),
    .X_14(decoder_2_out13), .X_15(decoder_2_out14), .X_16(decoder_2_out15));
  Input input_5 (
    .Y(decoder_1_out4), .Change_State(Change_State), .Row(Row_5), .out_20(Cell_change_5), .X(decoder_2_out0),
    .X_2(decoder_2_out1), .X_3(decoder_2_out2), .X_4(decoder_2_out3), .X_5(decoder_2_out4),
    .X_6(decoder_2_out5), .X_7(decoder_2_out6), .X_8(decoder_2_out7), .X_9(decoder_2_out8),
    .X_10(decoder_2_out9), .X_11(decoder_2_out10), .X_12(decoder_2_out11), .X_13(decoder_2_out12),
    .X_14(decoder_2_out13), .X_15(decoder_2_out14), .X_16(decoder_2_out15));
  Input input_6 (
    .Y(decoder_1_out5), .Change_State(Change_State), .Row(Row_6), .out_20(Cell_change_6), .X(decoder_2_out0),
    .X_2(decoder_2_out1), .X_3(decoder_2_out2), .X_4(decoder_2_out3), .X_5(decoder_2_out4),
    .X_6(decoder_2_out5), .X_7(decoder_2_out6), .X_8(decoder_2_out7), .X_9(decoder_2_out8),
    .X_10(decoder_2_out9), .X_11(decoder_2_out10), .X_12(decoder_2_out11), .X_13(decoder_2_out12),
    .X_14(decoder_2_out13), .X_15(decoder_2_out14), .X_16(decoder_2_out15));
  Input input_7 (
    .Y(decoder_1_out6), .Change_State(Change_State), .Row(Row_7), .out_20(Cell_change_7), .X(decoder_2_out0),
    .X_2(decoder_2_out1), .X_3(decoder_2_out2), .X_4(decoder_2_out3), .X_5(decoder_2_out4),
    .X_6(decoder_2_out5), .X_7(decoder_2_out6), .X_8(decoder_2_out7), .X_9(decoder_2_out8),
    .X_10(decoder_2_out9), .X_11(decoder_2_out10), .X_12(decoder_2_out11), .X_13(decoder_2_out12),
    .X_14(decoder_2_out13), .X_15(decoder_2_out14), .X_16(decoder_2_out15));
  Input input_8 (
    .Y(decoder_1_out7), .Change_State(Change_State), .Row(Row_8), .out_20(Cell_change_8), .X(decoder_2_out0),
    .X_2(decoder_2_out1), .X_3(decoder_2_out2), .X_4(decoder_2_out3), .X_5(decoder_2_out4),
    .X_6(decoder_2_out5), .X_7(decoder_2_out6), .X_8(decoder_2_out7), .X_9(decoder_2_out8),
    .X_10(decoder_2_out9), .X_11(decoder_2_out10), .X_12(decoder_2_out11), .X_13(decoder_2_out12),
    .X_14(decoder_2_out13), .X_15(decoder_2_out14), .X_16(decoder_2_out15));
  Input input_9 (
    .Y(decoder_1_out8), .Change_State(Change_State), .Row(Row_9), .out_20(Cell_change_9), .X(decoder_2_out0),
    .X_2(decoder_2_out1), .X_3(decoder_2_out2), .X_4(decoder_2_out3), .X_5(decoder_2_out4),
    .X_6(decoder_2_out5), .X_7(decoder_2_out6), .X_8(decoder_2_out7), .X_9(decoder_2_out8),
    .X_10(decoder_2_out9), .X_11(decoder_2_out10), .X_12(decoder_2_out11), .X_13(decoder_2_out12),
    .X_14(decoder_2_out13), .X_15(decoder_2_out14), .X_16(decoder_2_out15));
  Input input_10 (
    .Y(decoder_1_out9), .Change_State(Change_State), .Row(Row_10), .out_20(Cell_change_10),
    .X(decoder_2_out0), .X_2(decoder_2_out1), .X_3(decoder_2_out2), .X_4(decoder_2_out3),
    .X_5(decoder_2_out4), .X_6(decoder_2_out5), .X_7(decoder_2_out6), .X_8(decoder_2_out7),
    .X_9(decoder_2_out8), .X_10(decoder_2_out9), .X_11(decoder_2_out10), .X_12(decoder_2_out11),
    .X_13(decoder_2_out12), .X_14(decoder_2_out13), .X_15(decoder_2_out14), .X_16(decoder_2_out15));
  Input input_11 (
    .Y(decoder_1_out10), .Change_State(Change_State), .Row(Row_11), .out_20(Cell_change_11),
    .X(decoder_2_out0), .X_2(decoder_2_out1), .X_3(decoder_2_out2), .X_4(decoder_2_out3),
    .X_5(decoder_2_out4), .X_6(decoder_2_out5), .X_7(decoder_2_out6), .X_8(decoder_2_out7),
    .X_9(decoder_2_out8), .X_10(decoder_2_out9), .X_11(decoder_2_out10), .X_12(decoder_2_out11),
    .X_13(decoder_2_out12), .X_14(decoder_2_out13), .X_15(decoder_2_out14), .X_16(decoder_2_out15));
  Input input_12 (
    .Y(decoder_1_out11), .Change_State(Change_State), .Row(Row_12), .out_20(Cell_change_12),
    .X(decoder_2_out0), .X_2(decoder_2_out1), .X_3(decoder_2_out2), .X_4(decoder_2_out3),
    .X_5(decoder_2_out4), .X_6(decoder_2_out5), .X_7(decoder_2_out6), .X_8(decoder_2_out7),
    .X_9(decoder_2_out8), .X_10(decoder_2_out9), .X_11(decoder_2_out10), .X_12(decoder_2_out11),
    .X_13(decoder_2_out12), .X_14(decoder_2_out13), .X_15(decoder_2_out14), .X_16(decoder_2_out15));
  Input input_13 (
    .Y(decoder_1_out12), .Change_State(Change_State), .Row(Row_13), .out_20(Cell_change_13),
    .X(decoder_2_out0), .X_2(decoder_2_out1), .X_3(decoder_2_out2), .X_4(decoder_2_out3),
    .X_5(decoder_2_out4), .X_6(decoder_2_out5), .X_7(decoder_2_out6), .X_8(decoder_2_out7),
    .X_9(decoder_2_out8), .X_10(decoder_2_out9), .X_11(decoder_2_out10), .X_12(decoder_2_out11),
    .X_13(decoder_2_out12), .X_14(decoder_2_out13), .X_15(decoder_2_out14), .X_16(decoder_2_out15));
  Input input_14 (
    .Y(decoder_1_out13), .Change_State(Change_State), .Row(Row_14), .out_20(Cell_change_14),
    .X(decoder_2_out0), .X_2(decoder_2_out1), .X_3(decoder_2_out2), .X_4(decoder_2_out3),
    .X_5(decoder_2_out4), .X_6(decoder_2_out5), .X_7(decoder_2_out6), .X_8(decoder_2_out7),
    .X_9(decoder_2_out8), .X_10(decoder_2_out9), .X_11(decoder_2_out10), .X_12(decoder_2_out11),
    .X_13(decoder_2_out12), .X_14(decoder_2_out13), .X_15(decoder_2_out14), .X_16(decoder_2_out15));
  Input input_15 (
    .Y(decoder_1_out14), .Change_State(Change_State), .Row(Row_15), .out_20(Cell_change_15),
    .X(decoder_2_out0), .X_2(decoder_2_out1), .X_3(decoder_2_out2), .X_4(decoder_2_out3),
    .X_5(decoder_2_out4), .X_6(decoder_2_out5), .X_7(decoder_2_out6), .X_8(decoder_2_out7),
    .X_9(decoder_2_out8), .X_10(decoder_2_out9), .X_11(decoder_2_out10), .X_12(decoder_2_out11),
    .X_13(decoder_2_out12), .X_14(decoder_2_out13), .X_15(decoder_2_out14), .X_16(decoder_2_out15));
  Input input_16 (
    .Y(decoder_1_out15), .Change_State(Change_State), .Row(Row_16), .out_20(Cell_change_16),
    .X(decoder_2_out0), .X_2(decoder_2_out1), .X_3(decoder_2_out2), .X_4(decoder_2_out3),
    .X_5(decoder_2_out4), .X_6(decoder_2_out5), .X_7(decoder_2_out6), .X_8(decoder_2_out7),
    .X_9(decoder_2_out8), .X_10(decoder_2_out9), .X_11(decoder_2_out10), .X_12(decoder_2_out11),
    .X_13(decoder_2_out12), .X_14(decoder_2_out13), .X_15(decoder_2_out14), .X_16(decoder_2_out15));

  // Other names for the same wires on the sheet: set_prime = Change_State
endmodule

module Input (
  input  Y,
  input  X,
  input  X_2,
  input  X_3,
  input  X_4,
  input  X_5,
  input  X_6,
  input  X_7,
  input  X_8,
  input  X_9,
  input  X_10,
  input  X_11,
  input  X_12,
  input  X_13,
  input  X_14,
  input  X_15,
  input  X_16,
  input  Change_State,
  output [15:0] Row,
  output out_20
);

  wire or_1_out;

  and and_1 (Row[15], Y, X);
  and and_2 (Row[13], Y, X_3);
  and and_3 (Row[14], Y, X_2);
  and and_4 (Row[11], Y, X_5);
  and and_5 (Row[12], Y, X_4);
  and and_6 (Row[10], Y, X_6);
  and and_7 (Row[9], Y, X_7);
  and and_8 (Row[8], Y, X_8);
  and and_9 (Row[7], Y, X_9);
  and and_10 (Row[6], Y, X_10);
  and and_11 (Row[5], Y, X_11);
  and and_12 (Row[4], Y, X_12);
  and and_13 (Row[3], Y, X_13);
  and and_14 (Row[2], Y, X_14);
  and and_15 (Row[1], Y, X_15);
  and and_16 (Row[0], Y, X_16);
  or or_1 (or_1_out, Row[0], Row[1], Row[2], Row[3], Row[4], Row[5], Row[6], Row[7], Row[8], Row[9], Row[10], Row[11], Row[12], Row[13], Row[14], Row[15]);
  and and_17 (out_20, or_1_out, Change_State);

  // Notes on the sheet:
  //   Row: pull=down
endmodule

module Memory (
  input  Run,
  input  Pointer_clock,
  input  Game_clock,
  input  in_4,
  input  [15:0] Input_row,
  input  Change_State,
  input  [15:0] Input_row_2,
  input  Change_State_2,
  input  [15:0] Input_row_3,
  input  Change_State_3,
  input  [15:0] Input_row_4,
  input  Change_State_4,
  input  [15:0] Input_row_5,
  input  Change_State_5,
  input  [15:0] Input_row_6,
  input  Change_State_6,
  input  [15:0] Input_row_7,
  input  Change_State_7,
  input  [15:0] Input_row_8,
  input  Change_State_8,
  input  [15:0] Input_row_9,
  input  Change_State_9,
  input  [15:0] Input_row_10,
  input  Change_State_10,
  input  [15:0] Input_row_11,
  input  Change_State_11,
  input  [15:0] Input_row_12,
  input  Change_State_12,
  input  [15:0] Input_row_13,
  input  Change_State_13,
  input  [15:0] Input_row_14,
  input  Change_State_14,
  input  [15:0] Input_row_15,
  input  Change_State_15,
  input  [15:0] Input_row_16,
  input  Change_State_16,
  output [15:0] Output_row,
  output [15:0] Output_row_2,
  output [15:0] Output_row_3,
  output [15:0] Output_row_4,
  output [15:0] Output_row_5,
  output [15:0] Output_row_6,
  output [15:0] Output_row_7,
  output [15:0] Output_row_8,
  output [15:0] Output_row_9,
  output [15:0] Output_row_10,
  output [15:0] Output_row_11,
  output [15:0] Output_row_12,
  output [15:0] Output_row_13,
  output [15:0] Output_row_14,
  output [15:0] Output_row_15,
  output [15:0] Output_row_16
);

  wire Cl, cl_t, is;
  wire [15:0] down, rows_producer_1_middle_row_for_lower, rows_producer_2_middle_row_for_lower,
       rows_producer_2_middle_row_for_upper, rows_producer_3_middle_row_for_lower,
       rows_producer_3_middle_row_for_upper, rows_producer_4_middle_row_for_lower,
       rows_producer_4_middle_row_for_upper, rows_producer_5_middle_row_for_lower,
       rows_producer_5_middle_row_for_upper, rows_producer_6_middle_row_for_lower,
       rows_producer_6_middle_row_for_upper, rows_producer_7_middle_row_for_lower,
       rows_producer_7_middle_row_for_upper, rows_producer_8_middle_row_for_lower,
       rows_producer_8_middle_row_for_upper, rows_producer_9_middle_row_for_lower,
       rows_producer_9_middle_row_for_upper, rows_producer_10_middle_row_for_lower,
       rows_producer_10_middle_row_for_upper, rows_producer_11_middle_row_for_lower,
       rows_producer_11_middle_row_for_upper, rows_producer_12_middle_row_for_lower,
       rows_producer_12_middle_row_for_upper, rows_producer_13_middle_row_for_lower,
       rows_producer_13_middle_row_for_upper, rows_producer_14_middle_row_for_lower,
       rows_producer_14_middle_row_for_upper, rows_producer_15_middle_row_for_lower,
       rows_producer_15_middle_row_for_upper, rows_producer_16_middle_row_for_upper, up;

  Multiplexer #(.enable("false")) multiplexer_1 (.in0(Pointer_clock), .in1(Game_clock), .out(cl_t), .sel(Run));
  Rows_producer rows_producer_1 (
    .Input_row(Input_row), .Change_state(Change_State), .Output_row(Output_row), .ol(cl_t), .is(is), .Cl(Cl),
    .Lower_row(rows_producer_2_middle_row_for_upper), .Middle_row_for_upper(up), .Upper_row(down),
    .Middle_row_for_lower(rows_producer_1_middle_row_for_lower), .in_5(in_4));
  Rows_producer rows_producer_2 (
    .Input_row(Input_row_2), .Change_state(Change_State_2), .Output_row(Output_row_2), .ol(cl_t), .is(is),
    .Cl(Cl), .Lower_row(rows_producer_3_middle_row_for_upper),
    .Middle_row_for_upper(rows_producer_2_middle_row_for_upper),
    .Upper_row(rows_producer_1_middle_row_for_lower),
    .Middle_row_for_lower(rows_producer_2_middle_row_for_lower), .in_5(in_4));
  Rows_producer rows_producer_3 (
    .Input_row(Input_row_3), .Change_state(Change_State_3), .Output_row(Output_row_3), .ol(cl_t), .is(is),
    .Cl(Cl), .Lower_row(rows_producer_4_middle_row_for_upper),
    .Middle_row_for_upper(rows_producer_3_middle_row_for_upper),
    .Upper_row(rows_producer_2_middle_row_for_lower),
    .Middle_row_for_lower(rows_producer_3_middle_row_for_lower), .in_5(in_4));
  Rows_producer rows_producer_4 (
    .Input_row(Input_row_4), .Change_state(Change_State_4), .Output_row(Output_row_4), .ol(cl_t), .is(is),
    .Cl(Cl), .Lower_row(rows_producer_5_middle_row_for_upper),
    .Middle_row_for_upper(rows_producer_4_middle_row_for_upper),
    .Upper_row(rows_producer_3_middle_row_for_lower),
    .Middle_row_for_lower(rows_producer_4_middle_row_for_lower), .in_5(in_4));
  Rows_producer rows_producer_5 (
    .Input_row(Input_row_5), .Change_state(Change_State_5), .Output_row(Output_row_5), .ol(cl_t), .is(is),
    .Cl(Cl), .Lower_row(rows_producer_6_middle_row_for_upper),
    .Middle_row_for_upper(rows_producer_5_middle_row_for_upper),
    .Upper_row(rows_producer_4_middle_row_for_lower),
    .Middle_row_for_lower(rows_producer_5_middle_row_for_lower), .in_5(in_4));
  Rows_producer rows_producer_6 (
    .Input_row(Input_row_6), .Change_state(Change_State_6), .Output_row(Output_row_6), .ol(cl_t), .is(is),
    .Cl(Cl), .Lower_row(rows_producer_7_middle_row_for_upper),
    .Middle_row_for_upper(rows_producer_6_middle_row_for_upper),
    .Upper_row(rows_producer_5_middle_row_for_lower),
    .Middle_row_for_lower(rows_producer_6_middle_row_for_lower), .in_5(in_4));
  Rows_producer rows_producer_7 (
    .Input_row(Input_row_7), .Change_state(Change_State_7), .Output_row(Output_row_7), .ol(cl_t), .is(is),
    .Cl(Cl), .Lower_row(rows_producer_8_middle_row_for_upper),
    .Middle_row_for_upper(rows_producer_7_middle_row_for_upper),
    .Upper_row(rows_producer_6_middle_row_for_lower),
    .Middle_row_for_lower(rows_producer_7_middle_row_for_lower), .in_5(in_4));
  Rows_producer rows_producer_8 (
    .Input_row(Input_row_8), .Change_state(Change_State_8), .Output_row(Output_row_8), .ol(cl_t), .is(is),
    .Cl(Cl), .Lower_row(rows_producer_9_middle_row_for_upper),
    .Middle_row_for_upper(rows_producer_8_middle_row_for_upper),
    .Upper_row(rows_producer_7_middle_row_for_lower),
    .Middle_row_for_lower(rows_producer_8_middle_row_for_lower), .in_5(in_4));
  Rows_producer rows_producer_9 (
    .Input_row(Input_row_9), .Change_state(Change_State_9), .Output_row(Output_row_9), .ol(cl_t), .is(is),
    .Cl(Cl), .Lower_row(rows_producer_10_middle_row_for_upper),
    .Middle_row_for_upper(rows_producer_9_middle_row_for_upper),
    .Upper_row(rows_producer_8_middle_row_for_lower),
    .Middle_row_for_lower(rows_producer_9_middle_row_for_lower), .in_5(in_4));
  Rows_producer rows_producer_10 (
    .Input_row(Input_row_10), .Change_state(Change_State_10), .Output_row(Output_row_10), .ol(cl_t), .is(is),
    .Cl(Cl), .Lower_row(rows_producer_11_middle_row_for_upper),
    .Middle_row_for_upper(rows_producer_10_middle_row_for_upper),
    .Upper_row(rows_producer_9_middle_row_for_lower),
    .Middle_row_for_lower(rows_producer_10_middle_row_for_lower), .in_5(in_4));
  Rows_producer rows_producer_11 (
    .Input_row(Input_row_11), .Change_state(Change_State_11), .Output_row(Output_row_11), .ol(cl_t), .is(is),
    .Cl(Cl), .Lower_row(rows_producer_12_middle_row_for_upper),
    .Middle_row_for_upper(rows_producer_11_middle_row_for_upper),
    .Upper_row(rows_producer_10_middle_row_for_lower),
    .Middle_row_for_lower(rows_producer_11_middle_row_for_lower), .in_5(in_4));
  Rows_producer rows_producer_12 (
    .Input_row(Input_row_12), .Change_state(Change_State_12), .Output_row(Output_row_12), .ol(cl_t), .is(is),
    .Cl(Cl), .Lower_row(rows_producer_13_middle_row_for_upper),
    .Middle_row_for_upper(rows_producer_12_middle_row_for_upper),
    .Upper_row(rows_producer_11_middle_row_for_lower),
    .Middle_row_for_lower(rows_producer_12_middle_row_for_lower), .in_5(in_4));
  Rows_producer rows_producer_13 (
    .Input_row(Input_row_13), .Change_state(Change_State_13), .Output_row(Output_row_13), .ol(cl_t), .is(is),
    .Cl(Cl), .Lower_row(rows_producer_14_middle_row_for_upper),
    .Middle_row_for_upper(rows_producer_13_middle_row_for_upper),
    .Upper_row(rows_producer_12_middle_row_for_lower),
    .Middle_row_for_lower(rows_producer_13_middle_row_for_lower), .in_5(in_4));
  Rows_producer rows_producer_14 (
    .Input_row(Input_row_14), .Change_state(Change_State_14), .Output_row(Output_row_14), .ol(cl_t), .is(is),
    .Cl(Cl), .Lower_row(rows_producer_15_middle_row_for_upper),
    .Middle_row_for_upper(rows_producer_14_middle_row_for_upper),
    .Upper_row(rows_producer_13_middle_row_for_lower),
    .Middle_row_for_lower(rows_producer_14_middle_row_for_lower), .in_5(in_4));
  Rows_producer rows_producer_15 (
    .Input_row(Input_row_15), .Change_state(Change_State_15), .Output_row(Output_row_15), .ol(cl_t), .is(is),
    .Cl(Cl), .Lower_row(rows_producer_16_middle_row_for_upper),
    .Middle_row_for_upper(rows_producer_15_middle_row_for_upper),
    .Upper_row(rows_producer_14_middle_row_for_lower),
    .Middle_row_for_lower(rows_producer_15_middle_row_for_lower), .in_5(in_4));
  Rows_producer rows_producer_16 (
    .Input_row(Input_row_16), .Change_state(Change_State_16), .Output_row(Output_row_16), .ol(cl_t), .is(is),
    .Cl(Cl), .Lower_row(up), .Middle_row_for_upper(rows_producer_16_middle_row_for_upper),
    .Upper_row(rows_producer_15_middle_row_for_lower), .Middle_row_for_lower(down), .in_5(in_4));
  not not_1 (is, Run);
  assign Cl = Run ? cl_t : 1'bz;  // Controlled_Buffer controlled_buffer_1
  Pull_Resistor pull_resistor_1 (.node(Cl));

  // Other names for the same wires on the sheet: clear = in_4
endmodule

module Rows_producer (
  input  is,
  input  ol,
  input  [15:0] Input_row,
  input  [15:0] Upper_row,
  input  in_5,
  input  Change_state,
  input  [15:0] Lower_row,
  input  Cl,
  output [15:0] Middle_row_for_upper,
  output [15:0] Output_row,
  output [15:0] Middle_row_for_lower
);

  wire controlled_buffer_1_out, hide_pointer_1_out_3;
  wire [15:0] multiplexer_1_out, \new , p, pull_resistor_2_node, xor_1_out;
  wire [17:0] converter_16_to_18_1_out_2, converter_16_to_18_2_out_2, converter_16_to_18_3_out_2;

  Pointer pointer_1 (.Timer(ol), .IsChange(Change_state), .in_3(Input_row), .out_4(p));
  assign xor_1_out = Middle_row_for_lower ^ Input_row;  // XOR_Gate xor_1, 16 bits wide
  assign controlled_buffer_1_out = Change_state ? Change_state : 1'bz;  // Controlled_Buffer controlled_buffer_1
  Multiplexer #(.width(16), .enable("false")) multiplexer_1 (
    .in0(\new ), .in1(xor_1_out), .out(multiplexer_1_out), .sel(is));
  Pull_Resistor pull_resistor_1 (.node(controlled_buffer_1_out));
  Register #(.width(16)) register_1 (
    .D(multiplexer_1_out), .Q(Middle_row_for_lower), .clk(controlled_buffer_1_out), .clr(in_5));  // open: en
  assign controlled_buffer_1_out = hide_pointer_1_out_3 ? Cl : 1'bz;  // Controlled_Buffer controlled_buffer_2
  Hide_pointer hide_pointer_1 (.in_2(is), .out_3(hide_pointer_1_out_3), .in_1(Cl));
  Converter_16_to_18 converter_16_to_18_1 (.in_1(Upper_row), .out_2(converter_16_to_18_1_out_2));
  Converter_16_to_18 converter_16_to_18_2 (.in_1(Middle_row_for_lower), .out_2(converter_16_to_18_2_out_2));
  Converter_16_to_18 converter_16_to_18_3 (.in_1(Lower_row), .out_2(converter_16_to_18_3_out_2));
  Pull_Resistor pull_resistor_2 (.node(pull_resistor_2_node));
  assign pull_resistor_2_node = is ? p : 16'bz;  // Controlled_Buffer controlled_buffer_3
  One_row_logic one_row_logic_1 (
    .Upper_row(converter_16_to_18_1_out_2), .Middle_row(converter_16_to_18_2_out_2),
    .Lower_row(converter_16_to_18_3_out_2), .Row_with_game_logic(\new ));
  assign Output_row = pull_resistor_2_node ^ Middle_row_for_lower;  // XOR_Gate xor_2, 16 bits wide

  assign Middle_row_for_upper = Middle_row_for_lower;
endmodule

module Pointer (
  input  Timer,
  input  IsChange,
  input  [15:0] in_3,
  output [15:0] out_4
);

  wire controlled_buffer_1_out, not_1_out;

  not not_1 (not_1_out, IsChange);
  assign controlled_buffer_1_out = not_1_out ? Timer : 1'bz;  // Controlled_Buffer controlled_buffer_1
  Pull_Resistor pull_resistor_1 (.node(controlled_buffer_1_out));
  And and_1 (.in_2(in_3[0]), .in_1(controlled_buffer_1_out), .out_3(out_4[0]));
  And and_2 (.in_2(in_3[1]), .in_1(controlled_buffer_1_out), .out_3(out_4[1]));
  And and_3 (.in_2(in_3[2]), .in_1(controlled_buffer_1_out), .out_3(out_4[2]));
  And and_4 (.in_2(in_3[3]), .in_1(controlled_buffer_1_out), .out_3(out_4[3]));
  And and_5 (.in_2(in_3[4]), .in_1(controlled_buffer_1_out), .out_3(out_4[4]));
  And and_6 (.in_2(in_3[5]), .in_1(controlled_buffer_1_out), .out_3(out_4[5]));
  And and_7 (.in_2(in_3[6]), .in_1(controlled_buffer_1_out), .out_3(out_4[6]));
  And and_8 (.in_2(in_3[7]), .in_1(controlled_buffer_1_out), .out_3(out_4[7]));
  And and_9 (.in_2(in_3[8]), .in_1(controlled_buffer_1_out), .out_3(out_4[8]));
  And and_10 (.in_2(in_3[9]), .in_1(controlled_buffer_1_out), .out_3(out_4[9]));
  And and_11 (.in_2(in_3[10]), .in_1(controlled_buffer_1_out), .out_3(out_4[10]));
  And and_12 (.in_2(in_3[11]), .in_1(controlled_buffer_1_out), .out_3(out_4[11]));
  And and_13 (.in_2(in_3[12]), .in_1(controlled_buffer_1_out), .out_3(out_4[12]));
  And and_14 (.in_2(in_3[13]), .in_1(controlled_buffer_1_out), .out_3(out_4[13]));
  And and_15 (.in_2(in_3[14]), .in_1(controlled_buffer_1_out), .out_3(out_4[14]));
  And and_16 (.in_2(in_3[15]), .in_1(controlled_buffer_1_out), .out_3(out_4[15]));
endmodule

module And (
  input  in_1,
  input  in_2,
  output out_3
);

  and and_1 (out_3, in_1, in_2);
endmodule

module Hide_pointer (
  input  in_1,
  input  in_2,
  output out_3
);

  wire [1:0] counter_1_q;

  and and_1 (out_3, counter_1_q[1], counter_1_q[0], 1'b1);
  Counter #(.width(2), .max('h3), .ongoal("stay")) counter_1 (
    .Q(counter_1_q), .clk(in_1), .clr(in_2));  // open: load, D, count, carry
endmodule

module Converter_16_to_18 (
  input  [15:0] in_1,
  output [17:0] out_2
);


  assign out_2 = {in_1[0], in_1, in_1[15]};
endmodule

// Row logic
module One_row_logic (
  input  [17:0] Upper_row,
  input  [17:0] Middle_row,
  input  [17:0] Lower_row,
  output [15:0] Row_with_game_logic
);

  One_cell_logic one_cell_logic_1 (
    .in_1(Upper_row[0]), .in_2(Upper_row[1]), .in_3(Upper_row[2]), .in_4(Middle_row[0]),
    .in_5(Middle_row[2]), .current(Middle_row[1]), .in_7(Lower_row[0]), .in_8(Lower_row[1]),
    .in_9(Lower_row[2]), .out_10(Row_with_game_logic[0]));
  One_cell_logic one_cell_logic_2 (
    .in_1(Upper_row[1]), .in_2(Upper_row[2]), .in_3(Upper_row[3]), .in_4(Middle_row[1]),
    .in_5(Middle_row[3]), .current(Middle_row[2]), .in_7(Lower_row[1]), .in_8(Lower_row[2]),
    .in_9(Lower_row[3]), .out_10(Row_with_game_logic[1]));
  One_cell_logic one_cell_logic_3 (
    .in_1(Upper_row[2]), .in_2(Upper_row[3]), .in_3(Upper_row[4]), .in_4(Middle_row[2]),
    .in_5(Middle_row[4]), .current(Middle_row[3]), .in_7(Lower_row[2]), .in_8(Lower_row[3]),
    .in_9(Lower_row[4]), .out_10(Row_with_game_logic[2]));
  One_cell_logic one_cell_logic_4 (
    .in_1(Upper_row[3]), .in_2(Upper_row[4]), .in_3(Upper_row[5]), .in_4(Middle_row[3]),
    .in_5(Middle_row[5]), .current(Middle_row[4]), .in_7(Lower_row[3]), .in_8(Lower_row[4]),
    .in_9(Lower_row[5]), .out_10(Row_with_game_logic[3]));
  One_cell_logic one_cell_logic_5 (
    .in_1(Upper_row[4]), .in_2(Upper_row[5]), .in_3(Upper_row[6]), .in_4(Middle_row[4]),
    .in_5(Middle_row[6]), .current(Middle_row[5]), .in_7(Lower_row[4]), .in_8(Lower_row[5]),
    .in_9(Lower_row[6]), .out_10(Row_with_game_logic[4]));
  One_cell_logic one_cell_logic_6 (
    .in_1(Upper_row[5]), .in_2(Upper_row[6]), .in_3(Upper_row[7]), .in_4(Middle_row[5]),
    .in_5(Middle_row[7]), .current(Middle_row[6]), .in_7(Lower_row[5]), .in_8(Lower_row[6]),
    .in_9(Lower_row[7]), .out_10(Row_with_game_logic[5]));
  One_cell_logic one_cell_logic_7 (
    .in_1(Upper_row[6]), .in_2(Upper_row[7]), .in_3(Upper_row[8]), .in_4(Middle_row[6]),
    .in_5(Middle_row[8]), .current(Middle_row[7]), .in_7(Lower_row[6]), .in_8(Lower_row[7]),
    .in_9(Lower_row[8]), .out_10(Row_with_game_logic[6]));
  One_cell_logic one_cell_logic_8 (
    .in_1(Upper_row[7]), .in_2(Upper_row[8]), .in_3(Upper_row[9]), .in_4(Middle_row[7]),
    .in_5(Middle_row[9]), .current(Middle_row[8]), .in_7(Lower_row[7]), .in_8(Lower_row[8]),
    .in_9(Lower_row[9]), .out_10(Row_with_game_logic[7]));
  One_cell_logic one_cell_logic_9 (
    .in_1(Upper_row[8]), .in_2(Upper_row[9]), .in_3(Upper_row[10]), .in_4(Middle_row[8]),
    .in_5(Middle_row[10]), .current(Middle_row[9]), .in_7(Lower_row[8]), .in_8(Lower_row[9]),
    .in_9(Lower_row[10]), .out_10(Row_with_game_logic[8]));
  One_cell_logic one_cell_logic_10 (
    .in_1(Upper_row[9]), .in_2(Upper_row[10]), .in_3(Upper_row[11]), .in_4(Middle_row[9]),
    .in_5(Middle_row[11]), .current(Middle_row[10]), .in_7(Lower_row[9]), .in_8(Lower_row[10]),
    .in_9(Lower_row[11]), .out_10(Row_with_game_logic[9]));
  One_cell_logic one_cell_logic_11 (
    .in_1(Upper_row[10]), .in_2(Upper_row[11]), .in_3(Upper_row[12]), .in_4(Middle_row[10]),
    .in_5(Middle_row[12]), .current(Middle_row[11]), .in_7(Lower_row[10]), .in_8(Lower_row[11]),
    .in_9(Lower_row[12]), .out_10(Row_with_game_logic[10]));
  One_cell_logic one_cell_logic_12 (
    .in_1(Upper_row[11]), .in_2(Upper_row[12]), .in_3(Upper_row[13]), .in_4(Middle_row[11]),
    .in_5(Middle_row[13]), .current(Middle_row[12]), .in_7(Lower_row[11]), .in_8(Lower_row[12]),
    .in_9(Lower_row[13]), .out_10(Row_with_game_logic[11]));
  One_cell_logic one_cell_logic_13 (
    .in_1(Upper_row[12]), .in_2(Upper_row[13]), .in_3(Upper_row[14]), .in_4(Middle_row[12]),
    .in_5(Middle_row[14]), .current(Middle_row[13]), .in_7(Lower_row[12]), .in_8(Lower_row[13]),
    .in_9(Lower_row[14]), .out_10(Row_with_game_logic[12]));
  One_cell_logic one_cell_logic_14 (
    .in_1(Upper_row[13]), .in_2(Upper_row[14]), .in_3(Upper_row[15]), .in_4(Middle_row[13]),
    .in_5(Middle_row[15]), .current(Middle_row[14]), .in_7(Lower_row[13]), .in_8(Lower_row[14]),
    .in_9(Lower_row[15]), .out_10(Row_with_game_logic[13]));
  One_cell_logic one_cell_logic_15 (
    .in_1(Upper_row[14]), .in_2(Upper_row[15]), .in_3(Upper_row[16]), .in_4(Middle_row[14]),
    .in_5(Middle_row[16]), .current(Middle_row[15]), .in_7(Lower_row[14]), .in_8(Lower_row[15]),
    .in_9(Lower_row[16]), .out_10(Row_with_game_logic[14]));
  One_cell_logic one_cell_logic_16 (
    .in_1(Upper_row[15]), .in_2(Upper_row[16]), .in_3(Upper_row[17]), .in_4(Middle_row[15]),
    .in_5(Middle_row[17]), .current(Middle_row[16]), .in_7(Lower_row[15]), .in_8(Lower_row[16]),
    .in_9(Lower_row[17]), .out_10(Row_with_game_logic[15]));

  // Other names for the same wires on the sheet: _1[2:0] = Middle_row[2:0]; _1d[2:0] = Lower_row[2:0];
  //   _1u[2:0] = Upper_row[2:0]; _2[2:0] = Middle_row[3:1]; _2d[2:0] = Lower_row[3:1]; _2u[2:0] = Upper_row[3:1];
  //   _3[2:0] = Middle_row[4:2]; _3d[2:0] = Lower_row[4:2]; _3u[2:0] = Upper_row[4:2]; _4[2:0] = Middle_row[5:3];
  //   _4d[2:0] = Lower_row[5:3]; _4u[2:0] = Upper_row[5:3]; _5[2:0] = Middle_row[6:4]; _6[2:0] = Middle_row[7:5];
  //   _7[2:0] = Middle_row[8:6]; _5d[2:0] = Lower_row[6:4]; _6d[2:0] = Lower_row[7:5]; _7d[2:0] = Lower_row[8:6];
  //   _5u[2:0] = Upper_row[6:4]; _6u[2:0] = Upper_row[7:5]; _7u[2:0] = Upper_row[8:6]; _8[2:0] = Middle_row[9:7];
  //   _8d[2:0] = Lower_row[9:7]; _8u[2:0] = Upper_row[9:7]; _9[2:0] = Middle_row[10:8]; _9d[2:0] = Lower_row[10:8];
  //   _9u[2:0] = Upper_row[10:8]; _10[2:0] = Middle_row[11:9]; _10d[2:0] = Lower_row[11:9];
  //   _10u[2:0] = Upper_row[11:9]; _11[2:0] = Middle_row[12:10]; _11d[2:0] = Lower_row[12:10];
  //   _11u[2:0] = Upper_row[12:10]; _12[2:0] = Middle_row[13:11]; _12d[2:0] = Lower_row[13:11];
  //   _12u[2:0] = Upper_row[13:11]; _13[2:0] = Middle_row[14:12]; _14[2:0] = Middle_row[15:13];
  //   _15[2:0] = Middle_row[16:14]; _13d[2:0] = Lower_row[14:12]; _14d[2:0] = Lower_row[15:13];
  //   _15d[2:0] = Lower_row[16:14]; _13u[2:0] = Upper_row[14:12]; _14u[2:0] = Upper_row[15:13];
  //   _15u[2:0] = Upper_row[16:14]; _16[2:0] = Middle_row[17:15]; _16d[2:0] = Lower_row[17:15];
  //   _16u[2:0] = Upper_row[17:15]
endmodule

// Cell logic
module One_cell_logic (
  input  in_1,
  input  in_2,
  input  in_3,
  input  in_4,
  input  in_5,
  input  current,
  input  in_7,
  input  in_8,
  input  in_9,
  output out_10
);

  wire comparator_1_eq, comparator_1_gt, comparator_2_eq, comparator_2_gt;
  wire [1:0] adder_1_out, adder_2_out, adder_3_out, adder_4_out, adder_5_out, adder_6_out;
  wire [2:0] adder_7_out;
  wire [2:2] adder_5_cout, adder_6_cout;
  wire [3:3] adder_7_cout;

  Adder #(.width(1)) adder_1 (.a(in_1), .b(in_2), .out(adder_1_out[0]), .cout(adder_1_out[1]));  // open: cin
  Adder #(.width(1)) adder_2 (.a(in_3), .b(in_4), .out(adder_2_out[0]), .cout(adder_2_out[1]));  // open: cin
  Adder #(.width(1)) adder_3 (.a(in_5), .b(in_7), .out(adder_3_out[0]), .cout(adder_3_out[1]));  // open: cin
  Adder #(.width(1)) adder_4 (.a(in_8), .b(in_9), .out(adder_4_out[0]), .cout(adder_4_out[1]));  // open: cin
  Adder #(.width(2)) adder_5 (
    .a(adder_1_out), .b(adder_2_out), .out(adder_5_out), .cout(adder_5_cout[2]));  // open: cin
  Adder #(.width(2)) adder_6 (
    .a(adder_3_out), .b(adder_4_out), .out(adder_6_out), .cout(adder_6_cout[2]));  // open: cin
  Adder #(.width(3)) adder_7 (
    .a({adder_5_cout[2], adder_5_out}), .b({adder_6_cout[2], adder_6_out}), .out(adder_7_out),
    .cout(adder_7_cout[3]));  // open: cin
  Comparator #(.width(4), .mode("unsigned")) comparator_1 (
    .a({adder_7_cout[3], adder_7_out}), .b(4'b0011), .gt(comparator_1_gt), .eq(comparator_1_eq));  // open: lt
  Comparator #(.width(4), .mode("unsigned")) comparator_2 (
    .a(4'b0010), .b({adder_7_cout[3], adder_7_out}), .gt(comparator_2_gt), .eq(comparator_2_eq));  // open: lt
  assign out_10 = comparator_1_gt ? 1'b0 : 1'bz;  // Controlled_Buffer controlled_buffer_1
  assign out_10 = comparator_1_eq ? 1'b1 : 1'bz;  // Controlled_Buffer controlled_buffer_2
  assign out_10 = comparator_2_gt ? 1'b0 : 1'bz;  // Controlled_Buffer controlled_buffer_3
  assign out_10 = comparator_2_eq ? current : 1'bz;  // Controlled_Buffer controlled_buffer_4
endmodule

module Speed_changer (
  input  Pin_1,
  input  Pin_2,
  input  Pin_3,
  output Game_speed,
  output Pointer_speed
);

  wire clock_1_out, clock_2_out, clock_3_out, clock_4_out;
  wire [1:0] a, adder_1_out, adder_2_out, adder_3_out, b, c;

  Transistor #(.width(2)) transistor_1 (.in(2'b01), .out(a), .gate(Pin_1));
  Transistor #(.width(2)) transistor_2 (.in(2'b01), .out(b), .gate(Pin_2));
  Transistor #(.width(2)) transistor_3 (.in(2'b01), .out(c), .gate(Pin_3));
  Transistor #(.\type ("n"), .width(2)) transistor_4 (.in(2'b00), .out(a), .gate(Pin_1));
  Transistor #(.\type ("n"), .width(2)) transistor_5 (.in(2'b00), .out(b), .gate(Pin_2));
  Transistor #(.\type ("n"), .width(2)) transistor_6 (.in(2'b00), .out(c), .gate(Pin_3));
  Adder #(.width(2)) adder_1 (.a(2'b00), .b(a), .out(adder_1_out));  // open: cin, cout
  Adder #(.width(2)) adder_2 (.a(adder_1_out), .b(b), .out(adder_2_out));  // open: cin, cout
  Clock #(.highDuration(5), .lowDuration(5)) clock_1 (.out(clock_1_out));
  Adder #(.width(2)) adder_3 (.a(adder_2_out), .b(c), .out(adder_3_out));  // open: cin, cout
  Clock #(.highDuration(10), .lowDuration(10)) clock_2 (.out(clock_2_out));
  Clock #(.highDuration(30), .lowDuration(30)) clock_3 (.out(clock_3_out));
  Clock #(.highDuration(40), .lowDuration(40)) clock_4 (.out(clock_4_out));
  Multiplexer #(.select(2), .enable("false")) multiplexer_1 (
    .in0(clock_1_out), .in1(clock_2_out), .in2(clock_3_out), .in3(clock_4_out), .out(Game_speed),
    .sel(adder_3_out));
  Clock #(.highDuration(10), .lowDuration(10)) clock_5 (.out(Pointer_speed));

  // Notes on the sheet:
  //   3
  //   2
  //   1
  //   0
endmodule
